// Digital circuit SIGNED COMPARE V1.dig as structural Verilog
module SIGNED_COMPARE_V1 (
  input  A0,
  input  A1,
  input  A2,
  input  A3,
  input  A4,
  input  A5,
  input  A6,
  input  A7,
  input  A8,
  input  A9,
  input  A10,
  input  A11,
  input  A12,
  input  A13,
  input  A14,
  input  A15,
  input  A16,
  input  A17,
  input  A18,
  input  A19,
  input  A20,
  input  A21,
  input  A22,
  input  A23,
  input  A24,
  input  A25,
  input  A26,
  input  A27,
  input  A28,
  input  A29,
  input  A30,
  input  A31,
  input  S_U_BAR,
  output LT,
  output EQ,
  output GT
);

  wire and_1_out, and_2_out, and_3_out, and_4_out, not_1_out, not_2_out, not_3_out, not_4_out, not_5_out,
       or_1_out, or_2_out, or_3_out, unsigned_compare_v1_1_eq, unsigned_compare_v1_1_gt,
       unsigned_compare_v1_1_lt;

  not not_1 (not_1_out, A15);
  not not_2 (not_2_out, A31);
  and and_1 (and_1_out, not_1_out, A31);
  and and_2 (and_2_out, A15, not_2_out);
  and and_3 (and_3_out, and_1_out, S_U_BAR);
  and and_4 (and_4_out, S_U_BAR, and_2_out);
  unsigned_compare_v1 unsigned_compare_v1_1 (
    .A0(A0), .A1(A1), .A2(A2), .A3(A3), .A4(A4), .A5(A5), .A6(A6), .A7(A7), .A8(A8), .A9(A9), .A10(A10),
    .A11(A11), .A12(A12), .A13(A13), .A14(A14), .A15(A15), .A16(A16), .A17(A17), .A18(A18), .A19(A19),
    .A20(A20), .A21(A21), .A22(A22), .A23(A23), .A24(A24), .A25(A25), .A26(A26), .A27(A27), .A28(A28),
    .A29(A29), .A30(A30), .A31(A31), .EQ(unsigned_compare_v1_1_eq), .GT(unsigned_compare_v1_1_gt),
    .LT(unsigned_compare_v1_1_lt));
  or or_1 (or_1_out, and_3_out, and_4_out);
  or or_2 (or_2_out, unsigned_compare_v1_1_gt, and_3_out);
  or or_3 (or_3_out, unsigned_compare_v1_1_lt, and_4_out);
  not not_3 (not_3_out, or_1_out);
  not not_4 (not_4_out, and_4_out);
  not not_5 (not_5_out, and_3_out);
  and and_5 (EQ, unsigned_compare_v1_1_eq, not_3_out);
  and and_6 (GT, or_2_out, not_4_out);
  and and_7 (LT, or_3_out, not_5_out);
endmodule
