// Digital circuit unsigned comparator(corrected) v2.dig as structural Verilog
module unsigned_comparator_corrected__v2 (
  input  A0,
  input  A1,
  input  A2,
  input  A3,
  input  A4,
  input  A5,
  input  A6,
  input  A7,
  input  A8,
  input  A9,
  input  A10,
  input  A11,
  input  A12,
  input  A13,
  input  A14,
  input  A15,
  input  A16,
  input  A17,
  input  A18,
  input  A19,
  input  A20,
  input  A21,
  input  A22,
  input  A23,
  input  A24,
  input  A25,
  input  A26,
  input  A27,
  input  A28,
  input  A29,
  input  A30,
  input  A31,
  output LT,
  output EQ,
  output GT
);

  wire and_1_out, and_2_out, and_3_out, and_4_out, and_5_out, and_6_out, and_7_out, and_8_out, and_9_out,
       and_10_out, and_11_out, and_12_out, and_13_out, and_14_out, and_15_out, and_16_out, and_17_out,
       and_18_out, and_19_out, and_20_out, and_21_out, and_22_out, and_23_out, and_24_out, and_25_out,
       and_26_out, and_27_out, and_28_out, and_29_out, and_30_out, and_31_out, and_32_out, and_33_out,
       and_34_out, and_35_out, and_36_out, and_38_out, and_39_out, and_40_out, and_41_out, and_42_out,
       and_43_out, and_44_out, and_45_out, and_46_out, and_47_out, and_48_out, and_49_out, and_50_out,
       and_51_out, and_52_out, and_53_out, and_54_out, and_55_out, and_56_out, and_57_out, and_58_out,
       and_59_out, and_60_out, not_1_out, not_2_out, not_3_out, not_4_out, not_5_out, not_6_out, not_7_out,
       not_8_out, not_9_out, not_10_out, not_11_out, not_12_out, not_13_out, not_14_out, not_15_out,
       not_16_out, not_17_out, not_18_out, or_1_out, or_2_out, or_3_out, or_4_out, or_5_out, or_6_out,
       or_7_out, or_8_out, or_9_out, or_10_out, or_11_out, or_12_out, or_13_out, or_14_out, xnor_1_out,
       xnor_2_out, xnor_3_out, xnor_4_out, xnor_5_out, xnor_6_out, xnor_7_out, xnor_8_out, xnor_9_out,
       xnor_10_out, xnor_11_out, xnor_12_out, xnor_13_out, xnor_14_out, xnor_15_out, xnor_16_out,
       xnor_17_out, xnor_18_out, xnor_19_out, xnor_20_out, xnor_21_out, xnor_22_out, xnor_23_out,
       xnor_24_out, xnor_25_out, xnor_26_out, xnor_27_out, xnor_28_out, xnor_29_out, xnor_30_out, xnor_31_out;

  not not_1 (not_1_out, A0);
  not not_2 (not_2_out, A1);
  not not_3 (not_3_out, A2);
  not not_4 (not_4_out, A3);
  not not_5 (not_5_out, A4);
  not not_6 (not_6_out, A5);
  not not_7 (not_7_out, A6);
  not not_8 (not_8_out, A7);
  not not_9 (not_9_out, A8);
  not not_10 (not_10_out, A9);
  not not_11 (not_11_out, A10);
  not not_12 (not_12_out, A11);
  not not_13 (not_13_out, A12);
  not not_14 (not_14_out, A13);
  not not_15 (not_15_out, A14);
  not not_16 (not_16_out, A15);
  xnor xnor_1 (xnor_1_out, A0, A16);
  xnor xnor_2 (xnor_2_out, A1, A17);
  xnor xnor_3 (xnor_3_out, A2, A18);
  xnor xnor_4 (xnor_4_out, A3, A19);
  xnor xnor_5 (xnor_5_out, A4, A20);
  xnor xnor_6 (xnor_6_out, A5, A21);
  xnor xnor_7 (xnor_7_out, A6, A22);
  xnor xnor_8 (xnor_8_out, A7, A23);
  xnor xnor_9 (xnor_9_out, A8, A24);
  xnor xnor_10 (xnor_10_out, A9, A25);
  xnor xnor_11 (xnor_11_out, A10, A26);
  xnor xnor_12 (xnor_12_out, A11, A27);
  xnor xnor_13 (xnor_13_out, A12, A28);
  xnor xnor_14 (xnor_14_out, A13, A29);
  xnor xnor_15 (xnor_15_out, A14, A30);
  xnor xnor_16 (xnor_16_out, A15, A31);
  and and_1 (and_1_out, not_1_out, A16);
  xnor xnor_17 (xnor_17_out, A1, A17);
  and and_2 (and_2_out, not_2_out, A17);
  xnor xnor_18 (xnor_18_out, A2, A18);
  and and_3 (and_3_out, not_3_out, A18);
  xnor xnor_19 (xnor_19_out, A3, A19);
  and and_4 (and_4_out, not_4_out, A19);
  xnor xnor_20 (xnor_20_out, A4, A20);
  and and_5 (and_5_out, not_5_out, A20);
  xnor xnor_21 (xnor_21_out, A5, A21);
  and and_6 (and_6_out, not_6_out, A21);
  xnor xnor_22 (xnor_22_out, A6, A22);
  and and_7 (and_7_out, not_7_out, A22);
  xnor xnor_23 (xnor_23_out, A7, A23);
  and and_8 (and_8_out, not_8_out, A23);
  xnor xnor_24 (xnor_24_out, A8, A24);
  and and_9 (and_9_out, not_9_out, A24);
  xnor xnor_25 (xnor_25_out, A9, A25);
  and and_10 (and_10_out, not_10_out, A25);
  xnor xnor_26 (xnor_26_out, A10, A26);
  and and_11 (and_11_out, not_11_out, A26);
  xnor xnor_27 (xnor_27_out, A11, A27);
  and and_12 (and_12_out, not_12_out, A27);
  xnor xnor_28 (xnor_28_out, A12, A28);
  and and_13 (and_13_out, not_13_out, A28);
  xnor xnor_29 (xnor_29_out, A13, A29);
  and and_14 (and_14_out, not_14_out, A29);
  xnor xnor_30 (xnor_30_out, A14, A30);
  and and_15 (and_15_out, not_15_out, A30);
  xnor xnor_31 (xnor_31_out, A15, A31);
  and and_16 (and_16_out, not_16_out, A31);
  and and_17 (and_17_out, xnor_1_out, xnor_2_out);
  and and_18 (and_18_out, xnor_3_out, xnor_4_out);
  and and_19 (and_19_out, xnor_5_out, xnor_6_out);
  and and_20 (and_20_out, xnor_7_out, xnor_8_out);
  and and_21 (and_21_out, xnor_9_out, xnor_10_out);
  and and_22 (and_22_out, xnor_11_out, xnor_12_out);
  and and_23 (and_23_out, xnor_13_out, xnor_14_out);
  and and_24 (and_24_out, xnor_15_out, xnor_16_out);
  and and_25 (and_25_out, xnor_30_out, xnor_31_out);
  and and_26 (and_26_out, and_15_out, xnor_31_out);
  and and_27 (and_27_out, and_17_out, and_18_out);
  and and_28 (and_28_out, and_19_out, and_20_out);
  and and_29 (and_29_out, and_21_out, and_22_out);
  and and_30 (and_30_out, and_23_out, and_24_out);
  and and_31 (and_31_out, xnor_29_out, and_25_out);
  and and_32 (and_32_out, and_14_out, and_25_out);
  or or_1 (or_1_out, and_26_out, and_16_out);
  and and_33 (and_33_out, and_27_out, and_28_out);
  and and_34 (and_34_out, and_29_out, and_30_out);
  and and_35 (and_35_out, xnor_28_out, and_31_out);
  and and_36 (and_36_out, and_13_out, and_31_out);
  or or_2 (or_2_out, and_32_out, or_1_out);
  and and_37 (EQ, and_33_out, and_34_out);
  and and_38 (and_38_out, xnor_27_out, and_35_out);
  and and_39 (and_39_out, and_12_out, and_35_out);
  and and_40 (and_40_out, xnor_26_out, and_38_out);
  and and_41 (and_41_out, and_11_out, and_38_out);
  or or_3 (or_3_out, and_39_out, and_36_out);
  and and_42 (and_42_out, xnor_25_out, and_40_out);
  and and_43 (and_43_out, and_10_out, and_40_out);
  and and_44 (and_44_out, xnor_24_out, and_42_out);
  and and_45 (and_45_out, and_9_out, and_42_out);
  or or_4 (or_4_out, and_43_out, and_41_out);
  or or_5 (or_5_out, or_3_out, or_2_out);
  and and_46 (and_46_out, xnor_23_out, and_44_out);
  and and_47 (and_47_out, and_8_out, and_44_out);
  and and_48 (and_48_out, xnor_22_out, and_46_out);
  and and_49 (and_49_out, and_7_out, and_46_out);
  or or_6 (or_6_out, and_47_out, and_45_out);
  and and_50 (and_50_out, xnor_21_out, and_48_out);
  and and_51 (and_51_out, and_6_out, and_48_out);
  or or_7 (or_7_out, or_6_out, or_4_out);
  or or_8 (or_8_out, or_7_out, or_5_out);
  and and_52 (and_52_out, xnor_20_out, and_50_out);
  and and_53 (and_53_out, and_5_out, and_50_out);
  or or_9 (or_9_out, and_51_out, and_49_out);
  and and_54 (and_54_out, xnor_19_out, and_52_out);
  and and_55 (and_55_out, and_4_out, and_52_out);
  and and_56 (and_56_out, xnor_18_out, and_54_out);
  and and_57 (and_57_out, and_3_out, and_54_out);
  or or_10 (or_10_out, and_55_out, and_53_out);
  and and_58 (and_58_out, xnor_17_out, and_56_out);
  and and_59 (and_59_out, and_2_out, and_56_out);
  or or_11 (or_11_out, or_10_out, or_9_out);
  and and_60 (and_60_out, and_1_out, and_58_out);
  or or_12 (or_12_out, and_59_out, and_57_out);
  or or_13 (or_13_out, and_60_out, or_12_out);
  or or_14 (or_14_out, or_13_out, or_11_out);
  or or_15 (LT, or_14_out, or_8_out);
  not not_17 (not_17_out, EQ);
  not not_18 (not_18_out, LT);
  and and_61 (GT, not_17_out, not_18_out);
endmodule

/* Test case:
A0 A1 A2 A3 A4 A5 A6 A7 A8 A9 A10 A11 A12 A13 A14 A15 A16 A17 A18 A19 A20 A21 A22 A23 A24 A25 A26 A27 A28 A29 A30 A31 GT LT EQ
0 0 0 0 0 0 0 0 0 0 0 0 0 0 0 0  0 0 0 0 0 0 0 0 0 0 0 0 0 0 0 0  0 0 1
0 0 0 0 0 0 0 0 0 0 0 0 0 0 0 1  0 0 0 0 0 0 0 0 0 0 0 0 0 0 0 0  1 0 0
0 0 0 0 0 0 0 0 0 0 0 0 0 0 0 0  0 0 0 0 0 0 0 0 0 0 0 0 0 0 0 1  0 1 0
0 0 0 0 0 0 0 0 0 0 0 0 1 0 1 0  0 0 0 0 0 0 0 0 0 0 0 0 1 0 1 0  0 0 1
0 0 0 0 0 0 0 0 0 0 0 0 1 1 0 0  0 0 0 0 0 0 0 0 0 0 0 0 0 1 0 1  1 0 0
0 0 0 0 0 0 0 0 0 0 0 1 0 0 0 0  0 0 0 0 0 0 0 0 0 0 0 0 0 0 1 0  1 0 0
0 0 0 0 0 0 0 0 0 1 0 0 0 0 0 0  0 0 0 0 0 0 0 0 0 0 0 0 0 1 0 0  0 1 0
0 0 0 0 0 0 0 1 0 0 0 0 0 0 0 0  0 0 0 0 0 0 0 0 1 0 0 0 0 0 0 0  1 0 0
1 0 0 0 0 0 0 0 0 0 0 0 0 0 0 0  0 1 1 1 1 1 1 1 1 1 1 1 1 1 1 1  1 0 0
0 1 1 1 1 1 1 1 1 1 1 1 1 1 1 1  1 0 0 0 0 0 0 0 0 0 0 0 0 0 0 0  0 1 0
1 1 1 1 1 1 1 1 1 1 1 1 1 1 1 1  0 0 0 0 0 0 0 0 0 0 0 0 0 0 0 0  1 0 0
0 0 0 0 0 0 0 0 0 0 0 0 0 0 0 0  1 1 1 1 1 1 1 1 1 1 1 1 1 1 1 1  0 1 0
1 1 1 1 1 1 1 1 1 1 1 1 1 1 1 1  1 1 1 1 1 1 1 1 1 1 1 1 1 1 1 1  0 0 1
0 0 0 0 0 0 0 0 0 0 0 0 0 0 1 1  0 0 0 0 0 0 0 0 0 0 0 0 0 1 0 0  0 1 0
0 0 0 0 0 0 0 0 0 0 0 0 0 1 0 0  0 0 0 0 0 0 0 0 0 0 0 0 0 0 1 1  1 0 0
*/
