// Digital circuit 1 BIT ADDER DIV.dig as structural Verilog
module _1_BIT_ADDER_DIV (
  input  A,
  input  B,
  input  C,
  output S,
  output CO
);

  wire and_1_out, and_2_out, xor_1_out;

  xor xor_1 (xor_1_out, A, B);
  xor xor_2 (S, xor_1_out, C);
  and and_1 (and_1_out, xor_1_out, C);
  and and_2 (and_2_out, B, A);
  or or_1 (CO, and_1_out, and_2_out);
endmodule
