// Digital circuit A B CMP LT.dig as structural Verilog
module A_B_CMP_LT (
  input  A0,
  input  A1,
  input  A2,
  input  A3,
  input  A4,
  input  A5,
  input  A6,
  input  A7,
  input  A8,
  input  A9,
  input  A10,
  input  A11,
  input  A12,
  input  A13,
  input  A14,
  input  A15,
  input  B0,
  input  B1,
  input  B2,
  input  B3,
  input  B4,
  input  B5,
  input  B6,
  input  B7,
  input  B8,
  input  B9,
  input  B10,
  input  B11,
  input  B12,
  input  B13,
  input  B14,
  input  B15,
  output OUT
);

  wire and_1_out, and_2_out, and_3_out, and_4_out, and_5_out, and_6_out, and_7_out, and_8_out, and_9_out,
       and_10_out, and_11_out, and_12_out, and_13_out, and_14_out, and_15_out, and_16_out, and_17_out,
       and_18_out, and_19_out, and_20_out, and_21_out, and_22_out, and_23_out, and_24_out, and_25_out,
       and_26_out, and_27_out, and_28_out, and_29_out, and_30_out, and_31_out, and_32_out, and_33_out,
       and_34_out, and_35_out, and_36_out, and_37_out, and_38_out, and_39_out, and_40_out, and_41_out,
       and_42_out, and_43_out, and_44_out, and_45_out, not_1_out, not_2_out, not_3_out, not_4_out, not_5_out,
       not_6_out, not_7_out, not_8_out, not_9_out, not_10_out, not_11_out, not_12_out, not_13_out,
       not_14_out, not_15_out, not_16_out, or_1_out, or_2_out, or_3_out, or_4_out, or_5_out, or_6_out,
       or_7_out, or_8_out, or_9_out, or_10_out, or_11_out, or_12_out, or_13_out, or_14_out, xnor_1_out,
       xnor_2_out, xnor_3_out, xnor_4_out, xnor_5_out, xnor_6_out, xnor_7_out, xnor_8_out, xnor_9_out,
       xnor_10_out, xnor_11_out, xnor_12_out, xnor_13_out, xnor_14_out, xnor_15_out;

  not not_1 (not_1_out, A15);
  and and_1 (and_1_out, not_1_out, B15);
  not not_2 (not_2_out, A0);
  not not_3 (not_3_out, A1);
  not not_4 (not_4_out, A2);
  not not_5 (not_5_out, A3);
  not not_6 (not_6_out, A4);
  not not_7 (not_7_out, A5);
  not not_8 (not_8_out, A6);
  not not_9 (not_9_out, A7);
  not not_10 (not_10_out, A8);
  not not_11 (not_11_out, A9);
  not not_12 (not_12_out, A10);
  not not_13 (not_13_out, A11);
  not not_14 (not_14_out, A12);
  not not_15 (not_15_out, A13);
  not not_16 (not_16_out, A14);
  and and_2 (and_2_out, not_2_out, B0);
  and and_3 (and_3_out, not_3_out, B1);
  and and_4 (and_4_out, not_4_out, B2);
  and and_5 (and_5_out, not_5_out, B3);
  and and_6 (and_6_out, not_6_out, B4);
  and and_7 (and_7_out, not_7_out, B5);
  and and_8 (and_8_out, not_8_out, B6);
  and and_9 (and_9_out, not_9_out, B7);
  and and_10 (and_10_out, not_10_out, B8);
  and and_11 (and_11_out, not_11_out, B9);
  and and_12 (and_12_out, not_12_out, B10);
  and and_13 (and_13_out, not_13_out, B11);
  and and_14 (and_14_out, not_14_out, B12);
  and and_15 (and_15_out, not_15_out, B13);
  and and_16 (and_16_out, not_16_out, B14);
  xnor xnor_1 (xnor_1_out, A1, B1);
  xnor xnor_2 (xnor_2_out, A2, B2);
  xnor xnor_3 (xnor_3_out, A3, B3);
  xnor xnor_4 (xnor_4_out, A4, B4);
  xnor xnor_5 (xnor_5_out, A5, B5);
  xnor xnor_6 (xnor_6_out, A6, B6);
  xnor xnor_7 (xnor_7_out, A7, B7);
  xnor xnor_8 (xnor_8_out, A8, B8);
  xnor xnor_9 (xnor_9_out, A9, B9);
  xnor xnor_10 (xnor_10_out, A10, B10);
  xnor xnor_11 (xnor_11_out, A11, B11);
  xnor xnor_12 (xnor_12_out, A12, B12);
  xnor xnor_13 (xnor_13_out, A13, B13);
  xnor xnor_14 (xnor_14_out, A14, B14);
  xnor xnor_15 (xnor_15_out, A15, B15);
  and and_17 (and_17_out, xnor_14_out, xnor_15_out);
  and and_18 (and_18_out, and_16_out, xnor_15_out);
  and and_19 (and_19_out, xnor_13_out, and_17_out);
  and and_20 (and_20_out, and_15_out, and_17_out);
  or or_1 (or_1_out, and_18_out, and_1_out);
  and and_21 (and_21_out, xnor_12_out, and_19_out);
  and and_22 (and_22_out, and_14_out, and_19_out);
  or or_2 (or_2_out, and_20_out, or_1_out);
  and and_23 (and_23_out, xnor_11_out, and_21_out);
  and and_24 (and_24_out, and_13_out, and_21_out);
  or or_3 (or_3_out, and_22_out, or_2_out);
  and and_25 (and_25_out, xnor_10_out, and_23_out);
  and and_26 (and_26_out, and_12_out, and_23_out);
  or or_4 (or_4_out, and_24_out, or_3_out);
  and and_27 (and_27_out, xnor_9_out, and_25_out);
  and and_28 (and_28_out, and_11_out, and_25_out);
  or or_5 (or_5_out, and_26_out, or_4_out);
  and and_29 (and_29_out, xnor_8_out, and_27_out);
  and and_30 (and_30_out, and_10_out, and_27_out);
  or or_6 (or_6_out, and_28_out, or_5_out);
  and and_31 (and_31_out, xnor_7_out, and_29_out);
  and and_32 (and_32_out, and_9_out, and_29_out);
  or or_7 (or_7_out, and_30_out, or_6_out);
  and and_33 (and_33_out, xnor_6_out, and_31_out);
  and and_34 (and_34_out, and_8_out, and_31_out);
  or or_8 (or_8_out, and_32_out, or_7_out);
  and and_35 (and_35_out, xnor_5_out, and_33_out);
  and and_36 (and_36_out, and_7_out, and_33_out);
  or or_9 (or_9_out, and_34_out, or_8_out);
  and and_37 (and_37_out, xnor_4_out, and_35_out);
  and and_38 (and_38_out, and_6_out, and_35_out);
  or or_10 (or_10_out, and_36_out, or_9_out);
  and and_39 (and_39_out, xnor_3_out, and_37_out);
  and and_40 (and_40_out, and_5_out, and_37_out);
  or or_11 (or_11_out, and_38_out, or_10_out);
  and and_41 (and_41_out, xnor_2_out, and_39_out);
  and and_42 (and_42_out, and_4_out, and_39_out);
  or or_12 (or_12_out, and_40_out, or_11_out);
  and and_43 (and_43_out, xnor_1_out, and_41_out);
  and and_44 (and_44_out, and_3_out, and_41_out);
  or or_13 (or_13_out, and_42_out, or_12_out);
  and and_45 (and_45_out, and_2_out, and_43_out);
  or or_14 (or_14_out, and_44_out, or_13_out);
  or or_15 (OUT, and_45_out, or_14_out);
endmodule

/* Test case:
A0 A1 A2 A3 A4 A5 A6 A7 A8 A9 A10 A11 A12 A13 A14 A15 B0 B1 B2 B3 B4 B5 B6 B7 B8 B9 B10 B11 B12 B13 B14 B15 OUT

0 0 0 0 0 0 0 0 0 0 0 0 0 0 0 0   0 0 0 0 0 0 0 0 0 0 0 0 0 0 0 0   0
1 1 1 1 1 1 1 1 1 1 1 1 1 1 1 1   1 1 1 1 1 1 1 1 1 1 1 1 1 1 1 1   0

0 0 0 0 0 0 0 0 0 0 0 0 0 0 0 0   1 1 1 1 1 1 1 1 1 1 1 1 1 1 1 1   1
1 1 1 1 1 1 1 1 1 1 1 1 1 1 1 1   0 0 0 0 0 0 0 0 0 0 0 0 0 0 0 0   0

1 0 0 0 0 0 0 0 0 0 0 0 0 0 0 0   0 0 0 0 0 0 0 0 0 0 0 0 0 0 0 0   0
0 0 0 0 0 0 0 0 0 0 0 0 0 0 0 0   1 0 0 0 0 0 0 0 0 0 0 0 0 0 0 0   1

0 0 0 0 0 0 0 0 0 0 0 0 0 0 0 1   0 0 0 0 0 0 0 0 0 0 0 0 0 0 0 0   0
0 0 0 0 0 0 0 0 0 0 0 0 0 0 0 0   0 0 0 0 0 0 0 0 0 0 0 0 0 0 0 1   1

1 1 1 1 1 1 1 1 1 1 1 1 1 1 1 0   1 1 1 1 1 1 1 1 1 1 1 1 1 1 1 1   1
1 1 1 1 1 1 1 1 1 1 1 1 1 1 1 1   1 1 1 1 1 1 1 1 1 1 1 1 1 1 1 0   0

1 1 1 1 1 1 0 0 0 0 0 0 0 0 0 0   0 0 0 0 0 0 0 0 1 1 1 1 1 1 0 0   1

1 0 1 0 1 0 1 0 1 0 1 0 1 0 1 0   0 1 0 1 0 1 0 1 0 1 0 1 0 1 0 1   1
0 1 0 1 0 1 0 1 0 1 0 1 0 1 0 1   1 0 1 0 1 0 1 0 1 0 1 0 1 0 1 0   0

0 0 0 0 0 0 0 0 0 0 0 0 0 0 0 0   0 0 0 0 0 0 0 0 0 0 0 0 0 0 0 1   1
0 0 0 0 0 0 0 0 0 0 0 0 0 0 0 1   0 0 0 0 0 0 0 0 0 0 0 0 0 0 0 0   0

1 1 1 1 1 1 1 1 1 1 1 1 1 1 1 1   0 1 1 1 1 1 1 1 1 1 1 1 1 1 1 1   0
0 1 1 1 1 1 1 1 1 1 1 1 1 1 1 1   1 1 1 1 1 1 1 1 1 1 1 1 1 1 1 1   1
*/
