// Digital circuit COUNTER.dig as structural Verilog
module COUNTER (
  input  EN,
  input  CLK,
  input  RST,
  output O0,
  output O1,
  output O2,
  output O3,
  output O4,
  output O5,
  output O6,
  output O7,
  output O8,
  output O9,
  output O10,
  output O11,
  output O12,
  output O13,
  output O14,
  output O15
);

  wire and_1_out, and_2_out, and_3_out, and_4_out, and_5_out, and_6_out, and_7_out, and_8_out, and_9_out,
       and_10_out, and_11_out, and_12_out, and_13_out, and_14_out, and_15_out;

  T_RST t_rst_1 (.T(EN), .CLK(CLK), .RST(RST), .Q(O0));
  and and_1 (and_1_out, O0, EN);
  T_RST t_rst_2 (.T(and_1_out), .CLK(CLK), .RST(RST), .Q(O1));
  and and_2 (and_2_out, O1, and_1_out);
  T_RST t_rst_3 (.T(and_2_out), .CLK(CLK), .RST(RST), .Q(O2));
  and and_3 (and_3_out, O2, and_2_out);
  T_RST t_rst_4 (.T(and_3_out), .CLK(CLK), .RST(RST), .Q(O3));
  and and_4 (and_4_out, O3, and_3_out);
  T_RST t_rst_5 (.T(and_4_out), .CLK(CLK), .RST(RST), .Q(O4));
  and and_5 (and_5_out, O4, and_4_out);
  T_RST t_rst_6 (.T(and_5_out), .CLK(CLK), .RST(RST), .Q(O5));
  and and_6 (and_6_out, O5, and_5_out);
  T_RST t_rst_7 (.T(and_6_out), .CLK(CLK), .RST(RST), .Q(O6));
  and and_7 (and_7_out, O6, and_6_out);
  T_RST t_rst_8 (.T(and_7_out), .CLK(CLK), .RST(RST), .Q(O7));
  and and_8 (and_8_out, O7, and_7_out);
  T_RST t_rst_9 (.T(and_8_out), .CLK(CLK), .RST(RST), .Q(O8));
  and and_9 (and_9_out, O8, and_8_out);
  T_RST t_rst_10 (.T(and_9_out), .CLK(CLK), .RST(RST), .Q(O9));
  and and_10 (and_10_out, O9, and_9_out);
  T_RST t_rst_11 (.T(and_10_out), .CLK(CLK), .RST(RST), .Q(O10));
  and and_11 (and_11_out, O10, and_10_out);
  T_RST t_rst_12 (.T(and_11_out), .CLK(CLK), .RST(RST), .Q(O11));
  and and_12 (and_12_out, O11, and_11_out);
  T_RST t_rst_13 (.T(and_12_out), .CLK(CLK), .RST(RST), .Q(O12));
  and and_13 (and_13_out, O12, and_12_out);
  T_RST t_rst_14 (.T(and_13_out), .CLK(CLK), .RST(RST), .Q(O13));
  and and_14 (and_14_out, O13, and_13_out);
  T_RST t_rst_15 (.T(and_14_out), .CLK(CLK), .RST(RST), .Q(O14));
  and and_15 (and_15_out, O14, and_14_out);
  T_RST t_rst_16 (.T(and_15_out), .CLK(CLK), .RST(RST), .Q(O15));

  // Notes on the sheet:
  //   CLK: Hz: 2147483647
endmodule
