// Digital circuit D RST.dig as structural Verilog
module D_RST (
  input  CLK,
  input  RST,
  input  DIN,
  output Q
);

  wire and_1_out, not_1_out;

  not not_1 (not_1_out, RST);
  D_FF d_ff_1 (.D(and_1_out), .C(CLK), .Q(Q));  // open: nQ
  and and_1 (and_1_out, not_1_out, DIN);

  // Notes on the sheet:
  //   CLK: Hz: 10
endmodule
