// Digital circuit GPREG DIV.dig as structural Verilog
module GPREG_DIV (
  input  RST,
  input  EN,
  input  DIN1,
  input  CLK,
  input  DIN2,
  input  DIN3,
  input  DIN4,
  input  DIN5,
  input  DIN6,
  input  DIN7,
  input  DIN8,
  input  DIN9,
  input  DIN10,
  input  DIN11,
  input  DIN12,
  input  DIN13,
  input  DIN14,
  input  DIN15,
  input  DIN0,
  output DO0,
  output DO1,
  output DO2,
  output DO3,
  output DO4,
  output DO5,
  output DO6,
  output DO7,
  output DO8,
  output DO9,
  output DO10,
  output DO11,
  output DO12,
  output DO13,
  output DO14,
  output DO15
);

  // _1_BIT_REG_DIV _1_bit_reg_div_1: pin names not known; wires that end beside it: CLK, RST, EN, DIN0, DO0
  // _1_BIT_REG_DIV _1_bit_reg_div_2: pin names not known; wires that end beside it: CLK, RST, EN, DIN2, DO2
  // _1_BIT_REG_DIV _1_bit_reg_div_3: pin names not known; wires that end beside it: CLK, RST, EN, DIN4, DO4
  // _1_BIT_REG_DIV _1_bit_reg_div_4: pin names not known; wires that end beside it: CLK, RST, EN, DIN6, DO6
  // _1_BIT_REG_DIV _1_bit_reg_div_5: pin names not known; wires that end beside it: CLK, RST, EN, DIN8, DO8
  // _1_BIT_REG_DIV _1_bit_reg_div_6: pin names not known; wires that end beside it: CLK, RST, EN, DIN10, DO10
  // _1_BIT_REG_DIV _1_bit_reg_div_7: pin names not known; wires that end beside it: CLK, RST, EN, DIN12, DO12
  // _1_BIT_REG_DIV _1_bit_reg_div_8: pin names not known; wires that end beside it: CLK, RST, EN, DIN14, DO14
  // _1_BIT_REG_DIV _1_bit_reg_div_9: pin names not known; wires that end beside it: CLK, RST, EN, DIN1, DO1
  // _1_BIT_REG_DIV _1_bit_reg_div_10: pin names not known; wires that end beside it: CLK, RST, EN, DIN3, DO3
  // _1_BIT_REG_DIV _1_bit_reg_div_11: pin names not known; wires that end beside it: CLK, RST, EN, DIN5, DO5
  // _1_BIT_REG_DIV _1_bit_reg_div_12: pin names not known; wires that end beside it: CLK, RST, EN, DIN7, DO7
  // _1_BIT_REG_DIV _1_bit_reg_div_13: pin names not known; wires that end beside it: CLK, RST, EN, DIN9, DO9
  // _1_BIT_REG_DIV _1_bit_reg_div_14: pin names not known; wires that end beside it: CLK, RST, EN, DIN11, DO11
  // _1_BIT_REG_DIV _1_bit_reg_div_15: pin names not known; wires that end beside it: CLK, RST, EN, DIN13, DO13
  // _1_BIT_REG_DIV _1_bit_reg_div_16: pin names not known; wires that end beside it: CLK, RST, EN, DIN15, DO15

  // Notes on the sheet:
  //   CLK: Hz: 10
endmodule
