// Digital circuit SUBTRACTOR DIV V1.dig as structural Verilog
module SUBTRACTOR_DIV_V1 (
  input  A0,
  input  B0,
  input  A1,
  input  B1,
  input  A2,
  input  B2,
  input  A3,
  input  B3,
  input  A4,
  input  B4,
  input  A5,
  input  B5,
  input  A6,
  input  B6,
  input  A7,
  input  B7,
  input  A8,
  input  B8,
  input  A9,
  input  B9,
  input  A10,
  input  B10,
  input  A11,
  input  B11,
  input  A12,
  input  B12,
  input  A13,
  input  B13,
  input  A14,
  input  B14,
  input  A15,
  input  B15,
  output O0,
  output O1,
  output O2,
  output O3,
  output O4,
  output O5,
  output O6,
  output O7,
  output O8,
  output O9,
  output O10,
  output O11,
  output O12,
  output O13,
  output O14,
  output O15
);

  wire not_1_out, not_2_out, not_3_out, not_4_out, not_5_out, not_6_out, not_7_out, not_8_out, not_9_out,
       not_10_out, not_11_out, not_12_out, not_13_out, not_14_out, not_15_out, not_16_out;

  not not_1 (not_1_out, B0);
  not not_2 (not_2_out, B1);
  not not_3 (not_3_out, B2);
  not not_4 (not_4_out, B3);
  not not_5 (not_5_out, B4);
  not not_6 (not_6_out, B5);
  not not_7 (not_7_out, B6);
  not not_8 (not_8_out, B7);
  not not_9 (not_9_out, B8);
  not not_10 (not_10_out, B9);
  not not_11 (not_11_out, B10);
  not not_12 (not_12_out, B11);
  not not_13 (not_13_out, B12);
  not not_14 (not_14_out, B13);
  not not_15 (not_15_out, B14);
  not not_16 (not_16_out, B15);
  ADDER_V1_DIV adder_v1_div_1 (
    .CIN(1'b1), .A0(A0), .A1(A1), .A2(A2), .A3(A3), .A4(A4), .A5(A5), .A6(A6), .A7(A7), .A8(A8), .A9(A9),
    .A10(A10), .A11(A11), .A12(A12), .A13(A13), .A14(A14), .A15(A15), .A16(not_1_out), .A17(not_2_out),
    .A18(not_3_out), .A19(not_4_out), .A20(not_5_out), .A21(not_6_out), .A22(not_7_out), .A23(not_8_out),
    .A24(not_9_out), .A25(not_10_out), .A26(not_11_out), .A27(not_12_out), .A28(not_13_out),
    .A29(not_14_out), .A30(not_15_out), .A31(not_16_out), .S0(O0), .S1(O1), .S2(O2), .S3(O3), .S4(O4),
    .S5(O5), .S6(O6), .S7(O7), .S8(O8), .S9(O9), .S10(O10), .S11(O11), .S12(O12), .S13(O13), .S14(O14),
    .S15(O15));  // open: COUT
endmodule
