// Digital circuit T RST.dig as structural Verilog
module T_RST (
  input  T,
  input  CLK,
  input  RST,
  output Q
);

  wire and_1_out, and_2_out, not_1_out, or_1_out;

  and and_1 (and_1_out, T, not_1_out);
  not not_1 (not_1_out, RST);
  and and_2 (and_2_out, RST, Q);
  T_FF t_ff_1 (.T(or_1_out), .C(CLK), .Q(Q));  // open: nQ
  or or_1 (or_1_out, and_1_out, and_2_out);
endmodule
