// Digital circuit UNSIGNED_DIVIDER_V1.dig as structural Verilog
module UNSIGNED_DIVIDER_V1 (
  input  A0,
  input  B0,
  input  A1,
  input  B1,
  input  A2,
  input  B2,
  input  A3,
  input  B3,
  input  A4,
  input  B4,
  input  A5,
  input  B5,
  input  A6,
  input  B6,
  input  A7,
  input  B7,
  input  A8,
  input  B8,
  input  A9,
  input  B9,
  input  A10,
  input  B10,
  input  A11,
  input  B11,
  input  A12,
  input  B12,
  input  A13,
  input  B13,
  input  A14,
  input  B14,
  input  A15,
  input  B15,
  input  EN,
  input  CLK,
  input  D_BAR_M,
  output O0,
  output O1,
  output O2,
  output O3,
  output O4,
  output O5,
  output O6,
  output O7,
  output O8,
  output O9,
  output O10,
  output O11,
  output O12,
  output O13,
  output O14,
  output O15,
  output CMF
);

  wire _2x1_mux_16_bit_div_1_p17, _2x1_mux_16_bit_div_1_p18, _2x1_mux_16_bit_div_1_p19,
       _2x1_mux_16_bit_div_1_p20, _2x1_mux_16_bit_div_1_p21, _2x1_mux_16_bit_div_1_p22,
       _2x1_mux_16_bit_div_1_p23, _2x1_mux_16_bit_div_1_p24, _2x1_mux_16_bit_div_1_p25,
       _2x1_mux_16_bit_div_1_p26, _2x1_mux_16_bit_div_1_p27, _2x1_mux_16_bit_div_1_p28,
       _2x1_mux_16_bit_div_1_p29, _2x1_mux_16_bit_div_1_p30, _2x1_mux_16_bit_div_1_p31,
       _2x1_mux_16_bit_div_1_p32, _2x1_mux_16_bit_div_1_p33, _2x1_mux_16_bit_div_1_p34,
       _2x1_mux_16_bit_div_1_p35, _2x1_mux_16_bit_div_1_p36, _2x1_mux_16_bit_div_1_p37,
       _2x1_mux_16_bit_div_1_p38, _2x1_mux_16_bit_div_1_p39, _2x1_mux_16_bit_div_1_p40,
       _2x1_mux_16_bit_div_1_p41, _2x1_mux_16_bit_div_1_p42, _2x1_mux_16_bit_div_1_p43, a_b_cmp_lt_1_out,
       and_1_out, and_2_out, and_3_out, counter_1_o0, counter_1_o1, counter_1_o2, counter_1_o3, counter_1_o4,
       counter_1_o5, counter_1_o6, counter_1_o7, counter_1_o8, counter_1_o9, counter_1_o10, counter_1_o11,
       counter_1_o12, counter_1_o13, counter_1_o14, counter_1_o15, d_rst_1_q, gpreg_div_1_do14,
       gpreg_div_1_do15, not_1_out, not_2_out, not_3_out, not_4_out, not_5_out, not_6_out, not_7_out,
       or_1_out, or_2_out, or_3_out, or_4_out, or_5_out, or_6_out, or_7_out, or_8_out, or_9_out, or_10_out,
       or_11_out, or_12_out, or_13_out, or_14_out, or_15_out, or_16_out, subtractor_div_v1_1_o0,
       subtractor_div_v1_1_o1, subtractor_div_v1_1_o2, subtractor_div_v1_1_o3, subtractor_div_v1_1_o4,
       subtractor_div_v1_1_o5, subtractor_div_v1_1_o6, subtractor_div_v1_1_o7, subtractor_div_v1_1_o8,
       subtractor_div_v1_1_o9, subtractor_div_v1_1_o10, subtractor_div_v1_1_o11, subtractor_div_v1_1_o12,
       subtractor_div_v1_1_o13, subtractor_div_v1_1_o14, subtractor_div_v1_1_o15, undriven, undriven_2,
       undriven_3;

  D_RST d_rst_1 (.CLK(CLK), .RST(not_1_out), .DIN(EN), .Q(d_rst_1_q));
  not not_1 (not_1_out, EN);
  // _2X1_MUX_16_BIT_DIV _2x1_mux_16_bit_div_1: pin names not known; wires that end beside it: A0, A1, A2, A3, A4, A5, A6, A7, A8, A9, A10, A11, A12, A13, A14, A15, _2x1_mux_16_bit_div_1_p17, _2x1_mux_16_bit_div_1_p18, _2x1_mux_16_bit_div_1_p19, _2x1_mux_16_bit_div_1_p20, _2x1_mux_16_bit_div_1_p21, _2x1_mux_16_bit_div_1_p22, _2x1_mux_16_bit_div_1_p23, _2x1_mux_16_bit_div_1_p24, _2x1_mux_16_bit_div_1_p25, _2x1_mux_16_bit_div_1_p26, _2x1_mux_16_bit_div_1_p27, _2x1_mux_16_bit_div_1_p28, _2x1_mux_16_bit_div_1_p29, _2x1_mux_16_bit_div_1_p30, _2x1_mux_16_bit_div_1_p31, _2x1_mux_16_bit_div_1_p32, _2x1_mux_16_bit_div_1_p33, _2x1_mux_16_bit_div_1_p34, _2x1_mux_16_bit_div_1_p35, _2x1_mux_16_bit_div_1_p36, _2x1_mux_16_bit_div_1_p37, _2x1_mux_16_bit_div_1_p38, _2x1_mux_16_bit_div_1_p39, _2x1_mux_16_bit_div_1_p40, _2x1_mux_16_bit_div_1_p41, _2x1_mux_16_bit_div_1_p42, _2x1_mux_16_bit_div_1_p43
  SUBTRACTOR_DIV_V1 subtractor_div_v1_1 (
    .A0(_2x1_mux_16_bit_div_1_p31), .A1(_2x1_mux_16_bit_div_1_p32), .A2(_2x1_mux_16_bit_div_1_p33),
    .A3(_2x1_mux_16_bit_div_1_p34), .A4(_2x1_mux_16_bit_div_1_p35), .A5(_2x1_mux_16_bit_div_1_p36),
    .A6(_2x1_mux_16_bit_div_1_p37), .A7(_2x1_mux_16_bit_div_1_p38), .A8(_2x1_mux_16_bit_div_1_p39),
    .A9(_2x1_mux_16_bit_div_1_p40), .A10(_2x1_mux_16_bit_div_1_p41), .A11(_2x1_mux_16_bit_div_1_p42),
    .A12(_2x1_mux_16_bit_div_1_p43), .A13(undriven), .A14(undriven_2), .A15(undriven_3), .B0(B0), .B1(B1),
    .B2(B2), .B3(B3), .B4(B4), .B5(B5), .B6(B6), .B7(B7), .B8(B8), .B9(B9), .B10(B10), .B11(B11), .B12(B12),
    .B13(B13), .B14(B14), .B15(B15), .O0(subtractor_div_v1_1_o0), .O1(subtractor_div_v1_1_o1),
    .O2(subtractor_div_v1_1_o2), .O3(subtractor_div_v1_1_o3), .O4(subtractor_div_v1_1_o4),
    .O5(subtractor_div_v1_1_o5), .O6(subtractor_div_v1_1_o6), .O7(subtractor_div_v1_1_o7),
    .O8(subtractor_div_v1_1_o8), .O9(subtractor_div_v1_1_o9), .O10(subtractor_div_v1_1_o10),
    .O11(subtractor_div_v1_1_o11), .O12(subtractor_div_v1_1_o12), .O13(subtractor_div_v1_1_o13),
    .O14(subtractor_div_v1_1_o14), .O15(subtractor_div_v1_1_o15));
  A_B_CMP_LT a_b_cmp_lt_1 (
    .A0(_2x1_mux_16_bit_div_1_p31), .A1(_2x1_mux_16_bit_div_1_p32), .A2(_2x1_mux_16_bit_div_1_p33),
    .A3(_2x1_mux_16_bit_div_1_p34), .A4(_2x1_mux_16_bit_div_1_p35), .A5(_2x1_mux_16_bit_div_1_p36),
    .A6(_2x1_mux_16_bit_div_1_p37), .A7(_2x1_mux_16_bit_div_1_p38), .A8(_2x1_mux_16_bit_div_1_p39),
    .A9(_2x1_mux_16_bit_div_1_p40), .A10(_2x1_mux_16_bit_div_1_p41), .A11(_2x1_mux_16_bit_div_1_p42),
    .A12(_2x1_mux_16_bit_div_1_p43), .A13(undriven), .A14(undriven_2), .A15(undriven_3), .B0(B0), .B1(B1),
    .B2(B2), .B3(B3), .B4(B4), .B5(B5), .B6(B6), .B7(B7), .B8(B8), .B9(B9), .B10(B10), .B11(B11), .B12(B12),
    .B13(B13), .B14(B14), .B15(B15), .OUT(a_b_cmp_lt_1_out));
  or or_1 (or_1_out, B2, B3);
  or or_2 (or_2_out, B6, B7);
  or or_3 (or_3_out, B10, B11);
  or or_4 (or_4_out, B14, B15);
  not not_2 (not_2_out, a_b_cmp_lt_1_out);
  or or_5 (or_5_out, B0, B1);
  or or_6 (or_6_out, B4, B5);
  or or_7 (or_7_out, B8, B9);
  or or_8 (or_8_out, B12, B13);
  and and_1 (and_1_out, or_16_out, not_2_out);
  or or_9 (or_9_out, or_5_out, or_1_out);
  or or_10 (or_10_out, or_6_out, or_2_out);
  or or_11 (or_11_out, or_7_out, or_3_out);
  or or_12 (or_12_out, or_8_out, or_4_out);
  not not_3 (not_3_out, or_16_out);
  or or_13 (or_13_out, or_9_out, or_10_out);
  or or_14 (or_14_out, or_11_out, or_12_out);
  and and_2 (and_2_out, EN, and_1_out);
  or or_15 (or_15_out, a_b_cmp_lt_1_out, not_3_out);
  or or_16 (or_16_out, or_13_out, or_14_out);
  not not_4 (not_4_out, EN);
  not not_5 (not_5_out, EN);
  GPREG_DIV gpreg_div_1 (
    .DIN0(subtractor_div_v1_1_o0), .DIN1(subtractor_div_v1_1_o1), .DIN2(subtractor_div_v1_1_o2),
    .DIN3(subtractor_div_v1_1_o3), .DIN4(subtractor_div_v1_1_o4), .DIN5(subtractor_div_v1_1_o5),
    .DIN6(subtractor_div_v1_1_o6), .DIN7(subtractor_div_v1_1_o7), .DIN8(subtractor_div_v1_1_o8),
    .DIN9(subtractor_div_v1_1_o9), .DIN10(subtractor_div_v1_1_o10), .DIN11(subtractor_div_v1_1_o11),
    .DIN12(subtractor_div_v1_1_o12), .DIN13(subtractor_div_v1_1_o13), .DIN14(subtractor_div_v1_1_o14),
    .DIN15(subtractor_div_v1_1_o15), .CLK(CLK), .RST(not_4_out), .EN(and_2_out),
    .DO0(_2x1_mux_16_bit_div_1_p17), .DO1(_2x1_mux_16_bit_div_1_p18), .DO2(_2x1_mux_16_bit_div_1_p19),
    .DO3(_2x1_mux_16_bit_div_1_p20), .DO4(_2x1_mux_16_bit_div_1_p21), .DO5(_2x1_mux_16_bit_div_1_p22),
    .DO6(_2x1_mux_16_bit_div_1_p23), .DO7(_2x1_mux_16_bit_div_1_p24), .DO8(_2x1_mux_16_bit_div_1_p25),
    .DO9(_2x1_mux_16_bit_div_1_p26), .DO10(_2x1_mux_16_bit_div_1_p27), .DO11(_2x1_mux_16_bit_div_1_p28),
    .DO12(_2x1_mux_16_bit_div_1_p29), .DO13(_2x1_mux_16_bit_div_1_p30), .DO14(gpreg_div_1_do14),
    .DO15(gpreg_div_1_do15));
  D_RST d_rst_2 (.CLK(CLK), .RST(not_6_out), .DIN(or_15_out), .Q(CMF));
  not not_6 (not_6_out, EN);
  and and_3 (and_3_out, EN, and_1_out);
  not not_7 (not_7_out, D_BAR_M);
  COUNTER counter_1 (
    .CLK(CLK), .RST(not_5_out), .EN(and_3_out), .O0(counter_1_o0), .O1(counter_1_o1), .O2(counter_1_o2),
    .O3(counter_1_o3), .O4(counter_1_o4), .O5(counter_1_o5), .O6(counter_1_o6), .O7(counter_1_o7),
    .O8(counter_1_o8), .O9(counter_1_o9), .O10(counter_1_o10), .O11(counter_1_o11), .O12(counter_1_o12),
    .O13(counter_1_o13), .O14(counter_1_o14), .O15(counter_1_o15));
  // _2X1_MUX_16_BIT_DIV _2x1_mux_16_bit_div_2: pin names not known; wires that end beside it: _2x1_mux_16_bit_div_1_p17, _2x1_mux_16_bit_div_1_p18, _2x1_mux_16_bit_div_1_p19, _2x1_mux_16_bit_div_1_p20, _2x1_mux_16_bit_div_1_p21, _2x1_mux_16_bit_div_1_p22, _2x1_mux_16_bit_div_1_p23, _2x1_mux_16_bit_div_1_p24, _2x1_mux_16_bit_div_1_p25, _2x1_mux_16_bit_div_1_p26, _2x1_mux_16_bit_div_1_p27, _2x1_mux_16_bit_div_1_p28, _2x1_mux_16_bit_div_1_p29, _2x1_mux_16_bit_div_1_p30, gpreg_div_1_do14, gpreg_div_1_do15, counter_1_o0, counter_1_o1, counter_1_o2, counter_1_o3, counter_1_o4, counter_1_o5, counter_1_o6, counter_1_o7, counter_1_o8, counter_1_o9, counter_1_o10, counter_1_o11, counter_1_o12, counter_1_o13, O0, O1, O2, O3, O4, O5, O6, O7, O8, O9, O10, O11, O12

  // Notes on the sheet:
  //   CLK: Hz: 5000
endmodule
