// Digital circuit LOGIC CORE.dig as structural Verilog
module LOGIC_CORE (
  input  A0,
  input  B0,
  input  A1,
  input  B1,
  input  A2,
  input  B2,
  input  A3,
  input  B3,
  input  A4,
  input  B4,
  input  A5,
  input  B5,
  input  A6,
  input  B6,
  input  A7,
  input  B7,
  input  A8,
  input  B8,
  input  A9,
  input  B9,
  input  A10,
  input  B10,
  input  A11,
  input  B11,
  input  A12,
  input  B12,
  input  A13,
  input  B13,
  input  A14,
  input  B14,
  input  A15,
  input  B15,
  input  S0,
  input  S1,
  input  S2,
  input  EN,
  output O0,
  output O1,
  output O2,
  output O3,
  output O4,
  output O5,
  output O6,
  output O7,
  output O8,
  output O9,
  output O10,
  output O11,
  output O12,
  output O13,
  output O14,
  output O15
);

  wire _4x1_mux_16_bit_v1_1_1_o0, _4x1_mux_16_bit_v1_1_1_o1, _4x1_mux_16_bit_v1_1_1_o2,
       _4x1_mux_16_bit_v1_1_1_o3, _4x1_mux_16_bit_v1_1_1_o4, _4x1_mux_16_bit_v1_1_1_o5,
       _4x1_mux_16_bit_v1_1_1_o6, _4x1_mux_16_bit_v1_1_1_o7, _4x1_mux_16_bit_v1_1_1_o8,
       _4x1_mux_16_bit_v1_1_1_o9, _4x1_mux_16_bit_v1_1_1_o10, _4x1_mux_16_bit_v1_1_1_o11,
       _4x1_mux_16_bit_v1_1_1_o12, _4x1_mux_16_bit_v1_1_1_o13, _4x1_mux_16_bit_v1_1_1_o14,
       _4x1_mux_16_bit_v1_1_1_o15, and_1_out, and_2_out, and_3_out, and_4_out, and_5_out, and_6_out,
       and_7_out, and_8_out, and_9_out, and_10_out, and_11_out, and_12_out, and_13_out, and_14_out,
       and_15_out, and_16_out, not_1_out, not_2_out, not_3_out, not_4_out, not_5_out, not_6_out, not_7_out,
       not_8_out, not_9_out, not_10_out, not_11_out, not_12_out, not_13_out, not_14_out, not_15_out,
       not_16_out, or_1_out, or_2_out, or_3_out, or_4_out, or_5_out, or_6_out, or_7_out, or_8_out, or_9_out,
       or_10_out, or_11_out, or_12_out, or_13_out, or_14_out, or_15_out, or_16_out, xor_1_out, xor_2_out,
       xor_3_out, xor_4_out, xor_5_out, xor_6_out, xor_7_out, xor_8_out, xor_9_out, xor_10_out, xor_11_out,
       xor_12_out, xor_13_out, xor_14_out, xor_15_out, xor_16_out;

  or or_1 (or_1_out, A0, B0);
  or or_2 (or_2_out, A1, B1);
  or or_3 (or_3_out, A2, B2);
  or or_4 (or_4_out, A3, B3);
  or or_5 (or_5_out, A4, B4);
  or or_6 (or_6_out, A5, B5);
  or or_7 (or_7_out, A6, B6);
  or or_8 (or_8_out, A7, B7);
  or or_9 (or_9_out, A8, B8);
  or or_10 (or_10_out, A9, B9);
  or or_11 (or_11_out, A10, B10);
  or or_12 (or_12_out, A11, B11);
  or or_13 (or_13_out, A12, B12);
  or or_14 (or_14_out, A13, B13);
  or or_15 (or_15_out, A14, B14);
  or or_16 (or_16_out, A15, B15);
  not not_1 (not_1_out, A0);
  not not_2 (not_2_out, A1);
  not not_3 (not_3_out, A2);
  not not_4 (not_4_out, A3);
  not not_5 (not_5_out, A4);
  not not_6 (not_6_out, A5);
  not not_7 (not_7_out, A6);
  not not_8 (not_8_out, A7);
  not not_9 (not_9_out, A8);
  not not_10 (not_10_out, A9);
  not not_11 (not_11_out, A10);
  not not_12 (not_12_out, A11);
  not not_13 (not_13_out, A12);
  not not_14 (not_14_out, A13);
  not not_15 (not_15_out, A14);
  not not_16 (not_16_out, A15);
  and and_1 (and_1_out, A0, B0);
  and and_2 (and_2_out, A1, B1);
  and and_3 (and_3_out, A2, B2);
  and and_4 (and_4_out, A3, B3);
  and and_5 (and_5_out, A4, B4);
  and and_6 (and_6_out, A5, B5);
  and and_7 (and_7_out, A6, B6);
  and and_8 (and_8_out, A7, B7);
  and and_9 (and_9_out, A8, B8);
  and and_10 (and_10_out, A9, B9);
  and and_11 (and_11_out, A10, B10);
  and and_12 (and_12_out, A11, B11);
  and and_13 (and_13_out, A12, B12);
  and and_14 (and_14_out, A13, B13);
  and and_15 (and_15_out, A14, B14);
  and and_16 (and_16_out, A15, B15);
  xor xor_1 (xor_1_out, A0, B0);
  xor xor_2 (xor_2_out, A1, B1);
  xor xor_3 (xor_3_out, A2, B2);
  xor xor_4 (xor_4_out, A3, B3);
  xor xor_5 (xor_5_out, A4, B4);
  xor xor_6 (xor_6_out, A5, B5);
  xor xor_7 (xor_7_out, A6, B6);
  xor xor_8 (xor_8_out, A7, B7);
  xor xor_9 (xor_9_out, A8, B8);
  xor xor_10 (xor_10_out, A9, B9);
  xor xor_11 (xor_11_out, A10, B10);
  xor xor_12 (xor_12_out, A11, B11);
  xor xor_13 (xor_13_out, A12, B12);
  xor xor_14 (xor_14_out, A13, B13);
  xor xor_15 (xor_15_out, A14, B14);
  xor xor_16 (xor_16_out, A15, B15);
  _4X1_MUX_16_BIT_V1_1 _4x1_mux_16_bit_v1_1_1 (
    .O0(_4x1_mux_16_bit_v1_1_1_o0), .O1(_4x1_mux_16_bit_v1_1_1_o1), .O2(_4x1_mux_16_bit_v1_1_1_o2),
    .O3(_4x1_mux_16_bit_v1_1_1_o3), .O4(_4x1_mux_16_bit_v1_1_1_o4), .O5(_4x1_mux_16_bit_v1_1_1_o5),
    .O6(_4x1_mux_16_bit_v1_1_1_o6), .O7(_4x1_mux_16_bit_v1_1_1_o7), .O8(_4x1_mux_16_bit_v1_1_1_o8),
    .O9(_4x1_mux_16_bit_v1_1_1_o9), .O10(_4x1_mux_16_bit_v1_1_1_o10), .O11(_4x1_mux_16_bit_v1_1_1_o11),
    .O12(_4x1_mux_16_bit_v1_1_1_o12), .O13(_4x1_mux_16_bit_v1_1_1_o13), .O14(_4x1_mux_16_bit_v1_1_1_o14),
    .O15(_4x1_mux_16_bit_v1_1_1_o15), .IN0_0(not_1_out), .IN0_1(not_2_out), .IN0_2(not_3_out),
    .IN0_3(not_4_out), .IN0_4(not_5_out), .IN0_5(not_6_out), .IN0_6(not_7_out), .IN0_7(not_8_out),
    .IN0_8(not_9_out), .IN0_9(not_10_out), .IN0_10(not_11_out), .IN0_11(not_12_out), .IN0_12(not_13_out),
    .IN0_13(not_14_out), .IN0_14(not_15_out), .IN0_15(not_16_out), .IN1_0(or_1_out), .IN1_1(or_2_out),
    .IN1_2(or_3_out), .IN1_3(or_4_out), .IN1_4(or_5_out), .IN1_5(or_6_out), .IN1_6(or_7_out),
    .IN1_7(or_8_out), .IN1_8(or_9_out), .IN1_9(or_10_out), .IN1_10(or_11_out), .IN1_11(or_12_out),
    .IN1_12(or_13_out), .IN1_13(or_14_out), .IN1_14(or_15_out), .IN1_15(or_16_out), .IN2_0(and_1_out),
    .IN2_1(and_2_out), .IN2_2(and_3_out), .IN2_3(and_4_out), .IN2_4(and_5_out), .IN2_5(and_6_out),
    .IN2_6(and_7_out), .IN2_7(and_8_out), .IN2_8(and_9_out), .IN2_9(and_10_out), .IN2_10(and_11_out),
    .IN2_11(and_12_out), .IN2_12(and_13_out), .IN2_13(and_14_out), .IN2_14(and_15_out), .IN2_15(and_16_out),
    .IN3_0(xor_1_out), .IN3_1(xor_2_out), .IN3_2(xor_3_out), .IN3_3(xor_4_out), .IN3_4(xor_5_out),
    .IN3_5(xor_6_out), .IN3_6(xor_7_out), .IN3_7(xor_8_out), .IN3_8(xor_9_out), .IN3_9(xor_10_out),
    .IN3_10(xor_11_out), .IN3_11(xor_12_out), .IN3_12(xor_13_out), .IN3_13(xor_14_out), .IN3_14(xor_15_out),
    .IN3_15(xor_16_out), .S0(S0), .S1(S1), .EN(EN));
  xor xor_17 (O0, _4x1_mux_16_bit_v1_1_1_o0, S2);
  xor xor_18 (O1, _4x1_mux_16_bit_v1_1_1_o1, S2);
  xor xor_19 (O2, _4x1_mux_16_bit_v1_1_1_o2, S2);
  xor xor_20 (O3, _4x1_mux_16_bit_v1_1_1_o3, S2);
  xor xor_21 (O4, _4x1_mux_16_bit_v1_1_1_o4, S2);
  xor xor_22 (O5, _4x1_mux_16_bit_v1_1_1_o5, S2);
  xor xor_23 (O6, _4x1_mux_16_bit_v1_1_1_o6, S2);
  xor xor_24 (O7, _4x1_mux_16_bit_v1_1_1_o7, S2);
  xor xor_25 (O8, _4x1_mux_16_bit_v1_1_1_o8, S2);
  xor xor_26 (O9, _4x1_mux_16_bit_v1_1_1_o9, S2);
  xor xor_27 (O10, _4x1_mux_16_bit_v1_1_1_o10, S2);
  xor xor_28 (O11, _4x1_mux_16_bit_v1_1_1_o11, S2);
  xor xor_29 (O12, _4x1_mux_16_bit_v1_1_1_o12, S2);
  xor xor_30 (O13, _4x1_mux_16_bit_v1_1_1_o13, S2);
  xor xor_31 (O14, _4x1_mux_16_bit_v1_1_1_o14, S2);
  xor xor_32 (O15, _4x1_mux_16_bit_v1_1_1_o15, S2);
endmodule
