// Digital circuit MAIN ALU.dig as structural Verilog
module MAIN_ALU (
  input  A0,
  input  B0,
  input  A1,
  input  B1,
  input  A2,
  input  B2,
  input  A3,
  input  B3,
  input  A4,
  input  B4,
  input  A5,
  input  B5,
  input  A6,
  input  B6,
  input  A7,
  input  B7,
  input  A8,
  input  B8,
  input  A9,
  input  B9,
  input  A10,
  input  B10,
  input  A11,
  input  B11,
  input  A12,
  input  B12,
  input  A13,
  input  B13,
  input  A14,
  input  B14,
  input  A15,
  input  B15,
  input  S0,
  input  S1,
  input  S2,
  input  S3,
  input  EN,
  output C0,
  output C1,
  output C2,
  output C3,
  output C4,
  output C5,
  output C6,
  output C7,
  output C8,
  output C9,
  output C10,
  output C11,
  output C12,
  output C13,
  output C14,
  output C15,
  output COUT
);

  wire _2x1_mux_16_bit_v1_1_1_p31, _2x1_mux_16_bit_v1_1_1_p32, _2x1_mux_16_bit_v1_1_1_p33,
       _2x1_mux_16_bit_v1_1_1_p34, _2x1_mux_16_bit_v1_1_1_p35, _2x1_mux_16_bit_v1_1_1_p36,
       _2x1_mux_16_bit_v1_1_1_p37, _2x1_mux_16_bit_v1_1_1_p38, _2x1_mux_16_bit_v1_1_1_p39,
       _2x1_mux_16_bit_v1_1_1_p40, _2x1_mux_16_bit_v1_1_1_p41, _2x1_mux_16_bit_v1_1_1_p42,
       _2x1_mux_16_bit_v1_1_1_p43, _2x1_mux_16_bit_v1_1_2_p31, _2x1_mux_16_bit_v1_1_2_p32,
       _2x1_mux_16_bit_v1_1_2_p33, _2x1_mux_16_bit_v1_1_2_p34, _2x1_mux_16_bit_v1_1_2_p35,
       _2x1_mux_16_bit_v1_1_2_p36, _2x1_mux_16_bit_v1_1_2_p37, _2x1_mux_16_bit_v1_1_2_p38,
       _2x1_mux_16_bit_v1_1_2_p39, _2x1_mux_16_bit_v1_1_2_p40, _2x1_mux_16_bit_v1_1_2_p41,
       _2x1_mux_16_bit_v1_1_2_p42, _2x1_mux_16_bit_v1_1_2_p43, _2x1_mux_v1_1_1_out, _2x1_mux_v1_1_2_out,
       _2x1_mux_v1_1_3_out, _4x1_mux_16_bit_v1_1_1_o0, _4x1_mux_16_bit_v1_1_1_o1, _4x1_mux_16_bit_v1_1_1_o2,
       _4x1_mux_16_bit_v1_1_1_o3, _4x1_mux_16_bit_v1_1_1_o4, _4x1_mux_16_bit_v1_1_1_o5,
       _4x1_mux_16_bit_v1_1_1_o6, _4x1_mux_16_bit_v1_1_1_o7, _4x1_mux_16_bit_v1_1_1_o8,
       _4x1_mux_16_bit_v1_1_1_o9, _4x1_mux_16_bit_v1_1_1_o10, _4x1_mux_16_bit_v1_1_1_o11,
       _4x1_mux_16_bit_v1_1_1_o12, _4x1_mux_16_bit_v1_1_1_o13, _4x1_mux_16_bit_v1_1_1_o14,
       _4x1_mux_16_bit_v1_1_1_o15, _4x1_mux_16_bit_v1_1_2_o0, _4x1_mux_16_bit_v1_1_2_o1,
       _4x1_mux_16_bit_v1_1_2_o2, _4x1_mux_16_bit_v1_1_2_o3, _4x1_mux_16_bit_v1_1_2_o4,
       _4x1_mux_16_bit_v1_1_2_o5, _4x1_mux_16_bit_v1_1_2_o6, _4x1_mux_16_bit_v1_1_2_o7,
       _4x1_mux_16_bit_v1_1_2_o8, _4x1_mux_16_bit_v1_1_2_o9, _4x1_mux_16_bit_v1_1_2_o10,
       _4x1_mux_16_bit_v1_1_2_o11, _4x1_mux_16_bit_v1_1_2_o12, _4x1_mux_16_bit_v1_1_2_o13,
       _4x1_mux_16_bit_v1_1_2_o14, _4x1_mux_16_bit_v1_1_2_o15, _4x1_mux_v1_2_1_o, _8x1_mux_v1_2_1_out,
       _8x1_mux_v1_2_2_out, _8x1_mux_v1_2_3_out, _8x1_mux_v1_2_4_out, adder_v1_1_p31, adder_v1_1_p32,
       adder_v1_1_p33, adder_v1_1_p34, adder_v1_1_p35, adder_v1_1_p36, adder_v1_1_p37, adder_v1_1_p38,
       adder_v1_1_p39, adder_v1_1_p40, adder_v1_1_p41, adder_v1_1_p42, adder_v1_1_p43, adder_v1_1_p44,
       adder_v1_2_p16, adder_v1_2_p17, adder_v1_2_p31, adder_v1_2_p32, adder_v1_2_p33, adder_v1_2_p34,
       adder_v1_2_p35, adder_v1_2_p36, adder_v1_2_p37, adder_v1_2_p38, adder_v1_2_p39, adder_v1_2_p40,
       adder_v1_2_p41, adder_v1_2_p42, adder_v1_2_p43, adder_v1_2_p44, left_bareler_shift_1_o0,
       left_bareler_shift_1_o1, left_bareler_shift_1_o2, left_bareler_shift_1_o3, left_bareler_shift_1_o4,
       left_bareler_shift_1_o5, left_bareler_shift_1_o6, left_bareler_shift_1_o7, left_bareler_shift_1_o8,
       left_bareler_shift_1_o9, left_bareler_shift_1_o10, left_bareler_shift_1_o11, left_bareler_shift_1_o12,
       left_bareler_shift_1_o13, left_bareler_shift_1_o14, left_bareler_shift_1_o15, left_shift_1_o0,
       left_shift_1_o1, left_shift_1_o2, left_shift_1_o3, left_shift_1_o4, left_shift_1_o5, left_shift_1_o6,
       left_shift_1_o7, left_shift_1_o8, left_shift_1_o9, left_shift_1_o10, left_shift_1_o11,
       left_shift_1_o12, left_shift_1_o13, left_shift_1_o14, left_shift_1_o15, right_bareler_shift_1_o0,
       right_bareler_shift_1_o1, right_bareler_shift_1_o2, right_bareler_shift_1_o3,
       right_bareler_shift_1_o4, right_bareler_shift_1_o5, right_bareler_shift_1_o6,
       right_bareler_shift_1_o7, right_bareler_shift_1_o8, right_bareler_shift_1_o9,
       right_bareler_shift_1_o10, right_bareler_shift_1_o11, right_bareler_shift_1_o12,
       right_bareler_shift_1_o13, right_bareler_shift_1_o14, right_bareler_shift_1_o15, right_shift_1_o0,
       right_shift_1_o1, right_shift_1_o2, right_shift_1_o3, right_shift_1_o4, right_shift_1_o5,
       right_shift_1_o6, right_shift_1_o7, right_shift_1_o8, right_shift_1_o9, right_shift_1_o10,
       right_shift_1_o11, right_shift_1_o12, right_shift_1_o13, right_shift_1_o14, right_shift_1_o15,
       undriven, undriven_2, undriven_3, undriven_4, undriven_5, undriven_6, undriven_7, undriven_8,
       undriven_9, undriven_10, xor_1_out, xor_2_out, xor_3_out, xor_4_out, xor_5_out, xor_6_out, xor_7_out,
       xor_8_out, xor_9_out, xor_10_out, xor_11_out, xor_12_out, xor_13_out, xor_14_out, xor_15_out,
       xor_16_out;

  // _2X1_MUX_16_BIT_V1_1 _2x1_mux_16_bit_v1_1_1: pin names not known; wires that end beside it: A0, A1, A2, A3, A4, A5, A6, A7, A8, A9, A10, A11, A12, A13, A14, A15, B0, B1, B2, B3, B4, B5, B6, B7, B8, B9, B10, B11, B12, B13, _2x1_mux_16_bit_v1_1_1_p31, _2x1_mux_16_bit_v1_1_1_p32, _2x1_mux_16_bit_v1_1_1_p33, _2x1_mux_16_bit_v1_1_1_p34, _2x1_mux_16_bit_v1_1_1_p35, _2x1_mux_16_bit_v1_1_1_p36, _2x1_mux_16_bit_v1_1_1_p37, _2x1_mux_16_bit_v1_1_1_p38, _2x1_mux_16_bit_v1_1_1_p39, _2x1_mux_16_bit_v1_1_1_p40, _2x1_mux_16_bit_v1_1_1_p41, _2x1_mux_16_bit_v1_1_1_p42, _2x1_mux_16_bit_v1_1_1_p43
  LEFT_BARELER_SHIFT left_bareler_shift_1 (
    .I0(A0), .I1(A1), .I2(A2), .I3(A3), .I4(A4), .I5(A5), .I6(A6), .I7(A7), .I8(A8), .I9(A9), .I10(A10),
    .I11(A11), .I12(A12), .I13(A13), .I14(A14), .I15(A15), .S0(B0), .S1(B1), .S2(B2), .S3(B3), .EN(EN),
    .O0(left_bareler_shift_1_o0), .O1(left_bareler_shift_1_o1), .O2(left_bareler_shift_1_o2),
    .O3(left_bareler_shift_1_o3), .O4(left_bareler_shift_1_o4), .O5(left_bareler_shift_1_o5),
    .O6(left_bareler_shift_1_o6), .O7(left_bareler_shift_1_o7), .O8(left_bareler_shift_1_o8),
    .O9(left_bareler_shift_1_o9), .O10(left_bareler_shift_1_o10), .O11(left_bareler_shift_1_o11),
    .O12(left_bareler_shift_1_o12), .O13(left_bareler_shift_1_o13), .O14(left_bareler_shift_1_o14),
    .O15(left_bareler_shift_1_o15));
  RIGHT_BARELER_SHIFT right_bareler_shift_1 (
    .I0(A0), .I1(A1), .I2(A2), .I3(A3), .I4(A4), .I5(A5), .I6(A6), .I7(A7), .I8(A8), .I9(A9), .I10(A10),
    .I11(A11), .I12(A12), .I13(A13), .I14(A14), .I15(A15), .S0(B0), .S1(B1), .S2(B2), .S3(B3), .EN(EN),
    .O0(right_bareler_shift_1_o0), .O1(right_bareler_shift_1_o1), .O2(right_bareler_shift_1_o2),
    .O3(right_bareler_shift_1_o3), .O4(right_bareler_shift_1_o4), .O5(right_bareler_shift_1_o5),
    .O6(right_bareler_shift_1_o6), .O7(right_bareler_shift_1_o7), .O8(right_bareler_shift_1_o8),
    .O9(right_bareler_shift_1_o9), .O10(right_bareler_shift_1_o10), .O11(right_bareler_shift_1_o11),
    .O12(right_bareler_shift_1_o12), .O13(right_bareler_shift_1_o13), .O14(right_bareler_shift_1_o14),
    .O15(right_bareler_shift_1_o15));
  // _2X1_MUX_16_BIT_V1_1 _2x1_mux_16_bit_v1_1_2: pin names not known; wires that end beside it: left_bareler_shift_1_o0, left_bareler_shift_1_o1, left_bareler_shift_1_o2, left_bareler_shift_1_o3, left_bareler_shift_1_o4, left_bareler_shift_1_o5, left_bareler_shift_1_o6, left_bareler_shift_1_o7, left_bareler_shift_1_o8, left_bareler_shift_1_o9, left_bareler_shift_1_o10, left_bareler_shift_1_o11, left_bareler_shift_1_o12, left_bareler_shift_1_o13, left_bareler_shift_1_o14, left_bareler_shift_1_o15, right_bareler_shift_1_o0, right_bareler_shift_1_o1, right_bareler_shift_1_o2, right_bareler_shift_1_o3, right_bareler_shift_1_o4, right_bareler_shift_1_o5, right_bareler_shift_1_o6, right_bareler_shift_1_o7, right_bareler_shift_1_o8, right_bareler_shift_1_o9, right_bareler_shift_1_o10, right_bareler_shift_1_o11, right_bareler_shift_1_o12, right_bareler_shift_1_o13, _2x1_mux_16_bit_v1_1_2_p31, _2x1_mux_16_bit_v1_1_2_p32, _2x1_mux_16_bit_v1_1_2_p33, _2x1_mux_16_bit_v1_1_2_p34, _2x1_mux_16_bit_v1_1_2_p35, _2x1_mux_16_bit_v1_1_2_p36, _2x1_mux_16_bit_v1_1_2_p37, _2x1_mux_16_bit_v1_1_2_p38, _2x1_mux_16_bit_v1_1_2_p39, _2x1_mux_16_bit_v1_1_2_p40, _2x1_mux_16_bit_v1_1_2_p41, _2x1_mux_16_bit_v1_1_2_p42, _2x1_mux_16_bit_v1_1_2_p43
  xor xor_1 (xor_1_out, _2x1_mux_16_bit_v1_1_1_p31, S0);
  xor xor_2 (xor_2_out, _2x1_mux_16_bit_v1_1_1_p32, S0);
  xor xor_3 (xor_3_out, _2x1_mux_16_bit_v1_1_1_p33, S0);
  xor xor_4 (xor_4_out, _2x1_mux_16_bit_v1_1_1_p34, S0);
  xor xor_5 (xor_5_out, _2x1_mux_16_bit_v1_1_1_p35, S0);
  xor xor_6 (xor_6_out, _2x1_mux_16_bit_v1_1_1_p36, S0);
  xor xor_7 (xor_7_out, _2x1_mux_16_bit_v1_1_1_p37, S0);
  xor xor_8 (xor_8_out, _2x1_mux_16_bit_v1_1_1_p38, S0);
  xor xor_9 (xor_9_out, _2x1_mux_16_bit_v1_1_1_p39, S0);
  xor xor_10 (xor_10_out, _2x1_mux_16_bit_v1_1_1_p40, S0);
  xor xor_11 (xor_11_out, _2x1_mux_16_bit_v1_1_1_p41, S0);
  xor xor_12 (xor_12_out, _2x1_mux_16_bit_v1_1_1_p42, S0);
  xor xor_13 (xor_13_out, _2x1_mux_16_bit_v1_1_1_p43, S0);
  xor xor_14 (xor_14_out, undriven_8, S0);
  xor xor_15 (xor_15_out, undriven_9, S0);
  xor xor_16 (xor_16_out, undriven_10, S0);
  RIGHT_SHIFT right_shift_1 (
    .I0(A0), .I1(A1), .I2(A2), .I3(A3), .I4(A4), .I5(A5), .I6(A6), .I7(A7), .I8(A8), .I9(A9), .I10(A10),
    .I11(A11), .I12(A12), .I13(A13), .I14(A14), .I15(A15), .S0(B0), .S1(B1), .S2(B1), .S3(B3), .EN(EN),
    .LO_AR_BAR(S0), .O0(right_shift_1_o0), .O1(right_shift_1_o1), .O2(right_shift_1_o2),
    .O3(right_shift_1_o3), .O4(right_shift_1_o4), .O5(right_shift_1_o5), .O6(right_shift_1_o6),
    .O7(right_shift_1_o7), .O8(right_shift_1_o8), .O9(right_shift_1_o9), .O10(right_shift_1_o10),
    .O11(right_shift_1_o11), .O12(right_shift_1_o12), .O13(right_shift_1_o13), .O14(right_shift_1_o14),
    .O15(right_shift_1_o15));
  LEFT_SHIFT left_shift_1 (
    .I0(A0), .I1(A1), .I2(A2), .I3(A3), .I4(A4), .I5(A5), .I6(A6), .I7(A7), .I8(A8), .I9(A9), .I10(A10),
    .I11(A11), .I12(A12), .I13(A13), .I14(A14), .I15(A15), .S0(B0), .S1(B1), .S2(B2), .S3(B3), .EN(EN),
    .O0(left_shift_1_o0), .O1(left_shift_1_o1), .O2(left_shift_1_o2), .O3(left_shift_1_o3),
    .O4(left_shift_1_o4), .O5(left_shift_1_o5), .O6(left_shift_1_o6), .O7(left_shift_1_o7),
    .O8(left_shift_1_o8), .O9(left_shift_1_o9), .O10(left_shift_1_o10), .O11(left_shift_1_o11),
    .O12(left_shift_1_o12), .O13(left_shift_1_o13), .O14(left_shift_1_o14), .O15(left_shift_1_o15));
  // ADDER_V1 adder_v1_1: pin names not known; wires that end beside it: S0, xor_1_out, xor_2_out, xor_3_out, xor_4_out, xor_5_out, xor_6_out, xor_7_out, xor_8_out, xor_9_out, xor_10_out, xor_11_out, xor_12_out, xor_13_out, xor_14_out, xor_15_out, xor_16_out, 1'b0, 1'b0, 1'b0, 1'b0, 1'b0, 1'b0, 1'b0, 1'b0, 1'b0, 1'b0, 1'b0, 1'b0, 1'b0, adder_v1_1_p31, adder_v1_1_p32, adder_v1_1_p33, adder_v1_1_p34, adder_v1_1_p35, adder_v1_1_p36, adder_v1_1_p37, adder_v1_1_p38, adder_v1_1_p39, adder_v1_1_p40, adder_v1_1_p41, adder_v1_1_p42, adder_v1_1_p43, adder_v1_1_p44
  // ADDER_V1 adder_v1_2: pin names not known; wires that end beside it: 1'b0, adder_v1_1_p31, adder_v1_1_p32, adder_v1_1_p33, adder_v1_1_p34, adder_v1_1_p35, adder_v1_1_p36, adder_v1_1_p37, adder_v1_1_p38, adder_v1_1_p39, adder_v1_1_p40, adder_v1_1_p41, adder_v1_1_p42, adder_v1_1_p43, adder_v1_1_p44, adder_v1_2_p16, adder_v1_2_p17, A0, A1, A2, A3, A4, A5, A6, A7, A8, A9, A10, A11, A12, adder_v1_2_p31, adder_v1_2_p32, adder_v1_2_p33, adder_v1_2_p34, adder_v1_2_p35, adder_v1_2_p36, adder_v1_2_p37, adder_v1_2_p38, adder_v1_2_p39, adder_v1_2_p40, adder_v1_2_p41, adder_v1_2_p42, adder_v1_2_p43, adder_v1_2_p44
  _4X1_MUX_16_BIT_V1_1 _4x1_mux_16_bit_v1_1_1 (
    .O0(_4x1_mux_16_bit_v1_1_1_o0), .O1(_4x1_mux_16_bit_v1_1_1_o1), .O2(_4x1_mux_16_bit_v1_1_1_o2),
    .O3(_4x1_mux_16_bit_v1_1_1_o3), .O4(_4x1_mux_16_bit_v1_1_1_o4), .O5(_4x1_mux_16_bit_v1_1_1_o5),
    .O6(_4x1_mux_16_bit_v1_1_1_o6), .O7(_4x1_mux_16_bit_v1_1_1_o7), .O8(_4x1_mux_16_bit_v1_1_1_o8),
    .O9(_4x1_mux_16_bit_v1_1_1_o9), .O10(_4x1_mux_16_bit_v1_1_1_o10), .O11(_4x1_mux_16_bit_v1_1_1_o11),
    .O12(_4x1_mux_16_bit_v1_1_1_o12), .O13(_4x1_mux_16_bit_v1_1_1_o13), .O14(_4x1_mux_16_bit_v1_1_1_o14),
    .O15(_4x1_mux_16_bit_v1_1_1_o15), .IN0_0(adder_v1_1_p31), .IN0_1(adder_v1_1_p32), .IN0_2(adder_v1_1_p33),
    .IN0_3(adder_v1_1_p34), .IN0_4(adder_v1_1_p35), .IN0_5(adder_v1_1_p36), .IN0_6(adder_v1_1_p37),
    .IN0_7(adder_v1_1_p38), .IN0_8(adder_v1_1_p39), .IN0_9(adder_v1_1_p40), .IN0_10(adder_v1_1_p41),
    .IN0_11(adder_v1_1_p42), .IN0_12(adder_v1_1_p43), .IN0_13(adder_v1_1_p44), .IN0_14(adder_v1_2_p16),
    .IN0_15(adder_v1_2_p17), .IN1_0(adder_v1_2_p31), .IN1_1(adder_v1_2_p32), .IN1_2(adder_v1_2_p33),
    .IN1_3(adder_v1_2_p34), .IN1_4(adder_v1_2_p35), .IN1_5(adder_v1_2_p36), .IN1_6(adder_v1_2_p37),
    .IN1_7(adder_v1_2_p38), .IN1_8(adder_v1_2_p39), .IN1_9(adder_v1_2_p40), .IN1_10(adder_v1_2_p41),
    .IN1_11(adder_v1_2_p42), .IN1_12(adder_v1_2_p43), .IN1_13(adder_v1_2_p44), .IN1_14(undriven_6),
    .IN1_15(undriven_4), .IN2_0(1'b0), .IN2_1(1'b0), .IN2_2(1'b0), .IN2_3(1'b0), .IN2_4(1'b0), .IN2_5(1'b0),
    .IN2_6(1'b0), .IN2_7(1'b0), .IN2_8(1'b0), .IN2_9(1'b0), .IN2_10(1'b0), .IN2_11(1'b0), .IN2_12(1'b0),
    .IN2_13(1'b0), .IN2_14(1'b0), .IN2_15(1'b0), .IN3_0(1'b0), .IN3_1(1'b0), .IN3_2(1'b0), .IN3_3(1'b0),
    .IN3_4(1'b0), .IN3_5(1'b0), .IN3_6(1'b0), .IN3_7(1'b0), .IN3_8(1'b0), .IN3_9(1'b0), .IN3_10(1'b0),
    .IN3_11(1'b0), .IN3_12(1'b0), .IN3_13(1'b0), .IN3_14(1'b0), .IN3_15(1'b0), .S0(S1), .S1(S2), .EN(EN));
  _4X1_MUX_16_BIT_V1_1 _4x1_mux_16_bit_v1_1_2 (
    .O0(_4x1_mux_16_bit_v1_1_2_o0), .O1(_4x1_mux_16_bit_v1_1_2_o1), .O2(_4x1_mux_16_bit_v1_1_2_o2),
    .O3(_4x1_mux_16_bit_v1_1_2_o3), .O4(_4x1_mux_16_bit_v1_1_2_o4), .O5(_4x1_mux_16_bit_v1_1_2_o5),
    .O6(_4x1_mux_16_bit_v1_1_2_o6), .O7(_4x1_mux_16_bit_v1_1_2_o7), .O8(_4x1_mux_16_bit_v1_1_2_o8),
    .O9(_4x1_mux_16_bit_v1_1_2_o9), .O10(_4x1_mux_16_bit_v1_1_2_o10), .O11(_4x1_mux_16_bit_v1_1_2_o11),
    .O12(_4x1_mux_16_bit_v1_1_2_o12), .O13(_4x1_mux_16_bit_v1_1_2_o13), .O14(_4x1_mux_16_bit_v1_1_2_o14),
    .O15(_4x1_mux_16_bit_v1_1_2_o15), .IN0_0(1'b0), .IN0_1(1'b0), .IN0_2(1'b0), .IN0_3(1'b0), .IN0_4(1'b0),
    .IN0_5(1'b0), .IN0_6(1'b0), .IN0_7(1'b0), .IN0_8(1'b0), .IN0_9(1'b0), .IN0_10(1'b0), .IN0_11(1'b0),
    .IN0_12(1'b0), .IN0_13(1'b0), .IN0_14(1'b0), .IN0_15(1'b0), .IN1_0(_2x1_mux_16_bit_v1_1_2_p31),
    .IN1_1(_2x1_mux_16_bit_v1_1_2_p32), .IN1_2(_2x1_mux_16_bit_v1_1_2_p33),
    .IN1_3(_2x1_mux_16_bit_v1_1_2_p34), .IN1_4(_2x1_mux_16_bit_v1_1_2_p35),
    .IN1_5(_2x1_mux_16_bit_v1_1_2_p36), .IN1_6(_2x1_mux_16_bit_v1_1_2_p37),
    .IN1_7(_2x1_mux_16_bit_v1_1_2_p38), .IN1_8(_2x1_mux_16_bit_v1_1_2_p39),
    .IN1_9(_2x1_mux_16_bit_v1_1_2_p40), .IN1_10(_2x1_mux_16_bit_v1_1_2_p41),
    .IN1_11(_2x1_mux_16_bit_v1_1_2_p42), .IN1_12(_2x1_mux_16_bit_v1_1_2_p43), .IN1_13(undriven_2),
    .IN1_14(undriven_3), .IN1_15(undriven_5), .IN2_0(left_shift_1_o0), .IN2_1(left_shift_1_o1),
    .IN2_2(left_shift_1_o2), .IN2_3(left_shift_1_o3), .IN2_4(left_shift_1_o4), .IN2_5(left_shift_1_o5),
    .IN2_6(left_shift_1_o6), .IN2_7(left_shift_1_o7), .IN2_8(left_shift_1_o8), .IN2_9(left_shift_1_o9),
    .IN2_10(left_shift_1_o10), .IN2_11(left_shift_1_o11), .IN2_12(left_shift_1_o12),
    .IN2_13(left_shift_1_o13), .IN2_14(left_shift_1_o14), .IN2_15(left_shift_1_o15),
    .IN3_0(right_shift_1_o0), .IN3_1(right_shift_1_o1), .IN3_2(right_shift_1_o2), .IN3_3(right_shift_1_o3),
    .IN3_4(right_shift_1_o4), .IN3_5(right_shift_1_o5), .IN3_6(right_shift_1_o6), .IN3_7(right_shift_1_o7),
    .IN3_8(right_shift_1_o8), .IN3_9(right_shift_1_o9), .IN3_10(right_shift_1_o10),
    .IN3_11(right_shift_1_o11), .IN3_12(right_shift_1_o12), .IN3_13(right_shift_1_o13),
    .IN3_14(right_shift_1_o14), .IN3_15(right_shift_1_o15), .S0(S1), .S1(S2), .EN(EN));
  _8X1_MUX_V1_2 _8x1_mux_v1_2_1 (
    .I0(1'b0), .I1(A15), .I2(A14), .I3(A13), .I4(A12), .I5(A11), .I6(A10), .I7(A9), .S0(B0), .S1(B1),
    .S2(B2), .OUT(_8x1_mux_v1_2_1_out));
  _8X1_MUX_V1_2 _8x1_mux_v1_2_2 (
    .I0(A8), .I1(A7), .I2(A6), .I3(A5), .I4(A4), .I5(A3), .I6(A2), .I7(A1), .S0(B0), .S1(B1), .S2(B2),
    .OUT(_8x1_mux_v1_2_2_out));
  _8X1_MUX_V1_2 _8x1_mux_v1_2_3 (
    .I0(1'b0), .I1(A0), .I2(A1), .I3(A2), .I4(A3), .I5(A4), .I6(A5), .I7(A6), .S0(B0), .S1(B1), .S2(B2),
    .OUT(_8x1_mux_v1_2_3_out));
  _8X1_MUX_V1_2 _8x1_mux_v1_2_4 (
    .I0(A7), .I1(A8), .I2(A9), .I3(A10), .I4(A11), .I5(A12), .I6(A13), .I7(A14), .S0(B0), .S1(B1), .S2(B2),
    .OUT(_8x1_mux_v1_2_4_out));
  _4X1_MUX_V1_2 _4x1_mux_v1_2_1 (
    .I0(_8x1_mux_v1_2_1_out), .I1(_8x1_mux_v1_2_2_out), .I2(_8x1_mux_v1_2_3_out), .I3(_8x1_mux_v1_2_4_out),
    .S0(B3), .S1(S1), .O(_4x1_mux_v1_2_1_o));
  // _2X1_MUX_16_BIT_V1_1 _2x1_mux_16_bit_v1_1_3: pin names not known; wires that end beside it: _4x1_mux_16_bit_v1_1_1_o0, _4x1_mux_16_bit_v1_1_1_o1, _4x1_mux_16_bit_v1_1_1_o2, _4x1_mux_16_bit_v1_1_1_o3, _4x1_mux_16_bit_v1_1_1_o4, _4x1_mux_16_bit_v1_1_1_o5, _4x1_mux_16_bit_v1_1_1_o6, _4x1_mux_16_bit_v1_1_1_o7, _4x1_mux_16_bit_v1_1_1_o8, _4x1_mux_16_bit_v1_1_1_o9, _4x1_mux_16_bit_v1_1_1_o10, _4x1_mux_16_bit_v1_1_1_o11, _4x1_mux_16_bit_v1_1_1_o12, _4x1_mux_16_bit_v1_1_1_o13, _4x1_mux_16_bit_v1_1_1_o14, _4x1_mux_16_bit_v1_1_1_o15, _4x1_mux_16_bit_v1_1_2_o0, _4x1_mux_16_bit_v1_1_2_o1, _4x1_mux_16_bit_v1_1_2_o2, _4x1_mux_16_bit_v1_1_2_o3, _4x1_mux_16_bit_v1_1_2_o4, _4x1_mux_16_bit_v1_1_2_o5, _4x1_mux_16_bit_v1_1_2_o6, _4x1_mux_16_bit_v1_1_2_o7, _4x1_mux_16_bit_v1_1_2_o8, _4x1_mux_16_bit_v1_1_2_o9, _4x1_mux_16_bit_v1_1_2_o10, _4x1_mux_16_bit_v1_1_2_o11, _4x1_mux_16_bit_v1_1_2_o12, _4x1_mux_16_bit_v1_1_2_o13, C0, C1, C2, C3, C4, C5, C6, C7, C8, C9, C10, C11, C12
  _2X1_MUX_V1_1 _2x1_mux_v1_1_1 (.I0(_2x1_mux_16_bit_v1_1_2_p31), .I1(undriven_5), .S0(S0), .OUT(_2x1_mux_v1_1_1_out));
  _2X1_MUX_V1_1 _2x1_mux_v1_1_2 (.I0(undriven), .I1(undriven_7), .S0(S1), .OUT(_2x1_mux_v1_1_2_out));
  _2X1_MUX_V1_1 _2x1_mux_v1_1_3 (.I0(_2x1_mux_v1_1_1_out), .I1(_4x1_mux_v1_2_1_o), .S0(S2), .OUT(_2x1_mux_v1_1_3_out));
  _2X1_MUX_V1_1 _2x1_mux_v1_1_4 (.I0(_2x1_mux_v1_1_2_out), .I1(_2x1_mux_v1_1_3_out), .S0(S3), .OUT(COUT));
endmodule
