// Digital circuit 1 BIT ADDER V1.1.dig as structural Verilog
module _1_BIT_ADDER_V1_1 (
  input  A,
  input  B,
  input  C,
  output S,
  output CO
);

  wire and_1_out, and_2_out, undriven, xor_1_out;

  xor xor_1 (xor_1_out, A, B);
  and and_1 (and_1_out, C, A);
  and and_2 (and_2_out, B, A);
  // And and_3 has open pins: In_1=C, In_2=open, out=open
  xor xor_2 (S, xor_1_out, C);
  or or_1 (CO, and_1_out, and_2_out, undriven);
endmodule

/* Test case TEST 1:
A B C S CO
0 0 0 0 0
0 0 1 1 0
0 1 0 1 0
0 1 1 0 1
1 0 0 1 0
1 0 1 0 1
1 1 0 0 1
1 1 1 1 1
*/
