// Digital circuit 1 BIT ADDER V1.2.dig as structural Verilog
module _1_BIT_ADDER_V1_2 (
  input  A,
  input  B,
  input  C,
  output S,
  output CO
);

  wire and_1_out, and_2_out, and_3_out, xor_1_out;

  xor xor_1 (xor_1_out, A, B);
  and and_1 (and_1_out, C, A);
  and and_2 (and_2_out, B, A);
  and and_3 (and_3_out, B, C);
  xor xor_2 (S, xor_1_out, C);
  or or_1 (CO, and_1_out, and_2_out, and_3_out);
endmodule
