// Digital circuit ADDER_V1.2.dig as structural Verilog
module ADDER_V1_2 (
  input  A9,
  input  A1,
  input  A2,
  input  A3,
  input  A4,
  input  A5,
  input  A6,
  input  A7,
  input  A8,
  input  A10,
  input  A11,
  input  A12,
  input  A13,
  input  A14,
  input  A15,
  input  A0,
  input  A25,
  input  A17,
  input  A18,
  input  A19,
  input  A20,
  input  A21,
  input  A22,
  input  A23,
  input  A24,
  input  A26,
  input  A27,
  input  A28,
  input  A29,
  input  A30,
  input  A31,
  input  A16,
  input  CIN,
  output S0,
  output S1,
  output S2,
  output S3,
  output S4,
  output S5,
  output S6,
  output S7,
  output S8,
  output S9,
  output S10,
  output S11,
  output S12,
  output S13,
  output S14,
  output S15,
  output COUT
);

  wire _1_bit_adder_v1_2_1_co, _1_bit_adder_v1_2_2_co, _1_bit_adder_v1_2_3_co, _1_bit_adder_v1_2_4_co,
       _1_bit_adder_v1_2_5_co, _1_bit_adder_v1_2_6_co, _1_bit_adder_v1_2_7_co, _1_bit_adder_v1_2_8_co,
       _1_bit_adder_v1_2_9_co, _1_bit_adder_v1_2_10_co, _1_bit_adder_v1_2_11_co, _1_bit_adder_v1_2_12_co,
       _1_bit_adder_v1_2_13_co, _1_bit_adder_v1_2_14_co, _1_bit_adder_v1_2_15_co;

  _1_BIT_ADDER_V1_2 _1_bit_adder_v1_2_1 (.A(CIN), .B(A0), .C(A16), .S(S0), .CO(_1_bit_adder_v1_2_1_co));
  _1_BIT_ADDER_V1_2 _1_bit_adder_v1_2_2 (
    .A(_1_bit_adder_v1_2_1_co), .B(A1), .C(A17), .S(S1), .CO(_1_bit_adder_v1_2_2_co));
  _1_BIT_ADDER_V1_2 _1_bit_adder_v1_2_3 (
    .A(_1_bit_adder_v1_2_2_co), .B(A2), .C(A18), .S(S2), .CO(_1_bit_adder_v1_2_3_co));
  _1_BIT_ADDER_V1_2 _1_bit_adder_v1_2_4 (
    .A(_1_bit_adder_v1_2_3_co), .B(A3), .C(A19), .S(S3), .CO(_1_bit_adder_v1_2_4_co));
  _1_BIT_ADDER_V1_2 _1_bit_adder_v1_2_5 (
    .A(_1_bit_adder_v1_2_4_co), .B(A4), .C(A20), .S(S4), .CO(_1_bit_adder_v1_2_5_co));
  _1_BIT_ADDER_V1_2 _1_bit_adder_v1_2_6 (
    .A(_1_bit_adder_v1_2_5_co), .B(A5), .C(A21), .S(S5), .CO(_1_bit_adder_v1_2_6_co));
  _1_BIT_ADDER_V1_2 _1_bit_adder_v1_2_7 (
    .A(_1_bit_adder_v1_2_6_co), .B(A6), .C(A22), .S(S6), .CO(_1_bit_adder_v1_2_7_co));
  _1_BIT_ADDER_V1_2 _1_bit_adder_v1_2_8 (
    .A(_1_bit_adder_v1_2_7_co), .B(A7), .C(A23), .S(S7), .CO(_1_bit_adder_v1_2_8_co));
  _1_BIT_ADDER_V1_2 _1_bit_adder_v1_2_9 (
    .A(_1_bit_adder_v1_2_8_co), .B(A8), .C(A24), .S(S8), .CO(_1_bit_adder_v1_2_9_co));
  _1_BIT_ADDER_V1_2 _1_bit_adder_v1_2_10 (
    .A(_1_bit_adder_v1_2_9_co), .B(A9), .C(A25), .S(S9), .CO(_1_bit_adder_v1_2_10_co));
  _1_BIT_ADDER_V1_2 _1_bit_adder_v1_2_11 (
    .A(_1_bit_adder_v1_2_10_co), .B(A10), .C(A26), .S(S10), .CO(_1_bit_adder_v1_2_11_co));
  _1_BIT_ADDER_V1_2 _1_bit_adder_v1_2_12 (
    .A(_1_bit_adder_v1_2_11_co), .B(A11), .C(A27), .S(S11), .CO(_1_bit_adder_v1_2_12_co));
  _1_BIT_ADDER_V1_2 _1_bit_adder_v1_2_13 (
    .A(_1_bit_adder_v1_2_12_co), .B(A12), .C(A28), .S(S12), .CO(_1_bit_adder_v1_2_13_co));
  _1_BIT_ADDER_V1_2 _1_bit_adder_v1_2_14 (
    .A(_1_bit_adder_v1_2_13_co), .B(A13), .C(A29), .S(S13), .CO(_1_bit_adder_v1_2_14_co));
  _1_BIT_ADDER_V1_2 _1_bit_adder_v1_2_15 (
    .A(_1_bit_adder_v1_2_14_co), .B(A14), .C(A30), .S(S14), .CO(_1_bit_adder_v1_2_15_co));
  _1_BIT_ADDER_V1_2 _1_bit_adder_v1_2_16 (.A(_1_bit_adder_v1_2_15_co), .B(A15), .C(A31), .S(S15), .CO(COUT));
endmodule
