// Digital circuit RIGHT SHIFT.dig as structural Verilog
module RIGHT_SHIFT (
  input  I0,
  input  I1,
  input  I2,
  input  I3,
  input  I4,
  input  I5,
  input  I6,
  input  I7,
  input  I8,
  input  I9,
  input  I10,
  input  I11,
  input  I12,
  input  I13,
  input  I14,
  input  I15,
  input  S0,
  input  S1,
  input  S2,
  input  S3,
  input  EN,
  input  LO_AR_BAR,
  output O0,
  output O1,
  output O2,
  output O3,
  output O4,
  output O5,
  output O6,
  output O7,
  output O8,
  output O9,
  output O10,
  output O11,
  output O12,
  output O13,
  output O14,
  output O15
);

  wire _2x1_mux_16_bit_v1_1_1_p31, _2x1_mux_16_bit_v1_1_1_p32, _2x1_mux_16_bit_v1_1_1_p33,
       _2x1_mux_16_bit_v1_1_1_p34, _2x1_mux_16_bit_v1_1_1_p35, _2x1_mux_16_bit_v1_1_1_p36,
       _2x1_mux_16_bit_v1_1_1_p37, _2x1_mux_16_bit_v1_1_1_p38, _2x1_mux_16_bit_v1_1_1_p39,
       _2x1_mux_16_bit_v1_1_1_p40, _2x1_mux_16_bit_v1_1_1_p41, _2x1_mux_16_bit_v1_1_1_p42,
       _2x1_mux_16_bit_v1_1_1_p43, _2x1_mux_16_bit_v1_1_2_p14, _2x1_mux_16_bit_v1_1_2_p15,
       _2x1_mux_16_bit_v1_1_2_p16, _2x1_mux_16_bit_v1_1_2_p31, _2x1_mux_16_bit_v1_1_2_p32,
       _2x1_mux_16_bit_v1_1_2_p33, _2x1_mux_16_bit_v1_1_2_p34, _2x1_mux_16_bit_v1_1_2_p35,
       _2x1_mux_16_bit_v1_1_2_p36, _2x1_mux_16_bit_v1_1_2_p37, _2x1_mux_16_bit_v1_1_2_p38,
       _2x1_mux_16_bit_v1_1_2_p39, _2x1_mux_16_bit_v1_1_2_p40, _2x1_mux_16_bit_v1_1_2_p41,
       _2x1_mux_16_bit_v1_1_2_p42, _2x1_mux_16_bit_v1_1_2_p43, _2x1_mux_16_bit_v1_1_3_p14,
       _2x1_mux_16_bit_v1_1_3_p15, _2x1_mux_16_bit_v1_1_3_p16, _2x1_mux_16_bit_v1_1_3_p31,
       _2x1_mux_16_bit_v1_1_3_p32, _2x1_mux_16_bit_v1_1_3_p33, _2x1_mux_16_bit_v1_1_3_p34,
       _2x1_mux_16_bit_v1_1_3_p35, _2x1_mux_16_bit_v1_1_3_p36, _2x1_mux_16_bit_v1_1_3_p37,
       _2x1_mux_16_bit_v1_1_3_p38, _2x1_mux_16_bit_v1_1_3_p39, _2x1_mux_16_bit_v1_1_3_p40,
       _2x1_mux_16_bit_v1_1_3_p41, _2x1_mux_16_bit_v1_1_3_p42, _2x1_mux_16_bit_v1_1_3_p43,
       _2x1_mux_16_bit_v1_1_4_p14, _2x1_mux_16_bit_v1_1_4_p15, _2x1_mux_16_bit_v1_1_4_p16,
       _2x1_mux_v1_1_1_out;

  _2X1_MUX_V1_1 _2x1_mux_v1_1_1 (.I0(I15), .I1(1'b0), .S0(LO_AR_BAR), .OUT(_2x1_mux_v1_1_1_out));
  // _2X1_MUX_16_BIT_V1_1 _2x1_mux_16_bit_v1_1_1: pin names not known; wires that end beside it: I0, I1, I2, I3, I4, I5, I6, I7, I8, I9, I10, I11, I12, I13, I14, I15, I1, I2, I3, I4, I5, I6, I7, I8, I9, I10, I11, I12, I13, I14, _2x1_mux_16_bit_v1_1_1_p31, _2x1_mux_16_bit_v1_1_1_p32, _2x1_mux_16_bit_v1_1_1_p33, _2x1_mux_16_bit_v1_1_1_p34, _2x1_mux_16_bit_v1_1_1_p35, _2x1_mux_16_bit_v1_1_1_p36, _2x1_mux_16_bit_v1_1_1_p37, _2x1_mux_16_bit_v1_1_1_p38, _2x1_mux_16_bit_v1_1_1_p39, _2x1_mux_16_bit_v1_1_1_p40, _2x1_mux_16_bit_v1_1_1_p41, _2x1_mux_16_bit_v1_1_1_p42, _2x1_mux_16_bit_v1_1_1_p43
  // _2X1_MUX_16_BIT_V1_1 _2x1_mux_16_bit_v1_1_2: pin names not known; wires that end beside it: _2x1_mux_16_bit_v1_1_1_p31, _2x1_mux_16_bit_v1_1_1_p32, _2x1_mux_16_bit_v1_1_1_p33, _2x1_mux_16_bit_v1_1_1_p34, _2x1_mux_16_bit_v1_1_1_p35, _2x1_mux_16_bit_v1_1_1_p36, _2x1_mux_16_bit_v1_1_1_p37, _2x1_mux_16_bit_v1_1_1_p38, _2x1_mux_16_bit_v1_1_1_p39, _2x1_mux_16_bit_v1_1_1_p40, _2x1_mux_16_bit_v1_1_1_p41, _2x1_mux_16_bit_v1_1_1_p42, _2x1_mux_16_bit_v1_1_1_p43, _2x1_mux_16_bit_v1_1_2_p14, _2x1_mux_16_bit_v1_1_2_p15, _2x1_mux_16_bit_v1_1_2_p16, _2x1_mux_16_bit_v1_1_1_p33, _2x1_mux_16_bit_v1_1_1_p34, _2x1_mux_16_bit_v1_1_1_p35, _2x1_mux_16_bit_v1_1_1_p36, _2x1_mux_16_bit_v1_1_1_p37, _2x1_mux_16_bit_v1_1_1_p38, _2x1_mux_16_bit_v1_1_1_p39, _2x1_mux_16_bit_v1_1_1_p40, _2x1_mux_16_bit_v1_1_1_p41, _2x1_mux_16_bit_v1_1_1_p42, _2x1_mux_16_bit_v1_1_1_p43, _2x1_mux_16_bit_v1_1_2_p14, _2x1_mux_16_bit_v1_1_2_p15, _2x1_mux_16_bit_v1_1_2_p16, _2x1_mux_16_bit_v1_1_2_p31, _2x1_mux_16_bit_v1_1_2_p32, _2x1_mux_16_bit_v1_1_2_p33, _2x1_mux_16_bit_v1_1_2_p34, _2x1_mux_16_bit_v1_1_2_p35, _2x1_mux_16_bit_v1_1_2_p36, _2x1_mux_16_bit_v1_1_2_p37, _2x1_mux_16_bit_v1_1_2_p38, _2x1_mux_16_bit_v1_1_2_p39, _2x1_mux_16_bit_v1_1_2_p40, _2x1_mux_16_bit_v1_1_2_p41, _2x1_mux_16_bit_v1_1_2_p42, _2x1_mux_16_bit_v1_1_2_p43
  // _2X1_MUX_16_BIT_V1_1 _2x1_mux_16_bit_v1_1_3: pin names not known; wires that end beside it: _2x1_mux_16_bit_v1_1_2_p31, _2x1_mux_16_bit_v1_1_2_p32, _2x1_mux_16_bit_v1_1_2_p33, _2x1_mux_16_bit_v1_1_2_p34, _2x1_mux_16_bit_v1_1_2_p35, _2x1_mux_16_bit_v1_1_2_p36, _2x1_mux_16_bit_v1_1_2_p37, _2x1_mux_16_bit_v1_1_2_p38, _2x1_mux_16_bit_v1_1_2_p39, _2x1_mux_16_bit_v1_1_2_p40, _2x1_mux_16_bit_v1_1_2_p41, _2x1_mux_16_bit_v1_1_2_p42, _2x1_mux_16_bit_v1_1_2_p43, _2x1_mux_16_bit_v1_1_3_p14, _2x1_mux_16_bit_v1_1_3_p15, _2x1_mux_16_bit_v1_1_3_p16, _2x1_mux_16_bit_v1_1_2_p35, _2x1_mux_16_bit_v1_1_2_p36, _2x1_mux_16_bit_v1_1_2_p37, _2x1_mux_16_bit_v1_1_2_p38, _2x1_mux_16_bit_v1_1_2_p39, _2x1_mux_16_bit_v1_1_2_p40, _2x1_mux_16_bit_v1_1_2_p41, _2x1_mux_16_bit_v1_1_2_p42, _2x1_mux_16_bit_v1_1_2_p43, _2x1_mux_16_bit_v1_1_3_p14, _2x1_mux_16_bit_v1_1_3_p15, _2x1_mux_16_bit_v1_1_3_p16, _2x1_mux_v1_1_1_out, _2x1_mux_v1_1_1_out, _2x1_mux_16_bit_v1_1_3_p31, _2x1_mux_16_bit_v1_1_3_p32, _2x1_mux_16_bit_v1_1_3_p33, _2x1_mux_16_bit_v1_1_3_p34, _2x1_mux_16_bit_v1_1_3_p35, _2x1_mux_16_bit_v1_1_3_p36, _2x1_mux_16_bit_v1_1_3_p37, _2x1_mux_16_bit_v1_1_3_p38, _2x1_mux_16_bit_v1_1_3_p39, _2x1_mux_16_bit_v1_1_3_p40, _2x1_mux_16_bit_v1_1_3_p41, _2x1_mux_16_bit_v1_1_3_p42, _2x1_mux_16_bit_v1_1_3_p43
  // _2X1_MUX_16_BIT_V1_1 _2x1_mux_16_bit_v1_1_4: pin names not known; wires that end beside it: _2x1_mux_16_bit_v1_1_3_p31, _2x1_mux_16_bit_v1_1_3_p32, _2x1_mux_16_bit_v1_1_3_p33, _2x1_mux_16_bit_v1_1_3_p34, _2x1_mux_16_bit_v1_1_3_p35, _2x1_mux_16_bit_v1_1_3_p36, _2x1_mux_16_bit_v1_1_3_p37, _2x1_mux_16_bit_v1_1_3_p38, _2x1_mux_16_bit_v1_1_3_p39, _2x1_mux_16_bit_v1_1_3_p40, _2x1_mux_16_bit_v1_1_3_p41, _2x1_mux_16_bit_v1_1_3_p42, _2x1_mux_16_bit_v1_1_3_p43, _2x1_mux_16_bit_v1_1_4_p14, _2x1_mux_16_bit_v1_1_4_p15, _2x1_mux_16_bit_v1_1_4_p16, _2x1_mux_16_bit_v1_1_3_p39, _2x1_mux_16_bit_v1_1_3_p40, _2x1_mux_16_bit_v1_1_3_p41, _2x1_mux_16_bit_v1_1_3_p42, _2x1_mux_16_bit_v1_1_3_p43, _2x1_mux_16_bit_v1_1_4_p14, _2x1_mux_16_bit_v1_1_4_p15, _2x1_mux_16_bit_v1_1_4_p16, _2x1_mux_v1_1_1_out, _2x1_mux_v1_1_1_out, _2x1_mux_v1_1_1_out, _2x1_mux_v1_1_1_out, _2x1_mux_v1_1_1_out, _2x1_mux_v1_1_1_out, O0, O1, O2, O3, O4, O5, O6, O7, O8, O9, O10, O11, O12
endmodule
