// Digital circuit 2X1 MUX V1.1.dig as structural Verilog
module _2X1_MUX_V1_1 (
  input  I0,
  input  I1,
  input  S0,
  output OUT
);

  wire and_1_out, and_2_out, not_1_out;

  not not_1 (not_1_out, S0);
  and and_1 (and_1_out, I0, not_1_out);
  and and_2 (and_2_out, I1, S0);
  or or_1 (OUT, and_1_out, and_2_out);
endmodule
