// Digital circuit 4X1 MUX 16 BIT V1.1.dig as structural Verilog
module _4X1_MUX_16_BIT_V1_1 (
  input  S0,
  input  S1,
  input  IN2_0,
  input  IN3_0,
  input  IN0_0,
  input  IN1_0,
  input  IN0_1,
  input  IN0_2,
  input  IN0_3,
  input  IN0_4,
  input  IN0_5,
  input  IN0_6,
  input  IN0_7,
  input  IN0_8,
  input  IN0_9,
  input  IN0_10,
  input  IN0_11,
  input  IN0_12,
  input  IN0_13,
  input  IN0_14,
  input  IN0_15,
  input  IN1_1,
  input  IN1_2,
  input  IN1_3,
  input  IN1_4,
  input  IN1_5,
  input  IN1_6,
  input  IN1_7,
  input  IN1_8,
  input  IN1_9,
  input  IN1_10,
  input  IN1_11,
  input  IN1_12,
  input  IN1_13,
  input  IN1_14,
  input  IN1_15,
  input  IN2_1,
  input  IN2_2,
  input  IN2_3,
  input  IN2_4,
  input  IN2_5,
  input  IN2_6,
  input  IN2_7,
  input  IN2_8,
  input  IN2_9,
  input  IN2_10,
  input  IN2_11,
  input  IN2_12,
  input  IN2_13,
  input  IN2_14,
  input  IN2_15,
  input  IN3_1,
  input  IN3_2,
  input  IN3_3,
  input  IN3_4,
  input  IN3_5,
  input  IN3_6,
  input  IN3_7,
  input  IN3_8,
  input  IN3_9,
  input  IN3_10,
  input  IN3_11,
  input  IN3_12,
  input  IN3_13,
  input  IN3_14,
  input  IN3_15,
  input  EN,
  output O0,
  output O1,
  output O2,
  output O3,
  output O4,
  output O5,
  output O6,
  output O7,
  output O8,
  output O9,
  output O10,
  output O11,
  output O12,
  output O13,
  output O14,
  output O15
);

  wire _2x1_mux_16_bit_v1_1_1_p26, _2x1_mux_16_bit_v1_1_1_p27, _2x1_mux_16_bit_v1_1_1_p28,
       _2x1_mux_16_bit_v1_1_1_p29, _2x1_mux_16_bit_v1_1_1_p30, _2x1_mux_16_bit_v1_1_1_p31,
       _2x1_mux_16_bit_v1_1_1_p32, _2x1_mux_16_bit_v1_1_1_p33, _2x1_mux_16_bit_v1_1_1_p34,
       _2x1_mux_16_bit_v1_1_1_p35, _2x1_mux_16_bit_v1_1_1_p36, _2x1_mux_16_bit_v1_1_1_p37,
       _2x1_mux_16_bit_v1_1_2_p40, _2x1_mux_16_bit_v1_1_2_p41, _2x1_mux_16_bit_v1_1_2_p42,
       _2x1_mux_16_bit_v1_1_2_p43, _2x1_mux_16_bit_v1_1_2_p44, _2x1_mux_16_bit_v1_1_2_p45,
       _2x1_mux_16_bit_v1_1_2_p46, _2x1_mux_16_bit_v1_1_2_p47, _2x1_mux_16_bit_v1_1_2_p48,
       _2x1_mux_16_bit_v1_1_2_p49, _2x1_mux_16_bit_v1_1_2_p50, _2x1_mux_16_bit_v1_1_2_p51,
       _2x1_mux_16_bit_v1_1_2_p52, _2x1_mux_16_bit_v1_1_2_p53, _2x1_mux_16_bit_v1_1_2_p54,
       _2x1_mux_16_bit_v1_1_2_p55, _2x1_mux_16_bit_v1_1_2_p56, _2x1_mux_16_bit_v1_1_3_p30;

  // _2X1_MUX_16_BIT_V1_1 _2x1_mux_16_bit_v1_1_1: pin names not known; wires that end beside it: IN0_0, IN0_1, IN0_2, IN0_3, IN0_4, IN0_5, IN0_6, IN0_7, IN0_8, IN0_9, IN0_10, IN0_11, IN0_12, IN0_13, IN0_14, IN0_15, IN1_0, IN1_1, IN1_2, IN1_3, IN1_4, IN1_5, IN1_6, IN1_7, IN1_8, _2x1_mux_16_bit_v1_1_1_p26, _2x1_mux_16_bit_v1_1_1_p27, _2x1_mux_16_bit_v1_1_1_p28, _2x1_mux_16_bit_v1_1_1_p29, _2x1_mux_16_bit_v1_1_1_p30, _2x1_mux_16_bit_v1_1_1_p31, _2x1_mux_16_bit_v1_1_1_p32, _2x1_mux_16_bit_v1_1_1_p33, _2x1_mux_16_bit_v1_1_1_p34, _2x1_mux_16_bit_v1_1_1_p35, _2x1_mux_16_bit_v1_1_1_p36, _2x1_mux_16_bit_v1_1_1_p37
  // _2X1_MUX_16_BIT_V1_1 _2x1_mux_16_bit_v1_1_2: pin names not known; wires that end beside it: IN1_9, IN1_10, IN1_11, IN1_12, IN1_13, IN1_14, IN1_15, S0, EN, IN2_0, IN2_1, IN2_2, IN2_3, IN2_4, IN2_5, IN2_6, IN2_7, IN2_8, IN2_9, IN2_10, IN2_11, IN2_12, IN2_13, IN2_14, IN2_15, IN3_0, IN3_1, IN3_2, IN3_3, IN3_4, IN3_5, IN3_6, IN3_7, IN3_8, IN3_9, IN3_10, IN3_11, IN3_12, IN3_13, _2x1_mux_16_bit_v1_1_2_p40, _2x1_mux_16_bit_v1_1_2_p41, _2x1_mux_16_bit_v1_1_2_p42, _2x1_mux_16_bit_v1_1_2_p43, _2x1_mux_16_bit_v1_1_2_p44, _2x1_mux_16_bit_v1_1_2_p45, _2x1_mux_16_bit_v1_1_2_p46, _2x1_mux_16_bit_v1_1_2_p47, _2x1_mux_16_bit_v1_1_2_p48, _2x1_mux_16_bit_v1_1_2_p49, _2x1_mux_16_bit_v1_1_2_p50, _2x1_mux_16_bit_v1_1_2_p51, _2x1_mux_16_bit_v1_1_2_p52, _2x1_mux_16_bit_v1_1_2_p53, _2x1_mux_16_bit_v1_1_2_p54, _2x1_mux_16_bit_v1_1_2_p55, _2x1_mux_16_bit_v1_1_2_p56
  // _2X1_MUX_16_BIT_V1_1 _2x1_mux_16_bit_v1_1_3: pin names not known; wires that end beside it: _2x1_mux_16_bit_v1_1_1_p26, _2x1_mux_16_bit_v1_1_1_p27, _2x1_mux_16_bit_v1_1_1_p28, _2x1_mux_16_bit_v1_1_1_p29, _2x1_mux_16_bit_v1_1_1_p30, _2x1_mux_16_bit_v1_1_1_p31, _2x1_mux_16_bit_v1_1_1_p32, _2x1_mux_16_bit_v1_1_1_p33, _2x1_mux_16_bit_v1_1_1_p34, _2x1_mux_16_bit_v1_1_1_p35, _2x1_mux_16_bit_v1_1_1_p36, _2x1_mux_16_bit_v1_1_1_p37, _2x1_mux_16_bit_v1_1_2_p40, _2x1_mux_16_bit_v1_1_2_p41, _2x1_mux_16_bit_v1_1_2_p42, _2x1_mux_16_bit_v1_1_2_p43, _2x1_mux_16_bit_v1_1_2_p44, _2x1_mux_16_bit_v1_1_2_p45, _2x1_mux_16_bit_v1_1_2_p46, _2x1_mux_16_bit_v1_1_2_p47, _2x1_mux_16_bit_v1_1_2_p48, _2x1_mux_16_bit_v1_1_2_p49, _2x1_mux_16_bit_v1_1_2_p50, _2x1_mux_16_bit_v1_1_2_p51, _2x1_mux_16_bit_v1_1_2_p52, _2x1_mux_16_bit_v1_1_2_p53, _2x1_mux_16_bit_v1_1_2_p54, _2x1_mux_16_bit_v1_1_2_p55, _2x1_mux_16_bit_v1_1_2_p56, _2x1_mux_16_bit_v1_1_3_p30, O0, O1, O2, O3, O4, O5, O6, O7, O8, O9, O10, O11, O12
endmodule
