// Digital circuit 4X1 MUX V1.2.dig as structural Verilog
module _4X1_MUX_V1_2 (
  input  I0,
  input  I1,
  input  I2,
  input  I3,
  input  S0,
  input  S1,
  output O
);

  wire _2x1_mux_v1_1_1_out, _2x1_mux_v1_1_2_out;

  _2X1_MUX_V1_1 _2x1_mux_v1_1_1 (.I0(I0), .I1(I1), .S0(S0), .OUT(_2x1_mux_v1_1_1_out));
  _2X1_MUX_V1_1 _2x1_mux_v1_1_2 (.I0(I2), .I1(I3), .S0(S0), .OUT(_2x1_mux_v1_1_2_out));
  _2X1_MUX_V1_1 _2x1_mux_v1_1_3 (.I0(_2x1_mux_v1_1_1_out), .I1(_2x1_mux_v1_1_2_out), .S0(S1), .OUT(O));
endmodule
