// Digital circuit 8X1 MUX V1.2.dig as structural Verilog
module _8X1_MUX_V1_2 (
  input  I0,
  input  I1,
  input  I2,
  input  I3,
  input  I4,
  input  I5,
  input  I6,
  input  I7,
  input  S0,
  input  S1,
  input  S2,
  output OUT
);

  wire _4x1_mux_v1_2_1_o, _4x1_mux_v1_2_2_o;

  _4X1_MUX_V1_2 _4x1_mux_v1_2_1 (.I0(I0), .I1(I1), .I2(I2), .I3(I3), .S0(S0), .S1(S1), .O(_4x1_mux_v1_2_1_o));
  _4X1_MUX_V1_2 _4x1_mux_v1_2_2 (.I0(I4), .I1(I5), .I2(I6), .I3(I7), .S0(S0), .S1(S1), .O(_4x1_mux_v1_2_2_o));
  _2X1_MUX_V1_1 _2x1_mux_v1_1_1 (.I0(_4x1_mux_v1_2_1_o), .I1(_4x1_mux_v1_2_2_o), .S0(S2), .OUT(OUT));
endmodule
