// Digital circuit 3x8 DEC V1.dig as structural Verilog
module _3x8_DEC_V1 (
  input  I0,
  input  EN,
  input  I1,
  input  I2,
  output O0,
  output O1,
  output O2,
  output O3,
  output O4,
  output O5,
  output O6,
  output O7
);

  wire _1x2_dec_v1_1_p3, _1x2_dec_v1_1_p4;

  // _1x2_DEC_V1 _1x2_dec_v1_1: pin names not known; wires that end beside it: EN, I2, _1x2_dec_v1_1_p3, _1x2_dec_v1_1_p4
  _2x4_DEC_V1 _2x4_dec_v1_1 (.EN(_1x2_dec_v1_1_p3), .I0(I0), .I1(I1), .O0(O0), .O1(O1), .O2(O2), .O3(O3));
  _2x4_DEC_V1 _2x4_dec_v1_2 (.EN(_1x2_dec_v1_1_p4), .I0(I0), .I1(I1), .O0(O4), .O1(O5), .O2(O6), .O3(O7));
endmodule
