// Digital circuit 4x16 DEC V1.dig as structural Verilog
module _4x16_DEC_V1 (
  input  I0,
  input  EN,
  input  I1,
  input  I2,
  input  I3,
  output O0,
  output O1,
  output O2,
  output O3,
  output O4,
  output O5,
  output O6,
  output O7,
  output O8,
  output O9,
  output O10,
  output O11,
  output O12,
  output O13,
  output O14,
  output O15
);

  wire _1x2_dec_v1_1_p3, _1x2_dec_v1_1_p4;

  // _1x2_DEC_V1 _1x2_dec_v1_1: pin names not known; wires that end beside it: EN, I3, _1x2_dec_v1_1_p3, _1x2_dec_v1_1_p4
  _3x8_DEC_V1 _3x8_dec_v1_1 (
    .O0(O0), .O1(O1), .O2(O2), .O3(O3), .O4(O4), .O5(O5), .O6(O6), .O7(O7), .EN(_1x2_dec_v1_1_p3), .I0(I0),
    .I1(I1), .I2(I2));
  _3x8_DEC_V1 _3x8_dec_v1_2 (
    .O0(O8), .O1(O9), .O2(O10), .O3(O11), .O4(O12), .O5(O13), .O6(O14), .O7(O15), .EN(_1x2_dec_v1_1_p4),
    .I0(I0), .I1(I1), .I2(I2));
endmodule
