// Digital circuit 1x2 DENUX 16 BIT V1.dig as structural Verilog
module _1x2_DENUX_16_BIT_V1 (
  input  I0,
  input  I1,
  input  I2,
  input  I3,
  input  I4,
  input  I5,
  input  I6,
  input  I7,
  input  I8,
  input  I9,
  input  I10,
  input  I11,
  input  I12,
  input  I13,
  input  I14,
  input  I15,
  input  EN,
  input  S0,
  output O0_0,
  output O0_1,
  output O0_2,
  output O0_3,
  output O0_4,
  output O0_5,
  output O0_6,
  output O0_7,
  output O0_8,
  output O0_9,
  output O0_10,
  output O0_11,
  output O0_12,
  output O0_13,
  output O0_14,
  output O0_15,
  output O1_0,
  output O1_1,
  output O1_2,
  output O1_3,
  output O1_4,
  output O1_5,
  output O1_6,
  output O1_7,
  output O1_8,
  output O1_9,
  output O1_10,
  output O1_11,
  output O1_12,
  output O1_13,
  output O1_14,
  output O1_15
);

  wire _1x2_dec_v1_dec_1_p3, _1x2_dec_v1_dec_1_p4;

  // _1x2_DEC_V1_DEC _1x2_dec_v1_dec_1: pin names not known; wires that end beside it: EN, S0, _1x2_dec_v1_dec_1_p3, _1x2_dec_v1_dec_1_p4
  and and_1 (O0_0, I0, _1x2_dec_v1_dec_1_p3);
  and and_2 (O0_1, I1, _1x2_dec_v1_dec_1_p3);
  and and_3 (O0_2, I2, _1x2_dec_v1_dec_1_p3);
  and and_4 (O0_3, I3, _1x2_dec_v1_dec_1_p3);
  and and_5 (O0_4, I4, _1x2_dec_v1_dec_1_p3);
  and and_6 (O0_5, I5, _1x2_dec_v1_dec_1_p3);
  and and_7 (O0_6, I6, _1x2_dec_v1_dec_1_p3);
  and and_8 (O0_7, I7, _1x2_dec_v1_dec_1_p3);
  and and_9 (O0_8, I8, _1x2_dec_v1_dec_1_p3);
  and and_10 (O0_9, I9, _1x2_dec_v1_dec_1_p3);
  and and_11 (O0_10, I10, _1x2_dec_v1_dec_1_p3);
  and and_12 (O0_11, I11, _1x2_dec_v1_dec_1_p3);
  and and_13 (O0_12, I12, _1x2_dec_v1_dec_1_p3);
  and and_14 (O0_13, I13, _1x2_dec_v1_dec_1_p3);
  and and_15 (O0_14, I14, _1x2_dec_v1_dec_1_p3);
  and and_16 (O0_15, I15, _1x2_dec_v1_dec_1_p3);
  and and_17 (O1_0, I0, _1x2_dec_v1_dec_1_p4);
  and and_18 (O1_1, I1, _1x2_dec_v1_dec_1_p4);
  and and_19 (O1_2, I2, _1x2_dec_v1_dec_1_p4);
  and and_20 (O1_3, I3, _1x2_dec_v1_dec_1_p4);
  and and_21 (O1_4, I4, _1x2_dec_v1_dec_1_p4);
  and and_22 (O1_5, I5, _1x2_dec_v1_dec_1_p4);
  and and_23 (O1_6, I6, _1x2_dec_v1_dec_1_p4);
  and and_24 (O1_7, I7, _1x2_dec_v1_dec_1_p4);
  and and_25 (O1_8, I8, _1x2_dec_v1_dec_1_p4);
  and and_26 (O1_9, I9, _1x2_dec_v1_dec_1_p4);
  and and_27 (O1_10, I10, _1x2_dec_v1_dec_1_p4);
  and and_28 (O1_11, I11, _1x2_dec_v1_dec_1_p4);
  and and_29 (O1_12, I12, _1x2_dec_v1_dec_1_p4);
  and and_30 (O1_13, I13, _1x2_dec_v1_dec_1_p4);
  and and_31 (O1_14, I14, _1x2_dec_v1_dec_1_p4);
  and and_32 (O1_15, I15, _1x2_dec_v1_dec_1_p4);
endmodule
