// Digital circuit 1x4 DENUX 16 BIT V1.dig as structural Verilog
module _1x4_DENUX_16_BIT_V1 (
  input  EN,
  input  S1,
  input  S0,
  input  I0,
  input  I1,
  input  I2,
  input  I3,
  input  I4,
  input  I5,
  input  I6,
  input  I7,
  input  I8,
  input  I9,
  input  I10,
  input  I11,
  input  I12,
  input  I13,
  input  I14,
  input  I15,
  output O0_0,
  output O0_1,
  output O0_2,
  output O0_3,
  output O0_4,
  output O0_5,
  output O0_6,
  output O0_7,
  output O0_8,
  output O0_9,
  output O0_10,
  output O0_11,
  output O0_12,
  output O0_13,
  output O0_14,
  output O0_15,
  output O1_0,
  output O2_0,
  output O3_0,
  output O1_1,
  output O2_1,
  output O3_1,
  output O1_2,
  output O2_2,
  output O3_2,
  output O1_3,
  output O2_3,
  output O3_3,
  output O1_4,
  output O2_4,
  output O3_4,
  output O1_5,
  output O2_5,
  output O3_5,
  output O1_6,
  output O2_6,
  output O3_6,
  output O1_7,
  output O2_7,
  output O3_7,
  output O1_8,
  output O2_8,
  output O3_8,
  output O1_9,
  output O2_9,
  output O3_9,
  output O1_10,
  output O2_10,
  output O3_10,
  output O1_11,
  output O2_11,
  output O3_11,
  output O1_12,
  output O2_12,
  output O3_12,
  output O1_13,
  output O2_13,
  output O3_13,
  output O1_14,
  output O2_14,
  output O3_14,
  output O1_15,
  output O2_15,
  output O3_15
);

  wire _1x2_dec_v1_dec_1_p3, _1x2_dec_v1_dec_1_p4;

  // _1x2_DEC_V1_DEC _1x2_dec_v1_dec_1: pin names not known; wires that end beside it: EN, S1, _1x2_dec_v1_dec_1_p3, _1x2_dec_v1_dec_1_p4
  _1x2_DENUX_16_BIT_V1 _1x2_denux_16_bit_v1_1 (
    .O0_0(O0_0), .O0_1(O0_1), .O0_2(O0_2), .O0_3(O0_3), .O0_4(O0_4), .O0_5(O0_5), .O0_6(O0_6), .O0_7(O0_7),
    .O0_8(O0_8), .O0_9(O0_9), .O0_10(O0_10), .O0_11(O0_11), .O0_12(O0_12), .O0_13(O0_13), .O0_14(O0_14),
    .O0_15(O0_15), .O1_0(O1_0), .O1_1(O1_1), .O1_2(O1_2), .O1_3(O1_3), .O1_4(O1_4), .O1_5(O1_5), .O1_6(O1_6),
    .O1_7(O1_7), .O1_8(O1_8), .O1_9(O1_9), .O1_10(O1_10), .O1_11(O1_11), .O1_12(O1_12), .O1_13(O1_13),
    .O1_14(O1_14), .O1_15(O1_15), .EN(_1x2_dec_v1_dec_1_p3), .S0(S0), .I0(I0), .I1(I1), .I2(I2), .I3(I3),
    .I4(I4), .I5(I5), .I6(I6), .I7(I7), .I8(I8), .I9(I9), .I10(I10), .I11(I11), .I12(I12), .I13(I13),
    .I14(I14), .I15(I15));
  _1x2_DENUX_16_BIT_V1 _1x2_denux_16_bit_v1_2 (
    .O0_0(O2_0), .O0_1(O2_1), .O0_2(O2_2), .O0_3(O2_3), .O0_4(O2_4), .O0_5(O2_5), .O0_6(O2_6), .O0_7(O2_7),
    .O0_8(O2_8), .O0_9(O2_9), .O0_10(O2_10), .O0_11(O2_11), .O0_12(O2_12), .O0_13(O2_13), .O0_14(O2_14),
    .O0_15(O2_15), .O1_0(O3_0), .O1_1(O3_1), .O1_2(O3_2), .O1_3(O3_3), .O1_4(O3_4), .O1_5(O3_5), .O1_6(O3_6),
    .O1_7(O3_7), .O1_8(O3_8), .O1_9(O3_9), .O1_10(O3_10), .O1_11(O3_11), .O1_12(O3_12), .O1_13(O3_13),
    .O1_14(O3_14), .O1_15(O3_15), .EN(_1x2_dec_v1_dec_1_p4), .S0(S0), .I0(I0), .I1(I1), .I2(I2), .I3(I3),
    .I4(I4), .I5(I5), .I6(I6), .I7(I7), .I8(I8), .I9(I9), .I10(I10), .I11(I11), .I12(I12), .I13(I13),
    .I14(I14), .I15(I15));
endmodule
