// Digital circuit 2X1 MUX 4 BIT V1.dig as structural Verilog
module _2X1_MUX_4_BIT_V1 (
  input  S0,
  input  EN,
  input  I0_0,
  input  I1_0,
  input  I0_1,
  input  I1_1,
  input  I0_2,
  input  I1_2,
  input  I0_3,
  input  I1_3,
  output O0,
  output O1,
  output O2,
  output O3
);

  wire and_1_out, and_2_out, and_3_out, and_4_out, and_5_out, and_6_out, and_7_out, and_8_out, and_9_out,
       and_10_out, not_1_out;

  not not_1 (not_1_out, S0);
  and and_1 (and_1_out, not_1_out, EN);
  and and_2 (and_2_out, S0, EN);
  and and_3 (and_3_out, I0_0, and_1_out);
  and and_4 (and_4_out, I0_1, and_1_out);
  and and_5 (and_5_out, I0_2, and_1_out);
  and and_6 (and_6_out, I0_3, and_1_out);
  and and_7 (and_7_out, I1_0, and_2_out);
  and and_8 (and_8_out, I1_1, and_2_out);
  and and_9 (and_9_out, I1_2, and_2_out);
  and and_10 (and_10_out, I1_3, and_2_out);
  or or_1 (O0, and_3_out, and_7_out);
  or or_2 (O1, and_4_out, and_8_out);
  or or_3 (O2, and_5_out, and_9_out);
  or or_4 (O3, and_6_out, and_10_out);
endmodule
