// Digital circuit 4X1 MUX 4 BIT V1.dig as structural Verilog
module _4X1_MUX_4_BIT_V1 (
  input  I0_0,
  input  I1_0,
  input  S0,
  input  EN,
  input  S1,
  input  I2_0,
  input  I3_0,
  input  I0_1,
  input  I1_1,
  input  I2_1,
  input  I3_1,
  input  I0_2,
  input  I1_2,
  input  I2_2,
  input  I3_2,
  input  I0_3,
  input  I1_3,
  input  I2_3,
  input  I3_3,
  output O0,
  output O1,
  output O2,
  output O3
);

  wire _2x1_mux_4_bit_v1_1_o0, _2x1_mux_4_bit_v1_1_o1, _2x1_mux_4_bit_v1_1_o2, _2x1_mux_4_bit_v1_1_o3,
       _2x1_mux_4_bit_v1_2_o0, _2x1_mux_4_bit_v1_2_o1, _2x1_mux_4_bit_v1_2_o2, _2x1_mux_4_bit_v1_2_o3;

  _2X1_MUX_4_BIT_V1 _2x1_mux_4_bit_v1_1 (
    .I0_0(I0_0), .I0_1(I0_1), .I0_2(I0_2), .I0_3(I0_3), .I1_0(I1_0), .I1_1(I1_1), .I1_2(I1_2), .I1_3(I1_3),
    .S0(S0), .EN(EN), .O0(_2x1_mux_4_bit_v1_1_o0), .O1(_2x1_mux_4_bit_v1_1_o1), .O2(_2x1_mux_4_bit_v1_1_o2),
    .O3(_2x1_mux_4_bit_v1_1_o3));
  _2X1_MUX_4_BIT_V1 _2x1_mux_4_bit_v1_2 (
    .I0_0(I2_0), .I0_1(I2_1), .I0_2(I2_2), .I0_3(I2_3), .I1_0(I3_0), .I1_1(I3_1), .I1_2(I3_2), .I1_3(I3_3),
    .S0(S0), .EN(EN), .O0(_2x1_mux_4_bit_v1_2_o0), .O1(_2x1_mux_4_bit_v1_2_o1), .O2(_2x1_mux_4_bit_v1_2_o2),
    .O3(_2x1_mux_4_bit_v1_2_o3));
  _2X1_MUX_4_BIT_V1 _2x1_mux_4_bit_v1_3 (
    .I0_0(_2x1_mux_4_bit_v1_1_o0), .I0_1(_2x1_mux_4_bit_v1_1_o1), .I0_2(_2x1_mux_4_bit_v1_1_o2),
    .I0_3(_2x1_mux_4_bit_v1_1_o3), .I1_0(_2x1_mux_4_bit_v1_2_o0), .I1_1(_2x1_mux_4_bit_v1_2_o1),
    .I1_2(_2x1_mux_4_bit_v1_2_o2), .I1_3(_2x1_mux_4_bit_v1_2_o3), .S0(S1), .EN(EN), .O0(O0), .O1(O1),
    .O2(O2), .O3(O3));
endmodule
