// Digital circuit 8X1 MUX 16 BIT V1.dig as structural Verilog
module _8X1_MUX_16_BIT_V1 (
  input  IN0_0,
  input  IN1_0,
  input  IN0_1,
  input  IN0_2,
  input  IN0_3,
  input  IN0_4,
  input  IN0_5,
  input  IN0_6,
  input  IN0_7,
  input  IN0_8,
  input  IN0_9,
  input  IN0_10,
  input  IN0_11,
  input  IN0_12,
  input  IN0_13,
  input  IN0_14,
  input  IN0_15,
  input  IN1_1,
  input  IN1_2,
  input  IN1_3,
  input  IN1_4,
  input  IN1_5,
  input  IN1_6,
  input  IN1_7,
  input  IN1_8,
  input  IN1_9,
  input  IN1_10,
  input  IN1_11,
  input  IN1_12,
  input  IN1_13,
  input  IN1_14,
  input  IN1_15,
  input  IN2_0,
  input  IN3_0,
  input  IN2_1,
  input  IN2_2,
  input  IN2_3,
  input  IN2_4,
  input  IN2_5,
  input  IN2_6,
  input  IN2_7,
  input  IN2_8,
  input  IN2_9,
  input  IN2_10,
  input  IN2_11,
  input  IN2_12,
  input  IN2_13,
  input  IN2_14,
  input  IN2_15,
  input  IN3_1,
  input  IN3_2,
  input  IN3_3,
  input  IN3_4,
  input  IN3_5,
  input  IN3_6,
  input  IN3_7,
  input  IN3_8,
  input  IN3_9,
  input  IN3_10,
  input  IN3_11,
  input  IN3_12,
  input  IN3_13,
  input  IN3_14,
  input  IN3_15,
  input  IN4_0,
  input  IN5_0,
  input  IN6_0,
  input  IN7_0,
  input  IN4_1,
  input  IN5_1,
  input  IN6_1,
  input  IN7_1,
  input  IN4_2,
  input  IN5_2,
  input  IN6_2,
  input  IN7_2,
  input  IN4_3,
  input  IN5_3,
  input  IN6_3,
  input  IN7_3,
  input  IN4_4,
  input  IN5_4,
  input  IN6_4,
  input  IN7_4,
  input  IN4_5,
  input  IN5_5,
  input  IN6_5,
  input  IN7_5,
  input  IN4_6,
  input  IN5_6,
  input  IN6_6,
  input  IN7_6,
  input  IN4_7,
  input  IN5_7,
  input  IN6_7,
  input  IN7_7,
  input  IN4_8,
  input  IN5_8,
  input  IN6_8,
  input  IN7_8,
  input  IN4_9,
  input  IN5_9,
  input  IN6_9,
  input  IN7_9,
  input  IN4_10,
  input  IN5_10,
  input  IN6_10,
  input  IN7_10,
  input  IN4_11,
  input  IN5_11,
  input  IN6_11,
  input  IN7_11,
  input  IN4_12,
  input  IN5_12,
  input  IN6_12,
  input  IN7_12,
  input  IN4_13,
  input  IN5_13,
  input  IN6_13,
  input  IN7_13,
  input  IN4_14,
  input  IN5_14,
  input  IN6_14,
  input  IN7_14,
  input  IN4_15,
  input  IN5_15,
  input  IN6_15,
  input  IN7_15,
  input  S0,
  input  S1,
  input  S2,
  input  EN,
  output O0,
  output O1,
  output O2,
  output O3,
  output O4,
  output O5,
  output O6,
  output O7,
  output O8,
  output O9,
  output O10,
  output O11,
  output O12,
  output O13,
  output O14,
  output O15
);

  wire _4x1_mux_16_bit_v1_1_o0, _4x1_mux_16_bit_v1_1_o1, _4x1_mux_16_bit_v1_1_o2, _4x1_mux_16_bit_v1_1_o3,
       _4x1_mux_16_bit_v1_1_o4, _4x1_mux_16_bit_v1_1_o5, _4x1_mux_16_bit_v1_1_o6, _4x1_mux_16_bit_v1_1_o7,
       _4x1_mux_16_bit_v1_1_o8, _4x1_mux_16_bit_v1_1_o9, _4x1_mux_16_bit_v1_1_o10, _4x1_mux_16_bit_v1_1_o11,
       _4x1_mux_16_bit_v1_1_o12, _4x1_mux_16_bit_v1_1_o13, _4x1_mux_16_bit_v1_1_o14,
       _4x1_mux_16_bit_v1_1_o15, _4x1_mux_16_bit_v1_2_o0, _4x1_mux_16_bit_v1_2_o1, _4x1_mux_16_bit_v1_2_o2,
       _4x1_mux_16_bit_v1_2_o3, _4x1_mux_16_bit_v1_2_o4, _4x1_mux_16_bit_v1_2_o5, _4x1_mux_16_bit_v1_2_o6,
       _4x1_mux_16_bit_v1_2_o7, _4x1_mux_16_bit_v1_2_o8, _4x1_mux_16_bit_v1_2_o9, _4x1_mux_16_bit_v1_2_o10,
       _4x1_mux_16_bit_v1_2_o11, _4x1_mux_16_bit_v1_2_o12, _4x1_mux_16_bit_v1_2_o13,
       _4x1_mux_16_bit_v1_2_o14, _4x1_mux_16_bit_v1_2_o15;

  _4X1_MUX_16_BIT_V1 _4x1_mux_16_bit_v1_1 (
    .O0(_4x1_mux_16_bit_v1_1_o0), .O1(_4x1_mux_16_bit_v1_1_o1), .O2(_4x1_mux_16_bit_v1_1_o2),
    .O3(_4x1_mux_16_bit_v1_1_o3), .O4(_4x1_mux_16_bit_v1_1_o4), .O5(_4x1_mux_16_bit_v1_1_o5),
    .O6(_4x1_mux_16_bit_v1_1_o6), .O7(_4x1_mux_16_bit_v1_1_o7), .O8(_4x1_mux_16_bit_v1_1_o8),
    .O9(_4x1_mux_16_bit_v1_1_o9), .O10(_4x1_mux_16_bit_v1_1_o10), .O11(_4x1_mux_16_bit_v1_1_o11),
    .O12(_4x1_mux_16_bit_v1_1_o12), .O13(_4x1_mux_16_bit_v1_1_o13), .O14(_4x1_mux_16_bit_v1_1_o14),
    .O15(_4x1_mux_16_bit_v1_1_o15), .IN0_0(IN0_0), .IN0_1(IN0_1), .IN0_2(IN0_2), .IN0_3(IN0_3),
    .IN0_4(IN0_4), .IN0_5(IN0_5), .IN0_6(IN0_6), .IN0_7(IN0_7), .IN0_8(IN0_8), .IN0_9(IN0_9),
    .IN0_10(IN0_10), .IN0_11(IN0_11), .IN0_12(IN0_12), .IN0_13(IN0_13), .IN0_14(IN0_14), .IN0_15(IN0_15),
    .IN1_0(IN1_0), .IN1_1(IN1_1), .IN1_2(IN1_2), .IN1_3(IN1_3), .IN1_4(IN1_4), .IN1_5(IN1_5), .IN1_6(IN1_6),
    .IN1_7(IN1_7), .IN1_8(IN1_8), .IN1_9(IN1_9), .IN1_10(IN1_10), .IN1_11(IN1_11), .IN1_12(IN1_12),
    .IN1_13(IN1_13), .IN1_14(IN1_14), .IN1_15(IN1_15), .IN2_0(IN2_0), .IN2_1(IN2_1), .IN2_2(IN2_2),
    .IN2_3(IN2_3), .IN2_4(IN2_4), .IN2_5(IN2_5), .IN2_6(IN2_6), .IN2_7(IN2_7), .IN2_8(IN2_8), .IN2_9(IN2_9),
    .IN2_10(IN2_10), .IN2_11(IN2_11), .IN2_12(IN2_12), .IN2_13(IN2_13), .IN2_14(IN2_14), .IN2_15(IN2_15),
    .IN3_0(IN3_0), .IN3_1(IN3_1), .IN3_2(IN3_2), .IN3_3(IN3_3), .IN3_4(IN3_4), .IN3_5(IN3_5), .IN3_6(IN3_6),
    .IN3_7(IN3_7), .IN3_8(IN3_8), .IN3_9(IN3_9), .IN3_10(IN3_10), .IN3_11(IN3_11), .IN3_12(IN3_12),
    .IN3_13(IN3_13), .IN3_14(IN3_14), .IN3_15(IN3_15), .S0(S0), .S1(S1), .EN(EN));
  _4X1_MUX_16_BIT_V1 _4x1_mux_16_bit_v1_2 (
    .O0(_4x1_mux_16_bit_v1_2_o0), .O1(_4x1_mux_16_bit_v1_2_o1), .O2(_4x1_mux_16_bit_v1_2_o2),
    .O3(_4x1_mux_16_bit_v1_2_o3), .O4(_4x1_mux_16_bit_v1_2_o4), .O5(_4x1_mux_16_bit_v1_2_o5),
    .O6(_4x1_mux_16_bit_v1_2_o6), .O7(_4x1_mux_16_bit_v1_2_o7), .O8(_4x1_mux_16_bit_v1_2_o8),
    .O9(_4x1_mux_16_bit_v1_2_o9), .O10(_4x1_mux_16_bit_v1_2_o10), .O11(_4x1_mux_16_bit_v1_2_o11),
    .O12(_4x1_mux_16_bit_v1_2_o12), .O13(_4x1_mux_16_bit_v1_2_o13), .O14(_4x1_mux_16_bit_v1_2_o14),
    .O15(_4x1_mux_16_bit_v1_2_o15), .IN0_0(IN4_0), .IN0_1(IN4_1), .IN0_2(IN4_2), .IN0_3(IN4_3),
    .IN0_4(IN4_4), .IN0_5(IN4_5), .IN0_6(IN4_6), .IN0_7(IN4_7), .IN0_8(IN4_8), .IN0_9(IN4_9),
    .IN0_10(IN4_10), .IN0_11(IN4_11), .IN0_12(IN4_12), .IN0_13(IN4_13), .IN0_14(IN4_14), .IN0_15(IN4_15),
    .IN1_0(IN5_0), .IN1_1(IN5_1), .IN1_2(IN5_2), .IN1_3(IN5_3), .IN1_4(IN5_4), .IN1_5(IN5_5), .IN1_6(IN5_6),
    .IN1_7(IN5_7), .IN1_8(IN5_8), .IN1_9(IN5_9), .IN1_10(IN5_10), .IN1_11(IN5_11), .IN1_12(IN5_12),
    .IN1_13(IN5_13), .IN1_14(IN5_14), .IN1_15(IN5_15), .IN2_0(IN6_0), .IN2_1(IN6_1), .IN2_2(IN6_2),
    .IN2_3(IN6_3), .IN2_4(IN6_4), .IN2_5(IN6_5), .IN2_6(IN6_6), .IN2_7(IN6_7), .IN2_8(IN6_8), .IN2_9(IN6_9),
    .IN2_10(IN6_10), .IN2_11(IN6_11), .IN2_12(IN6_12), .IN2_13(IN6_13), .IN2_14(IN6_14), .IN2_15(IN6_15),
    .IN3_0(IN7_0), .IN3_1(IN7_1), .IN3_2(IN7_2), .IN3_3(IN7_3), .IN3_4(IN7_4), .IN3_5(IN7_5), .IN3_6(IN7_6),
    .IN3_7(IN7_7), .IN3_8(IN7_8), .IN3_9(IN7_9), .IN3_10(IN7_10), .IN3_11(IN7_11), .IN3_12(IN7_12),
    .IN3_13(IN7_13), .IN3_14(IN7_14), .IN3_15(IN7_15), .S0(S0), .S1(S1), .EN(EN));
  _2X1_MUX_16_BIT_V1 _2x1_mux_16_bit_v1_1 (
    .IN0_0(_4x1_mux_16_bit_v1_1_o0), .IN0_1(_4x1_mux_16_bit_v1_1_o1), .IN0_2(_4x1_mux_16_bit_v1_1_o2),
    .IN0_3(_4x1_mux_16_bit_v1_1_o3), .IN0_4(_4x1_mux_16_bit_v1_1_o4), .IN0_5(_4x1_mux_16_bit_v1_1_o5),
    .IN0_6(_4x1_mux_16_bit_v1_1_o6), .IN0_7(_4x1_mux_16_bit_v1_1_o7), .IN0_8(_4x1_mux_16_bit_v1_1_o8),
    .IN0_9(_4x1_mux_16_bit_v1_1_o9), .IN0_10(_4x1_mux_16_bit_v1_1_o10), .IN0_11(_4x1_mux_16_bit_v1_1_o11),
    .IN0_12(_4x1_mux_16_bit_v1_1_o12), .IN0_13(_4x1_mux_16_bit_v1_1_o13), .IN0_14(_4x1_mux_16_bit_v1_1_o14),
    .IN0_15(_4x1_mux_16_bit_v1_1_o15), .IN1_0(_4x1_mux_16_bit_v1_2_o0), .IN1_1(_4x1_mux_16_bit_v1_2_o1),
    .IN1_2(_4x1_mux_16_bit_v1_2_o2), .IN1_3(_4x1_mux_16_bit_v1_2_o3), .IN1_4(_4x1_mux_16_bit_v1_2_o4),
    .IN1_5(_4x1_mux_16_bit_v1_2_o5), .IN1_6(_4x1_mux_16_bit_v1_2_o6), .IN1_7(_4x1_mux_16_bit_v1_2_o7),
    .IN1_8(_4x1_mux_16_bit_v1_2_o8), .IN1_9(_4x1_mux_16_bit_v1_2_o9), .IN1_10(_4x1_mux_16_bit_v1_2_o10),
    .IN1_11(_4x1_mux_16_bit_v1_2_o11), .IN1_12(_4x1_mux_16_bit_v1_2_o12), .IN1_13(_4x1_mux_16_bit_v1_2_o13),
    .IN1_14(_4x1_mux_16_bit_v1_2_o14), .IN1_15(_4x1_mux_16_bit_v1_2_o15), .S0(S2), .EN(EN), .O0(O0), .O1(O1),
    .O2(O2), .O3(O3), .O4(O4), .O5(O5), .O6(O6), .O7(O7), .O8(O8), .O9(O9), .O10(O10), .O11(O11), .O12(O12),
    .O13(O13), .O14(O14), .O15(O15));
endmodule
