// Digital circuit 16 BIT ADD MEM.dig as structural Verilog
module _16_BIT_ADD_MEM (
  input  RST,
  input  WE,
  input  D0,
  input  D1,
  input  D2,
  input  D3,
  input  D4,
  input  D5,
  input  D6,
  input  D7,
  input  D8,
  input  D9,
  input  D10,
  input  D11,
  input  D12,
  input  D13,
  input  D14,
  input  D15,
  input  AD0,
  input  AD1,
  input  AW2,
  input  AW3,
  input  AW1,
  input  AW0,
  input  AD2,
  input  AD3,
  input  AW4,
  input  AW5,
  input  AD4,
  input  AD5,
  input  AW6,
  input  AW7,
  input  AD6,
  input  AD7,
  input  AD8,
  input  AD9,
  input  AW8,
  input  AW9,
  input  AW10,
  input  AW11,
  input  AD10,
  input  AD11,
  input  AW12,
  input  AW13,
  input  AD12,
  input  AD13,
  input  AW14,
  input  AW15,
  input  AD14,
  input  AD15,
  input  CLK,
  output OD0,
  output OD1,
  output OD2,
  output OD3,
  output OD4,
  output OD5,
  output OD6,
  output OD7,
  output OD8,
  output OD9,
  output OD10,
  output OD11,
  output OD12,
  output OD13,
  output OD14,
  output OD15
);

  wire _2x4_dec_v1_3_1_o0, _2x4_dec_v1_3_1_o1, _2x4_dec_v1_3_1_o2, _2x4_dec_v1_3_1_o3, _14_bit_add_mem_1_od0,
       _14_bit_add_mem_1_od1, _14_bit_add_mem_1_od2, _14_bit_add_mem_1_od3, _14_bit_add_mem_1_od4,
       _14_bit_add_mem_1_od5, _14_bit_add_mem_1_od6, _14_bit_add_mem_1_od7, _14_bit_add_mem_1_od8,
       _14_bit_add_mem_1_od9, _14_bit_add_mem_1_od10, _14_bit_add_mem_1_od11, _14_bit_add_mem_1_od12,
       _14_bit_add_mem_1_od13, _14_bit_add_mem_1_od14, _14_bit_add_mem_1_od15, _14_bit_add_mem_2_od0,
       _14_bit_add_mem_2_od1, _14_bit_add_mem_2_od2, _14_bit_add_mem_2_od3, _14_bit_add_mem_2_od4,
       _14_bit_add_mem_2_od5, _14_bit_add_mem_2_od6, _14_bit_add_mem_2_od7, _14_bit_add_mem_2_od8,
       _14_bit_add_mem_2_od9, _14_bit_add_mem_2_od10, _14_bit_add_mem_2_od11, _14_bit_add_mem_2_od12,
       _14_bit_add_mem_2_od13, _14_bit_add_mem_2_od14, _14_bit_add_mem_2_od15, _14_bit_add_mem_3_od0,
       _14_bit_add_mem_3_od1, _14_bit_add_mem_3_od2, _14_bit_add_mem_3_od3, _14_bit_add_mem_3_od4,
       _14_bit_add_mem_3_od5, _14_bit_add_mem_3_od6, _14_bit_add_mem_3_od7, _14_bit_add_mem_3_od8,
       _14_bit_add_mem_3_od9, _14_bit_add_mem_3_od10, _14_bit_add_mem_3_od11, _14_bit_add_mem_3_od12,
       _14_bit_add_mem_3_od13, _14_bit_add_mem_3_od14, _14_bit_add_mem_3_od15, _14_bit_add_mem_4_od0,
       _14_bit_add_mem_4_od1, _14_bit_add_mem_4_od2, _14_bit_add_mem_4_od3, _14_bit_add_mem_4_od4,
       _14_bit_add_mem_4_od5, _14_bit_add_mem_4_od6, _14_bit_add_mem_4_od7, _14_bit_add_mem_4_od8,
       _14_bit_add_mem_4_od9, _14_bit_add_mem_4_od10, _14_bit_add_mem_4_od11, _14_bit_add_mem_4_od12,
       _14_bit_add_mem_4_od13, _14_bit_add_mem_4_od14, _14_bit_add_mem_4_od15;

  _2x4_DEC_V1_3 _2x4_dec_v1_3_1 (
    .EN(WE), .I0(AW14), .I1(AW15), .O0(_2x4_dec_v1_3_1_o0), .O1(_2x4_dec_v1_3_1_o1), .O2(_2x4_dec_v1_3_1_o2),
    .O3(_2x4_dec_v1_3_1_o3));
  _4X1_MUX_16_BIT_V1_3 _4x1_mux_16_bit_v1_3_1 (
    .O0(OD0), .O1(OD1), .O2(OD2), .O3(OD3), .O4(OD4), .O5(OD5), .O6(OD6), .O7(OD7), .O8(OD8), .O9(OD9),
    .O10(OD10), .O11(OD11), .O12(OD12), .O13(OD13), .O14(OD14), .O15(OD15), .IN0_0(_14_bit_add_mem_4_od0),
    .IN0_1(_14_bit_add_mem_4_od1), .IN0_2(_14_bit_add_mem_4_od2), .IN0_3(_14_bit_add_mem_4_od3),
    .IN0_4(_14_bit_add_mem_4_od4), .IN0_5(_14_bit_add_mem_4_od5), .IN0_6(_14_bit_add_mem_4_od6),
    .IN0_7(_14_bit_add_mem_4_od7), .IN0_8(_14_bit_add_mem_4_od8), .IN0_9(_14_bit_add_mem_4_od9),
    .IN0_10(_14_bit_add_mem_4_od10), .IN0_11(_14_bit_add_mem_4_od11), .IN0_12(_14_bit_add_mem_4_od12),
    .IN0_13(_14_bit_add_mem_4_od13), .IN0_14(_14_bit_add_mem_4_od14), .IN0_15(_14_bit_add_mem_4_od15),
    .IN1_0(_14_bit_add_mem_3_od0), .IN1_1(_14_bit_add_mem_3_od1), .IN1_2(_14_bit_add_mem_3_od2),
    .IN1_3(_14_bit_add_mem_3_od3), .IN1_4(_14_bit_add_mem_3_od4), .IN1_5(_14_bit_add_mem_3_od5),
    .IN1_6(_14_bit_add_mem_3_od6), .IN1_7(_14_bit_add_mem_3_od7), .IN1_8(_14_bit_add_mem_3_od8),
    .IN1_9(_14_bit_add_mem_3_od9), .IN1_10(_14_bit_add_mem_3_od10), .IN1_11(_14_bit_add_mem_3_od11),
    .IN1_12(_14_bit_add_mem_3_od12), .IN1_13(_14_bit_add_mem_3_od13), .IN1_14(_14_bit_add_mem_3_od14),
    .IN1_15(_14_bit_add_mem_3_od15), .IN2_0(_14_bit_add_mem_2_od0), .IN2_1(_14_bit_add_mem_2_od1),
    .IN2_2(_14_bit_add_mem_2_od2), .IN2_3(_14_bit_add_mem_2_od3), .IN2_4(_14_bit_add_mem_2_od4),
    .IN2_5(_14_bit_add_mem_2_od5), .IN2_6(_14_bit_add_mem_2_od6), .IN2_7(_14_bit_add_mem_2_od7),
    .IN2_8(_14_bit_add_mem_2_od8), .IN2_9(_14_bit_add_mem_2_od9), .IN2_10(_14_bit_add_mem_2_od10),
    .IN2_11(_14_bit_add_mem_2_od11), .IN2_12(_14_bit_add_mem_2_od12), .IN2_13(_14_bit_add_mem_2_od13),
    .IN2_14(_14_bit_add_mem_2_od14), .IN2_15(_14_bit_add_mem_2_od15), .IN3_0(_14_bit_add_mem_1_od0),
    .IN3_1(_14_bit_add_mem_1_od1), .IN3_2(_14_bit_add_mem_1_od2), .IN3_3(_14_bit_add_mem_1_od3),
    .IN3_4(_14_bit_add_mem_1_od4), .IN3_5(_14_bit_add_mem_1_od5), .IN3_6(_14_bit_add_mem_1_od6),
    .IN3_7(_14_bit_add_mem_1_od7), .IN3_8(_14_bit_add_mem_1_od8), .IN3_9(_14_bit_add_mem_1_od9),
    .IN3_10(_14_bit_add_mem_1_od10), .IN3_11(_14_bit_add_mem_1_od11), .IN3_12(_14_bit_add_mem_1_od12),
    .IN3_13(_14_bit_add_mem_1_od13), .IN3_14(_14_bit_add_mem_1_od14), .IN3_15(_14_bit_add_mem_1_od15),
    .S0(AD14), .S1(AD15), .EN(1'b1));
  _14_BIT_ADD_MEM _14_bit_add_mem_1 (
    .CLK(CLK), .RST(RST), .WE(_2x4_dec_v1_3_1_o0), .AW0(AW0), .AW1(AW1), .AW2(AW2), .AW3(AW3), .AW4(AW4),
    .AW5(AW5), .AW6(AW6), .AW7(AW7), .AW8(AW8), .AW9(AW9), .AW10(AW10), .AW11(AW11), .AW12(AW12),
    .AW13(AW13), .D0(D0), .D1(D1), .D2(D2), .D3(D3), .D4(D4), .D5(D5), .D6(D6), .D7(D7), .D8(D8), .D9(D9),
    .D10(D10), .D11(D11), .D12(D12), .D13(D13), .D14(D14), .D15(D15), .AD0(AD0), .AD1(AD1), .AD2(AD2),
    .AD3(AD3), .AD4(AD4), .AD5(AD5), .AD6(AD6), .AD7(AD7), .AD8(AD8), .AD9(AD9), .AD10(AD10), .AD11(AD11),
    .AD12(AD12), .AD13(AD13), .OD15(_14_bit_add_mem_1_od15), .OD14(_14_bit_add_mem_1_od14),
    .OD13(_14_bit_add_mem_1_od13), .OD12(_14_bit_add_mem_1_od12), .OD11(_14_bit_add_mem_1_od11),
    .OD10(_14_bit_add_mem_1_od10), .OD9(_14_bit_add_mem_1_od9), .OD8(_14_bit_add_mem_1_od8),
    .OD7(_14_bit_add_mem_1_od7), .OD6(_14_bit_add_mem_1_od6), .OD5(_14_bit_add_mem_1_od5),
    .OD4(_14_bit_add_mem_1_od4), .OD3(_14_bit_add_mem_1_od3), .OD2(_14_bit_add_mem_1_od2),
    .OD1(_14_bit_add_mem_1_od1), .OD0(_14_bit_add_mem_1_od0));
  _14_BIT_ADD_MEM _14_bit_add_mem_2 (
    .CLK(CLK), .RST(RST), .WE(_2x4_dec_v1_3_1_o1), .AW0(AW0), .AW1(AW1), .AW2(AW2), .AW3(AW3), .AW4(AW4),
    .AW5(AW5), .AW6(AW6), .AW7(AW7), .AW8(AW8), .AW9(AW9), .AW10(AW10), .AW11(AW11), .AW12(AW12),
    .AW13(AW13), .D0(D0), .D1(D1), .D2(D2), .D3(D3), .D4(D4), .D5(D5), .D6(D6), .D7(D7), .D8(D8), .D9(D9),
    .D10(D10), .D11(D11), .D12(D12), .D13(D13), .D14(D14), .D15(D15), .AD0(AD0), .AD1(AD1), .AD2(AD2),
    .AD3(AD3), .AD4(AD4), .AD5(AD5), .AD6(AD6), .AD7(AD7), .AD8(AD8), .AD9(AD9), .AD10(AD10), .AD11(AD11),
    .AD12(AD12), .AD13(AD13), .OD15(_14_bit_add_mem_2_od15), .OD14(_14_bit_add_mem_2_od14),
    .OD13(_14_bit_add_mem_2_od13), .OD12(_14_bit_add_mem_2_od12), .OD11(_14_bit_add_mem_2_od11),
    .OD10(_14_bit_add_mem_2_od10), .OD9(_14_bit_add_mem_2_od9), .OD8(_14_bit_add_mem_2_od8),
    .OD7(_14_bit_add_mem_2_od7), .OD6(_14_bit_add_mem_2_od6), .OD5(_14_bit_add_mem_2_od5),
    .OD4(_14_bit_add_mem_2_od4), .OD3(_14_bit_add_mem_2_od3), .OD2(_14_bit_add_mem_2_od2),
    .OD1(_14_bit_add_mem_2_od1), .OD0(_14_bit_add_mem_2_od0));
  _14_BIT_ADD_MEM _14_bit_add_mem_3 (
    .CLK(CLK), .RST(RST), .WE(_2x4_dec_v1_3_1_o2), .AW0(AW0), .AW1(AW1), .AW2(AW2), .AW3(AW3), .AW4(AW4),
    .AW5(AW5), .AW6(AW6), .AW7(AW7), .AW8(AW8), .AW9(AW9), .AW10(AW10), .AW11(AW11), .AW12(AW12),
    .AW13(AW13), .D0(D0), .D1(D1), .D2(D2), .D3(D3), .D4(D4), .D5(D5), .D6(D6), .D7(D7), .D8(D8), .D9(D9),
    .D10(D10), .D11(D11), .D12(D12), .D13(D13), .D14(D14), .D15(D15), .AD0(AD0), .AD1(AD1), .AD2(AD2),
    .AD3(AD3), .AD4(AD4), .AD5(AD5), .AD6(AD6), .AD7(AD7), .AD8(AD8), .AD9(AD9), .AD10(AD10), .AD11(AD11),
    .AD12(AD12), .AD13(AD13), .OD15(_14_bit_add_mem_3_od15), .OD14(_14_bit_add_mem_3_od14),
    .OD13(_14_bit_add_mem_3_od13), .OD12(_14_bit_add_mem_3_od12), .OD11(_14_bit_add_mem_3_od11),
    .OD10(_14_bit_add_mem_3_od10), .OD9(_14_bit_add_mem_3_od9), .OD8(_14_bit_add_mem_3_od8),
    .OD7(_14_bit_add_mem_3_od7), .OD6(_14_bit_add_mem_3_od6), .OD5(_14_bit_add_mem_3_od5),
    .OD4(_14_bit_add_mem_3_od4), .OD3(_14_bit_add_mem_3_od3), .OD2(_14_bit_add_mem_3_od2),
    .OD1(_14_bit_add_mem_3_od1), .OD0(_14_bit_add_mem_3_od0));
  _14_BIT_ADD_MEM _14_bit_add_mem_4 (
    .CLK(CLK), .RST(RST), .WE(_2x4_dec_v1_3_1_o3), .AW0(AW0), .AW1(AW1), .AW2(AW2), .AW3(AW3), .AW4(AW4),
    .AW5(AW5), .AW6(AW6), .AW7(AW7), .AW8(AW8), .AW9(AW9), .AW10(AW10), .AW11(AW11), .AW12(AW12),
    .AW13(AW13), .D0(D0), .D1(D1), .D2(D2), .D3(D3), .D4(D4), .D5(D5), .D6(D6), .D7(D7), .D8(D8), .D9(D9),
    .D10(D10), .D11(D11), .D12(D12), .D13(D13), .D14(D14), .D15(D15), .AD0(AD0), .AD1(AD1), .AD2(AD2),
    .AD3(AD3), .AD4(AD4), .AD5(AD5), .AD6(AD6), .AD7(AD7), .AD8(AD8), .AD9(AD9), .AD10(AD10), .AD11(AD11),
    .AD12(AD12), .AD13(AD13), .OD15(_14_bit_add_mem_4_od15), .OD14(_14_bit_add_mem_4_od14),
    .OD13(_14_bit_add_mem_4_od13), .OD12(_14_bit_add_mem_4_od12), .OD11(_14_bit_add_mem_4_od11),
    .OD10(_14_bit_add_mem_4_od10), .OD9(_14_bit_add_mem_4_od9), .OD8(_14_bit_add_mem_4_od8),
    .OD7(_14_bit_add_mem_4_od7), .OD6(_14_bit_add_mem_4_od6), .OD5(_14_bit_add_mem_4_od5),
    .OD4(_14_bit_add_mem_4_od4), .OD3(_14_bit_add_mem_4_od3), .OD2(_14_bit_add_mem_4_od2),
    .OD1(_14_bit_add_mem_4_od1), .OD0(_14_bit_add_mem_4_od0));

  // Notes on the sheet:
  //   CLK: Hz: 2147483647
endmodule
