// Digital circuit 1x2 DEC V1.3.dig as structural Verilog
module _1x2_DEC_V1_3 (
  input  I0,
  input  EN,
  output O0,
  output O1
);

  wire not_1_out;

  not not_1 (not_1_out, I0);
  and and_1 (O0, EN, not_1_out);
  and and_2 (O1, EN, I0);
endmodule
