// Digital circuit 2 BIT DAT MEM.dig as structural Verilog
module _2_BIT_DAT_MEM (
  input  CLK,
  input  RST,
  input  WE,
  input  AW0,
  input  AW1,
  input  D0,
  input  D1,
  input  D2,
  input  D3,
  input  D4,
  input  D5,
  input  D6,
  input  D7,
  input  D8,
  input  D9,
  input  D10,
  input  D11,
  input  D12,
  input  D13,
  input  D14,
  input  D15,
  input  AD0,
  input  AD1,
  output OD0,
  output OD1,
  output OD2,
  output OD3,
  output OD4,
  output OD5,
  output OD6,
  output OD7,
  output OD8,
  output OD9,
  output OD10,
  output OD11,
  output OD12,
  output OD13,
  output OD14,
  output OD15
);

  wire _2x4_dec_v1_3_1_o0, _2x4_dec_v1_3_1_o1, _2x4_dec_v1_3_1_o2, _2x4_dec_v1_3_1_o3, datreg_v1_1_1_do0,
       datreg_v1_1_1_do1, datreg_v1_1_1_do2, datreg_v1_1_1_do3, datreg_v1_1_1_do4, datreg_v1_1_1_do5,
       datreg_v1_1_1_do6, datreg_v1_1_1_do7, datreg_v1_1_1_do8, datreg_v1_1_1_do9, datreg_v1_1_1_do10,
       datreg_v1_1_1_do11, datreg_v1_1_1_do12, datreg_v1_1_1_do13, datreg_v1_1_1_do14, datreg_v1_1_1_do15,
       datreg_v1_1_2_do0, datreg_v1_1_2_do1, datreg_v1_1_2_do2, datreg_v1_1_2_do3, datreg_v1_1_2_do4,
       datreg_v1_1_2_do5, datreg_v1_1_2_do6, datreg_v1_1_2_do7, datreg_v1_1_2_do8, datreg_v1_1_2_do9,
       datreg_v1_1_2_do10, datreg_v1_1_2_do11, datreg_v1_1_2_do12, datreg_v1_1_2_do13, datreg_v1_1_2_do14,
       datreg_v1_1_2_do15, datreg_v1_1_3_do0, datreg_v1_1_3_do1, datreg_v1_1_3_do2, datreg_v1_1_3_do3,
       datreg_v1_1_3_do4, datreg_v1_1_3_do5, datreg_v1_1_3_do6, datreg_v1_1_3_do7, datreg_v1_1_3_do8,
       datreg_v1_1_3_do9, datreg_v1_1_3_do10, datreg_v1_1_3_do11, datreg_v1_1_3_do12, datreg_v1_1_3_do13,
       datreg_v1_1_3_do14, datreg_v1_1_3_do15, datreg_v1_1_4_do0, datreg_v1_1_4_do1, datreg_v1_1_4_do2,
       datreg_v1_1_4_do3, datreg_v1_1_4_do4, datreg_v1_1_4_do5, datreg_v1_1_4_do6, datreg_v1_1_4_do7,
       datreg_v1_1_4_do8, datreg_v1_1_4_do9, datreg_v1_1_4_do10, datreg_v1_1_4_do11, datreg_v1_1_4_do12,
       datreg_v1_1_4_do13, datreg_v1_1_4_do14, datreg_v1_1_4_do15;

  _2x4_DEC_V1_3 _2x4_dec_v1_3_1 (
    .EN(WE), .I0(AW0), .I1(AW1), .O0(_2x4_dec_v1_3_1_o0), .O1(_2x4_dec_v1_3_1_o1), .O2(_2x4_dec_v1_3_1_o2),
    .O3(_2x4_dec_v1_3_1_o3));
  DATREG_V1_1 datreg_v1_1_1 (
    .DIN1(D0), .DIN2(D1), .DIN3(D2), .DIN4(D3), .DIN5(D4), .DIN6(D5), .DIN7(D6), .DIN8(D7), .DIN9(D8),
    .DIN10(D9), .DIN11(D10), .DIN12(D11), .DIN13(D12), .DIN14(D13), .DIN15(D14), .DIN16(D15), .CLK(CLK),
    .RST(RST), .EN(_2x4_dec_v1_3_1_o0), .DO0(datreg_v1_1_1_do0), .DO1(datreg_v1_1_1_do1),
    .DO2(datreg_v1_1_1_do2), .DO3(datreg_v1_1_1_do3), .DO4(datreg_v1_1_1_do4), .DO5(datreg_v1_1_1_do5),
    .DO6(datreg_v1_1_1_do6), .DO7(datreg_v1_1_1_do7), .DO8(datreg_v1_1_1_do8), .DO9(datreg_v1_1_1_do9),
    .DO10(datreg_v1_1_1_do10), .DO11(datreg_v1_1_1_do11), .DO12(datreg_v1_1_1_do12),
    .DO13(datreg_v1_1_1_do13), .DO14(datreg_v1_1_1_do14), .DO15(datreg_v1_1_1_do15));
  DATREG_V1_1 datreg_v1_1_2 (
    .DIN1(D0), .DIN2(D1), .DIN3(D2), .DIN4(D3), .DIN5(D4), .DIN6(D5), .DIN7(D6), .DIN8(D7), .DIN9(D8),
    .DIN10(D9), .DIN11(D10), .DIN12(D11), .DIN13(D12), .DIN14(D13), .DIN15(D14), .DIN16(D15), .CLK(CLK),
    .RST(RST), .EN(_2x4_dec_v1_3_1_o1), .DO0(datreg_v1_1_2_do0), .DO1(datreg_v1_1_2_do1),
    .DO2(datreg_v1_1_2_do2), .DO3(datreg_v1_1_2_do3), .DO4(datreg_v1_1_2_do4), .DO5(datreg_v1_1_2_do5),
    .DO6(datreg_v1_1_2_do6), .DO7(datreg_v1_1_2_do7), .DO8(datreg_v1_1_2_do8), .DO9(datreg_v1_1_2_do9),
    .DO10(datreg_v1_1_2_do10), .DO11(datreg_v1_1_2_do11), .DO12(datreg_v1_1_2_do12),
    .DO13(datreg_v1_1_2_do13), .DO14(datreg_v1_1_2_do14), .DO15(datreg_v1_1_2_do15));
  DATREG_V1_1 datreg_v1_1_3 (
    .DIN1(D0), .DIN2(D1), .DIN3(D2), .DIN4(D3), .DIN5(D4), .DIN6(D5), .DIN7(D6), .DIN8(D7), .DIN9(D8),
    .DIN10(D9), .DIN11(D10), .DIN12(D11), .DIN13(D12), .DIN14(D13), .DIN15(D14), .DIN16(D15), .CLK(CLK),
    .RST(RST), .EN(_2x4_dec_v1_3_1_o2), .DO0(datreg_v1_1_3_do0), .DO1(datreg_v1_1_3_do1),
    .DO2(datreg_v1_1_3_do2), .DO3(datreg_v1_1_3_do3), .DO4(datreg_v1_1_3_do4), .DO5(datreg_v1_1_3_do5),
    .DO6(datreg_v1_1_3_do6), .DO7(datreg_v1_1_3_do7), .DO8(datreg_v1_1_3_do8), .DO9(datreg_v1_1_3_do9),
    .DO10(datreg_v1_1_3_do10), .DO11(datreg_v1_1_3_do11), .DO12(datreg_v1_1_3_do12),
    .DO13(datreg_v1_1_3_do13), .DO14(datreg_v1_1_3_do14), .DO15(datreg_v1_1_3_do15));
  DATREG_V1_1 datreg_v1_1_4 (
    .DIN1(D0), .DIN2(D1), .DIN3(D2), .DIN4(D3), .DIN5(D4), .DIN6(D5), .DIN7(D6), .DIN8(D7), .DIN9(D8),
    .DIN10(D9), .DIN11(D10), .DIN12(D11), .DIN13(D12), .DIN14(D13), .DIN15(D14), .DIN16(D15), .CLK(CLK),
    .RST(RST), .EN(_2x4_dec_v1_3_1_o3), .DO0(datreg_v1_1_4_do0), .DO1(datreg_v1_1_4_do1),
    .DO2(datreg_v1_1_4_do2), .DO3(datreg_v1_1_4_do3), .DO4(datreg_v1_1_4_do4), .DO5(datreg_v1_1_4_do5),
    .DO6(datreg_v1_1_4_do6), .DO7(datreg_v1_1_4_do7), .DO8(datreg_v1_1_4_do8), .DO9(datreg_v1_1_4_do9),
    .DO10(datreg_v1_1_4_do10), .DO11(datreg_v1_1_4_do11), .DO12(datreg_v1_1_4_do12),
    .DO13(datreg_v1_1_4_do13), .DO14(datreg_v1_1_4_do14), .DO15(datreg_v1_1_4_do15));
  _4X1_MUX_16_BIT_V1_3 _4x1_mux_16_bit_v1_3_1 (
    .O0(OD0), .O1(OD1), .O2(OD2), .O3(OD3), .O4(OD4), .O5(OD5), .O6(OD6), .O7(OD7), .O8(OD8), .O9(OD9),
    .O10(OD10), .O11(OD11), .O12(OD12), .O13(OD13), .O14(OD14), .O15(OD15), .IN0_0(datreg_v1_1_1_do0),
    .IN0_1(datreg_v1_1_1_do1), .IN0_2(datreg_v1_1_1_do2), .IN0_3(datreg_v1_1_1_do3),
    .IN0_4(datreg_v1_1_1_do4), .IN0_5(datreg_v1_1_1_do5), .IN0_6(datreg_v1_1_1_do6),
    .IN0_7(datreg_v1_1_1_do7), .IN0_8(datreg_v1_1_1_do8), .IN0_9(datreg_v1_1_1_do9),
    .IN0_10(datreg_v1_1_1_do10), .IN0_11(datreg_v1_1_1_do11), .IN0_12(datreg_v1_1_1_do12),
    .IN0_13(datreg_v1_1_1_do13), .IN0_14(datreg_v1_1_1_do14), .IN0_15(datreg_v1_1_1_do15),
    .IN1_0(datreg_v1_1_2_do0), .IN1_1(datreg_v1_1_2_do1), .IN1_2(datreg_v1_1_2_do2),
    .IN1_3(datreg_v1_1_2_do3), .IN1_4(datreg_v1_1_2_do4), .IN1_5(datreg_v1_1_2_do5),
    .IN1_6(datreg_v1_1_2_do6), .IN1_7(datreg_v1_1_2_do7), .IN1_8(datreg_v1_1_2_do8),
    .IN1_9(datreg_v1_1_2_do9), .IN1_10(datreg_v1_1_2_do10), .IN1_11(datreg_v1_1_2_do11),
    .IN1_12(datreg_v1_1_2_do12), .IN1_13(datreg_v1_1_2_do13), .IN1_14(datreg_v1_1_2_do14),
    .IN1_15(datreg_v1_1_2_do15), .IN2_0(datreg_v1_1_3_do0), .IN2_1(datreg_v1_1_3_do1),
    .IN2_2(datreg_v1_1_3_do2), .IN2_3(datreg_v1_1_3_do3), .IN2_4(datreg_v1_1_3_do4),
    .IN2_5(datreg_v1_1_3_do5), .IN2_6(datreg_v1_1_3_do6), .IN2_7(datreg_v1_1_3_do7),
    .IN2_8(datreg_v1_1_3_do8), .IN2_9(datreg_v1_1_3_do9), .IN2_10(datreg_v1_1_3_do10),
    .IN2_11(datreg_v1_1_3_do11), .IN2_12(datreg_v1_1_3_do12), .IN2_13(datreg_v1_1_3_do13),
    .IN2_14(datreg_v1_1_3_do14), .IN2_15(datreg_v1_1_3_do15), .IN3_0(datreg_v1_1_4_do0),
    .IN3_1(datreg_v1_1_4_do1), .IN3_2(datreg_v1_1_4_do2), .IN3_3(datreg_v1_1_4_do3),
    .IN3_4(datreg_v1_1_4_do4), .IN3_5(datreg_v1_1_4_do5), .IN3_6(datreg_v1_1_4_do6),
    .IN3_7(datreg_v1_1_4_do7), .IN3_8(datreg_v1_1_4_do8), .IN3_9(datreg_v1_1_4_do9),
    .IN3_10(datreg_v1_1_4_do10), .IN3_11(datreg_v1_1_4_do11), .IN3_12(datreg_v1_1_4_do12),
    .IN3_13(datreg_v1_1_4_do13), .IN3_14(datreg_v1_1_4_do14), .IN3_15(datreg_v1_1_4_do15), .S0(AD0),
    .S1(AD1), .EN(1'b1));
endmodule
