// Digital circuit 2x4 DEC V1.3.dig as structural Verilog
module _2x4_DEC_V1_3 (
  input  I0,
  input  EN,
  input  I1,
  output O0,
  output O1,
  output O2,
  output O3
);

  wire _1x2_dec_v1_3_1_o0, _1x2_dec_v1_3_1_o1;

  _1x2_DEC_V1_3 _1x2_dec_v1_3_1 (.O0(_1x2_dec_v1_3_1_o0), .O1(_1x2_dec_v1_3_1_o1), .EN(EN), .I0(I1));
  _1x2_DEC_V1_3 _1x2_dec_v1_3_2 (.O0(O0), .O1(O1), .EN(_1x2_dec_v1_3_1_o0), .I0(I0));
  _1x2_DEC_V1_3 _1x2_dec_v1_3_3 (.O0(O2), .O1(O3), .EN(_1x2_dec_v1_3_1_o1), .I0(I0));
endmodule
