// Digital circuit DATREG V1.1.dig as structural Verilog
module DATREG_V1_1 (
  input  RST,
  input  EN,
  input  DIN1,
  input  CLK,
  input  DIN2,
  input  DIN3,
  input  DIN4,
  input  DIN5,
  input  DIN6,
  input  DIN7,
  input  DIN8,
  input  DIN9,
  input  DIN10,
  input  DIN11,
  input  DIN12,
  input  DIN13,
  input  DIN14,
  input  DIN15,
  input  DIN16,
  output DO0,
  output DO1,
  output DO2,
  output DO3,
  output DO4,
  output DO5,
  output DO6,
  output DO7,
  output DO8,
  output DO9,
  output DO10,
  output DO11,
  output DO12,
  output DO13,
  output DO14,
  output DO15
);

  // _1_BIT_REG_V1_5 _1_bit_reg_v1_5_1: pin names not known; wires that end beside it: CLK, RST, EN, DIN1, DO0
  // _1_BIT_REG_V1_5 _1_bit_reg_v1_5_2: pin names not known; wires that end beside it: CLK, RST, EN, DIN3, DO2
  // _1_BIT_REG_V1_5 _1_bit_reg_v1_5_3: pin names not known; wires that end beside it: CLK, RST, EN, DIN5, DO4
  // _1_BIT_REG_V1_5 _1_bit_reg_v1_5_4: pin names not known; wires that end beside it: CLK, RST, EN, DIN7, DO6
  // _1_BIT_REG_V1_5 _1_bit_reg_v1_5_5: pin names not known; wires that end beside it: CLK, RST, EN, DIN9, DO8
  // _1_BIT_REG_V1_5 _1_bit_reg_v1_5_6: pin names not known; wires that end beside it: CLK, RST, EN, DIN11, DO10
  // _1_BIT_REG_V1_5 _1_bit_reg_v1_5_7: pin names not known; wires that end beside it: CLK, RST, EN, DIN13, DO12
  // _1_BIT_REG_V1_5 _1_bit_reg_v1_5_8: pin names not known; wires that end beside it: CLK, RST, EN, DIN15, DO14
  // _1_BIT_REG_V1_5 _1_bit_reg_v1_5_9: pin names not known; wires that end beside it: CLK, RST, EN, DIN2, DO1
  // _1_BIT_REG_V1_5 _1_bit_reg_v1_5_10: pin names not known; wires that end beside it: CLK, RST, EN, DIN4, DO3
  // _1_BIT_REG_V1_5 _1_bit_reg_v1_5_11: pin names not known; wires that end beside it: CLK, RST, EN, DIN6, DO5
  // _1_BIT_REG_V1_5 _1_bit_reg_v1_5_12: pin names not known; wires that end beside it: CLK, RST, EN, DIN8, DO7
  // _1_BIT_REG_V1_5 _1_bit_reg_v1_5_13: pin names not known; wires that end beside it: CLK, RST, EN, DIN10, DO9
  // _1_BIT_REG_V1_5 _1_bit_reg_v1_5_14: pin names not known; wires that end beside it: CLK, RST, EN, DIN12, DO11
  // _1_BIT_REG_V1_5 _1_bit_reg_v1_5_15: pin names not known; wires that end beside it: CLK, RST, EN, DIN14, DO13
  // _1_BIT_REG_V1_5 _1_bit_reg_v1_5_16: pin names not known; wires that end beside it: CLK, RST, EN, DIN16, DO15

  // Notes on the sheet:
  //   CLK: Hz: 10
endmodule
