// Digital circuit 16 ADDR MEM 24 BIT.dig as structural Verilog
module _16_ADDR_MEM_24_BIT (
  input  RST,
  input  WEN,
  input  CLK,
  input  AW15,
  input  AW0,
  input  AW1,
  input  AW2,
  input  AW3,
  input  AW4,
  input  AW5,
  input  AW6,
  input  AW7,
  input  AW8,
  input  AW9,
  input  AW10,
  input  AW11,
  input  AW12,
  input  AW13,
  input  AW14,
  input  I0,
  input  I1,
  input  I2,
  input  I3,
  input  I4,
  input  I5,
  input  I6,
  input  I7,
  input  I8,
  input  I9,
  input  I10,
  input  I11,
  input  I12,
  input  I13,
  input  I14,
  input  I15,
  input  I16,
  input  I17,
  input  I18,
  input  I19,
  input  I20,
  input  I21,
  input  I22,
  input  I23,
  input  AR0,
  input  AR1,
  input  AR2,
  input  AR3,
  input  AR4,
  input  AR5,
  input  AR6,
  input  AR7,
  input  AR8,
  input  AR9,
  input  AR10,
  input  AR11,
  input  AR12,
  input  AR13,
  input  AR14,
  input  AR15,
  output O0,
  output O1,
  output O2,
  output O3,
  output O4,
  output O5,
  output O6,
  output O7,
  output O8,
  output O9,
  output O10,
  output O11,
  output O12,
  output O13,
  output O14,
  output O15,
  output O16,
  output O17,
  output O18,
  output O19,
  output O20,
  output O21,
  output O22,
  output O23
);

  wire _1x2_dec_mem_1_p3, _1x2_dec_mem_1_p4, _15_addr_mem_24_bit_1_o0, _15_addr_mem_24_bit_1_o1,
       _15_addr_mem_24_bit_1_o2, _15_addr_mem_24_bit_1_o3, _15_addr_mem_24_bit_1_o4,
       _15_addr_mem_24_bit_1_o5, _15_addr_mem_24_bit_1_o6, _15_addr_mem_24_bit_1_o7,
       _15_addr_mem_24_bit_1_o8, _15_addr_mem_24_bit_1_o9, _15_addr_mem_24_bit_1_o10,
       _15_addr_mem_24_bit_1_o11, _15_addr_mem_24_bit_1_o12, _15_addr_mem_24_bit_1_o13,
       _15_addr_mem_24_bit_1_o14, _15_addr_mem_24_bit_1_o15, _15_addr_mem_24_bit_1_o16,
       _15_addr_mem_24_bit_1_o17, _15_addr_mem_24_bit_1_o18, _15_addr_mem_24_bit_1_o19,
       _15_addr_mem_24_bit_1_o20, _15_addr_mem_24_bit_1_o21, _15_addr_mem_24_bit_1_o22,
       _15_addr_mem_24_bit_1_o23, _15_addr_mem_24_bit_2_o0, _15_addr_mem_24_bit_2_o1,
       _15_addr_mem_24_bit_2_o2, _15_addr_mem_24_bit_2_o3, _15_addr_mem_24_bit_2_o4,
       _15_addr_mem_24_bit_2_o5, _15_addr_mem_24_bit_2_o6, _15_addr_mem_24_bit_2_o7,
       _15_addr_mem_24_bit_2_o8, _15_addr_mem_24_bit_2_o9, _15_addr_mem_24_bit_2_o10,
       _15_addr_mem_24_bit_2_o11, _15_addr_mem_24_bit_2_o12, _15_addr_mem_24_bit_2_o13,
       _15_addr_mem_24_bit_2_o14, _15_addr_mem_24_bit_2_o15, _15_addr_mem_24_bit_2_o16,
       _15_addr_mem_24_bit_2_o17, _15_addr_mem_24_bit_2_o18, _15_addr_mem_24_bit_2_o19,
       _15_addr_mem_24_bit_2_o20, _15_addr_mem_24_bit_2_o21, _15_addr_mem_24_bit_2_o22,
       _15_addr_mem_24_bit_2_o23, not_1_out;

  not not_1 (not_1_out, AR15);
  _2X1_MUX_24_BIT_V1 _2x1_mux_24_bit_v1_1 (
    .IN0_0(_15_addr_mem_24_bit_2_o0), .IN0_1(_15_addr_mem_24_bit_2_o1), .IN0_2(_15_addr_mem_24_bit_2_o2),
    .IN0_3(_15_addr_mem_24_bit_2_o3), .IN0_4(_15_addr_mem_24_bit_2_o4), .IN0_5(_15_addr_mem_24_bit_2_o5),
    .IN0_6(_15_addr_mem_24_bit_2_o6), .IN0_7(_15_addr_mem_24_bit_2_o7), .IN0_8(_15_addr_mem_24_bit_2_o8),
    .IN0_9(_15_addr_mem_24_bit_2_o9), .IN0_10(_15_addr_mem_24_bit_2_o10), .IN0_11(_15_addr_mem_24_bit_2_o11),
    .IN0_12(_15_addr_mem_24_bit_2_o12), .IN0_13(_15_addr_mem_24_bit_2_o13),
    .IN0_14(_15_addr_mem_24_bit_2_o14), .IN0_15(_15_addr_mem_24_bit_2_o15),
    .IN0_16(_15_addr_mem_24_bit_2_o16), .IN0_17(_15_addr_mem_24_bit_2_o17),
    .IN0_18(_15_addr_mem_24_bit_2_o18), .IN0_19(_15_addr_mem_24_bit_2_o19),
    .IN0_20(_15_addr_mem_24_bit_2_o20), .IN0_21(_15_addr_mem_24_bit_2_o21),
    .IN0_22(_15_addr_mem_24_bit_2_o22), .IN0_23(_15_addr_mem_24_bit_2_o23), .IN1_0(_15_addr_mem_24_bit_1_o0),
    .IN1_1(_15_addr_mem_24_bit_1_o1), .IN1_2(_15_addr_mem_24_bit_1_o2), .IN1_3(_15_addr_mem_24_bit_1_o3),
    .IN1_4(_15_addr_mem_24_bit_1_o4), .IN1_5(_15_addr_mem_24_bit_1_o5), .IN1_6(_15_addr_mem_24_bit_1_o6),
    .IN1_7(_15_addr_mem_24_bit_1_o7), .IN1_8(_15_addr_mem_24_bit_1_o8), .IN1_9(_15_addr_mem_24_bit_1_o9),
    .IN1_10(_15_addr_mem_24_bit_1_o10), .IN1_11(_15_addr_mem_24_bit_1_o11),
    .IN1_12(_15_addr_mem_24_bit_1_o12), .IN1_13(_15_addr_mem_24_bit_1_o13),
    .IN1_14(_15_addr_mem_24_bit_1_o14), .IN1_15(_15_addr_mem_24_bit_1_o15),
    .IN1_16(_15_addr_mem_24_bit_1_o16), .IN1_17(_15_addr_mem_24_bit_1_o17),
    .IN1_18(_15_addr_mem_24_bit_1_o18), .IN1_19(_15_addr_mem_24_bit_1_o19),
    .IN1_20(_15_addr_mem_24_bit_1_o20), .IN1_21(_15_addr_mem_24_bit_1_o21),
    .IN1_22(_15_addr_mem_24_bit_1_o22), .IN1_23(_15_addr_mem_24_bit_1_o23), .S0(not_1_out), .EN(1'b1),
    .O0(O0), .O1(O1), .O2(O2), .O3(O3), .O4(O4), .O5(O5), .O6(O6), .O7(O7), .O8(O8), .O9(O9), .O10(O10),
    .O11(O11), .O12(O12), .O13(O13), .O14(O14), .O15(O15), .O16(O16), .O17(O17), .O18(O18), .O19(O19),
    .O20(O20), .O21(O21), .O22(O22), .O23(O23));
  // _1x2_DEC_MEM _1x2_dec_mem_1: pin names not known; wires that end beside it: AW15, WEN, _1x2_dec_mem_1_p3, _1x2_dec_mem_1_p4
  _15_ADDR_MEM_24_BIT _15_addr_mem_24_bit_1 (
    .CLK(CLK), .RST(RST), .WEN(_1x2_dec_mem_1_p3), .AW0(AW0), .AW1(AW1), .AW2(AW2), .AW3(AW3), .AW4(AW4),
    .AW5(AW5), .AW6(AW6), .AW7(AW7), .AW8(AW8), .AW9(AW9), .AW10(AW10), .AW11(AW11), .AW12(AW12),
    .AW13(AW13), .AW14(AW14), .I0(I0), .I1(I1), .I2(I2), .I3(I3), .I4(I4), .I5(I5), .I6(I6), .I7(I7),
    .I8(I8), .I9(I9), .I10(I10), .I11(I11), .I12(I12), .I13(I13), .I14(I14), .I15(I15), .I16(I16), .I17(I17),
    .I18(I18), .I19(I19), .I20(I20), .I21(I21), .I22(I22), .I23(I23), .AR0(AR0), .AR1(AR1), .AR2(AR2),
    .AR3(AR3), .AR4(AR4), .AR5(AR5), .AR6(AR6), .AR7(AR7), .AR8(AR8), .AR9(AR9), .AR10(AR10), .AR11(AR11),
    .AR12(AR12), .AR13(AR13), .AR14(AR14), .O0(_15_addr_mem_24_bit_1_o0), .O1(_15_addr_mem_24_bit_1_o1),
    .O2(_15_addr_mem_24_bit_1_o2), .O3(_15_addr_mem_24_bit_1_o3), .O4(_15_addr_mem_24_bit_1_o4),
    .O5(_15_addr_mem_24_bit_1_o5), .O6(_15_addr_mem_24_bit_1_o6), .O7(_15_addr_mem_24_bit_1_o7),
    .O8(_15_addr_mem_24_bit_1_o8), .O9(_15_addr_mem_24_bit_1_o9), .O10(_15_addr_mem_24_bit_1_o10),
    .O11(_15_addr_mem_24_bit_1_o11), .O12(_15_addr_mem_24_bit_1_o12), .O13(_15_addr_mem_24_bit_1_o13),
    .O14(_15_addr_mem_24_bit_1_o14), .O15(_15_addr_mem_24_bit_1_o15), .O16(_15_addr_mem_24_bit_1_o16),
    .O17(_15_addr_mem_24_bit_1_o17), .O18(_15_addr_mem_24_bit_1_o18), .O19(_15_addr_mem_24_bit_1_o19),
    .O20(_15_addr_mem_24_bit_1_o20), .O21(_15_addr_mem_24_bit_1_o21), .O22(_15_addr_mem_24_bit_1_o22),
    .O23(_15_addr_mem_24_bit_1_o23));
  _15_ADDR_MEM_24_BIT _15_addr_mem_24_bit_2 (
    .CLK(CLK), .RST(RST), .WEN(_1x2_dec_mem_1_p4), .AW0(AW0), .AW1(AW1), .AW2(AW2), .AW3(AW3), .AW4(AW4),
    .AW5(AW5), .AW6(AW6), .AW7(AW7), .AW8(AW8), .AW9(AW9), .AW10(AW10), .AW11(AW11), .AW12(AW12),
    .AW13(AW13), .AW14(AW14), .I0(I0), .I1(I1), .I2(I2), .I3(I3), .I4(I4), .I5(I5), .I6(I6), .I7(I7),
    .I8(I8), .I9(I9), .I10(I10), .I11(I11), .I12(I12), .I13(I13), .I14(I14), .I15(I15), .I16(I16), .I17(I17),
    .I18(I18), .I19(I19), .I20(I20), .I21(I21), .I22(I22), .I23(I23), .AR0(AR0), .AR1(AR1), .AR2(AR2),
    .AR3(AR3), .AR4(AR4), .AR5(AR5), .AR6(AR6), .AR7(AR7), .AR8(AR8), .AR9(AR9), .AR10(AR10), .AR11(AR11),
    .AR12(AR12), .AR13(AR13), .AR14(AR14), .O0(_15_addr_mem_24_bit_2_o0), .O1(_15_addr_mem_24_bit_2_o1),
    .O2(_15_addr_mem_24_bit_2_o2), .O3(_15_addr_mem_24_bit_2_o3), .O4(_15_addr_mem_24_bit_2_o4),
    .O5(_15_addr_mem_24_bit_2_o5), .O6(_15_addr_mem_24_bit_2_o6), .O7(_15_addr_mem_24_bit_2_o7),
    .O8(_15_addr_mem_24_bit_2_o8), .O9(_15_addr_mem_24_bit_2_o9), .O10(_15_addr_mem_24_bit_2_o10),
    .O11(_15_addr_mem_24_bit_2_o11), .O12(_15_addr_mem_24_bit_2_o12), .O13(_15_addr_mem_24_bit_2_o13),
    .O14(_15_addr_mem_24_bit_2_o14), .O15(_15_addr_mem_24_bit_2_o15), .O16(_15_addr_mem_24_bit_2_o16),
    .O17(_15_addr_mem_24_bit_2_o17), .O18(_15_addr_mem_24_bit_2_o18), .O19(_15_addr_mem_24_bit_2_o19),
    .O20(_15_addr_mem_24_bit_2_o20), .O21(_15_addr_mem_24_bit_2_o21), .O22(_15_addr_mem_24_bit_2_o22),
    .O23(_15_addr_mem_24_bit_2_o23));

  // Notes on the sheet:
  //   CLK: Hz: 200
endmodule
