// Digital circuit 2 ADDR MEM 24 BIT.dig as structural Verilog
module _2_ADDR_MEM_24_BIT (
  input  I0,
  input  I1,
  input  I2,
  input  I3,
  input  I4,
  input  I5,
  input  I6,
  input  I7,
  input  I8,
  input  I9,
  input  I10,
  input  I11,
  input  I12,
  input  I13,
  input  I14,
  input  I15,
  input  AW0,
  input  AW1,
  input  RST,
  input  I16,
  input  I17,
  input  I18,
  input  I19,
  input  I20,
  input  I21,
  input  I22,
  input  I23,
  input  AR0,
  input  AR1,
  input  WEN,
  input  CLK,
  output O0,
  output O1,
  output O2,
  output O3,
  output O4,
  output O5,
  output O6,
  output O7,
  output O8,
  output O9,
  output O10,
  output O11,
  output O12,
  output O13,
  output O14,
  output O15,
  output O16,
  output O17,
  output O18,
  output O19,
  output O20,
  output O21,
  output O22,
  output O23
);

  wire _2x1_mux_24_bit_v1_1_o0, _2x1_mux_24_bit_v1_1_o1, _2x1_mux_24_bit_v1_1_o2, _2x1_mux_24_bit_v1_1_o3,
       _2x1_mux_24_bit_v1_1_o4, _2x1_mux_24_bit_v1_1_o5, _2x1_mux_24_bit_v1_1_o6, _2x1_mux_24_bit_v1_1_o7,
       _2x1_mux_24_bit_v1_1_o8, _2x1_mux_24_bit_v1_1_o9, _2x1_mux_24_bit_v1_1_o10, _2x1_mux_24_bit_v1_1_o11,
       _2x1_mux_24_bit_v1_1_o12, _2x1_mux_24_bit_v1_1_o13, _2x1_mux_24_bit_v1_1_o14,
       _2x1_mux_24_bit_v1_1_o15, _2x1_mux_24_bit_v1_1_o16, _2x1_mux_24_bit_v1_1_o17,
       _2x1_mux_24_bit_v1_1_o18, _2x1_mux_24_bit_v1_1_o19, _2x1_mux_24_bit_v1_1_o20,
       _2x1_mux_24_bit_v1_1_o21, _2x1_mux_24_bit_v1_1_o22, _2x1_mux_24_bit_v1_1_o23, _2x1_mux_24_bit_v1_2_o0,
       _2x1_mux_24_bit_v1_2_o1, _2x1_mux_24_bit_v1_2_o2, _2x1_mux_24_bit_v1_2_o3, _2x1_mux_24_bit_v1_2_o4,
       _2x1_mux_24_bit_v1_2_o5, _2x1_mux_24_bit_v1_2_o6, _2x1_mux_24_bit_v1_2_o7, _2x1_mux_24_bit_v1_2_o8,
       _2x1_mux_24_bit_v1_2_o9, _2x1_mux_24_bit_v1_2_o10, _2x1_mux_24_bit_v1_2_o11, _2x1_mux_24_bit_v1_2_o12,
       _2x1_mux_24_bit_v1_2_o13, _2x1_mux_24_bit_v1_2_o14, _2x1_mux_24_bit_v1_2_o15,
       _2x1_mux_24_bit_v1_2_o16, _2x1_mux_24_bit_v1_2_o17, _2x1_mux_24_bit_v1_2_o18,
       _2x1_mux_24_bit_v1_2_o19, _2x1_mux_24_bit_v1_2_o20, _2x1_mux_24_bit_v1_2_o21,
       _2x1_mux_24_bit_v1_2_o22, _2x1_mux_24_bit_v1_2_o23, _2x4_dec_mem_1_o0, _2x4_dec_mem_1_o1,
       _2x4_dec_mem_1_o2, _2x4_dec_mem_1_o3, _24_bit_instruction_reg_1_do0, _24_bit_instruction_reg_1_do1,
       _24_bit_instruction_reg_1_do2, _24_bit_instruction_reg_1_do3, _24_bit_instruction_reg_1_do4,
       _24_bit_instruction_reg_1_do5, _24_bit_instruction_reg_1_do6, _24_bit_instruction_reg_1_do7,
       _24_bit_instruction_reg_1_do8, _24_bit_instruction_reg_1_do9, _24_bit_instruction_reg_1_do10,
       _24_bit_instruction_reg_1_do11, _24_bit_instruction_reg_1_do12, _24_bit_instruction_reg_1_do13,
       _24_bit_instruction_reg_1_do14, _24_bit_instruction_reg_1_do15, _24_bit_instruction_reg_1_do16,
       _24_bit_instruction_reg_1_do17, _24_bit_instruction_reg_1_do18, _24_bit_instruction_reg_1_do19,
       _24_bit_instruction_reg_1_do20, _24_bit_instruction_reg_1_do21, _24_bit_instruction_reg_1_do22,
       _24_bit_instruction_reg_1_do23, _24_bit_instruction_reg_2_do0, _24_bit_instruction_reg_2_do1,
       _24_bit_instruction_reg_2_do2, _24_bit_instruction_reg_2_do3, _24_bit_instruction_reg_2_do4,
       _24_bit_instruction_reg_2_do5, _24_bit_instruction_reg_2_do6, _24_bit_instruction_reg_2_do7,
       _24_bit_instruction_reg_2_do8, _24_bit_instruction_reg_2_do9, _24_bit_instruction_reg_2_do10,
       _24_bit_instruction_reg_2_do11, _24_bit_instruction_reg_2_do12, _24_bit_instruction_reg_2_do13,
       _24_bit_instruction_reg_2_do14, _24_bit_instruction_reg_2_do15, _24_bit_instruction_reg_2_do16,
       _24_bit_instruction_reg_2_do17, _24_bit_instruction_reg_2_do18, _24_bit_instruction_reg_2_do19,
       _24_bit_instruction_reg_2_do20, _24_bit_instruction_reg_2_do21, _24_bit_instruction_reg_2_do22,
       _24_bit_instruction_reg_2_do23, _24_bit_instruction_reg_3_do0, _24_bit_instruction_reg_3_do1,
       _24_bit_instruction_reg_3_do2, _24_bit_instruction_reg_3_do3, _24_bit_instruction_reg_3_do4,
       _24_bit_instruction_reg_3_do5, _24_bit_instruction_reg_3_do6, _24_bit_instruction_reg_3_do7,
       _24_bit_instruction_reg_3_do8, _24_bit_instruction_reg_3_do9, _24_bit_instruction_reg_3_do10,
       _24_bit_instruction_reg_3_do11, _24_bit_instruction_reg_3_do12, _24_bit_instruction_reg_3_do13,
       _24_bit_instruction_reg_3_do14, _24_bit_instruction_reg_3_do15, _24_bit_instruction_reg_3_do16,
       _24_bit_instruction_reg_3_do17, _24_bit_instruction_reg_3_do18, _24_bit_instruction_reg_3_do19,
       _24_bit_instruction_reg_3_do20, _24_bit_instruction_reg_3_do21, _24_bit_instruction_reg_3_do22,
       _24_bit_instruction_reg_3_do23, _24_bit_instruction_reg_4_do0, _24_bit_instruction_reg_4_do1,
       _24_bit_instruction_reg_4_do2, _24_bit_instruction_reg_4_do3, _24_bit_instruction_reg_4_do4,
       _24_bit_instruction_reg_4_do5, _24_bit_instruction_reg_4_do6, _24_bit_instruction_reg_4_do7,
       _24_bit_instruction_reg_4_do8, _24_bit_instruction_reg_4_do9, _24_bit_instruction_reg_4_do10,
       _24_bit_instruction_reg_4_do11, _24_bit_instruction_reg_4_do12, _24_bit_instruction_reg_4_do13,
       _24_bit_instruction_reg_4_do14, _24_bit_instruction_reg_4_do15, _24_bit_instruction_reg_4_do16,
       _24_bit_instruction_reg_4_do17, _24_bit_instruction_reg_4_do18, _24_bit_instruction_reg_4_do19,
       _24_bit_instruction_reg_4_do20, _24_bit_instruction_reg_4_do21, _24_bit_instruction_reg_4_do22,
       _24_bit_instruction_reg_4_do23;

  _2x4_DEC_MEM _2x4_dec_mem_1 (
    .EN(WEN), .I0(AW0), .I1(AW1), .O0(_2x4_dec_mem_1_o0), .O1(_2x4_dec_mem_1_o1), .O2(_2x4_dec_mem_1_o2),
    .O3(_2x4_dec_mem_1_o3));
  _24_BIT_INSTRUCTION_REG _24_bit_instruction_reg_1 (
    .DIN0(I0), .DIN1(I1), .DIN2(I2), .DIN3(I3), .DIN4(I4), .DIN5(I5), .DIN6(I6), .DIN7(I7), .DIN8(I8),
    .DIN9(I9), .DIN10(I10), .DIN11(I11), .DIN12(I12), .DIN13(I13), .DIN14(I14), .DIN15(I15), .DIN16(I16),
    .DIN17(I17), .DIN18(I18), .DIN19(I19), .DIN20(I20), .DIN21(I21), .DIN22(I22), .DIN23(I23), .CLK(CLK),
    .RST(RST), .EN(_2x4_dec_mem_1_o0), .DO0(_24_bit_instruction_reg_1_do0),
    .DO1(_24_bit_instruction_reg_1_do1), .DO2(_24_bit_instruction_reg_1_do2),
    .DO3(_24_bit_instruction_reg_1_do3), .DO4(_24_bit_instruction_reg_1_do4),
    .DO5(_24_bit_instruction_reg_1_do5), .DO6(_24_bit_instruction_reg_1_do6),
    .DO7(_24_bit_instruction_reg_1_do7), .DO8(_24_bit_instruction_reg_1_do8),
    .DO9(_24_bit_instruction_reg_1_do9), .DO10(_24_bit_instruction_reg_1_do10),
    .DO11(_24_bit_instruction_reg_1_do11), .DO12(_24_bit_instruction_reg_1_do12),
    .DO13(_24_bit_instruction_reg_1_do13), .DO14(_24_bit_instruction_reg_1_do14),
    .DO15(_24_bit_instruction_reg_1_do15), .DO16(_24_bit_instruction_reg_1_do16),
    .DO17(_24_bit_instruction_reg_1_do17), .DO18(_24_bit_instruction_reg_1_do18),
    .DO19(_24_bit_instruction_reg_1_do19), .DO20(_24_bit_instruction_reg_1_do20),
    .DO21(_24_bit_instruction_reg_1_do21), .DO22(_24_bit_instruction_reg_1_do22),
    .DO23(_24_bit_instruction_reg_1_do23));
  _24_BIT_INSTRUCTION_REG _24_bit_instruction_reg_2 (
    .DIN0(I0), .DIN1(I1), .DIN2(I2), .DIN3(I3), .DIN4(I4), .DIN5(I5), .DIN6(I6), .DIN7(I7), .DIN8(I8),
    .DIN9(I9), .DIN10(I10), .DIN11(I11), .DIN12(I12), .DIN13(I13), .DIN14(I14), .DIN15(I15), .DIN16(I16),
    .DIN17(I17), .DIN18(I18), .DIN19(I19), .DIN20(I20), .DIN21(I21), .DIN22(I22), .DIN23(I23), .CLK(CLK),
    .RST(RST), .EN(_2x4_dec_mem_1_o1), .DO0(_24_bit_instruction_reg_2_do0),
    .DO1(_24_bit_instruction_reg_2_do1), .DO2(_24_bit_instruction_reg_2_do2),
    .DO3(_24_bit_instruction_reg_2_do3), .DO4(_24_bit_instruction_reg_2_do4),
    .DO5(_24_bit_instruction_reg_2_do5), .DO6(_24_bit_instruction_reg_2_do6),
    .DO7(_24_bit_instruction_reg_2_do7), .DO8(_24_bit_instruction_reg_2_do8),
    .DO9(_24_bit_instruction_reg_2_do9), .DO10(_24_bit_instruction_reg_2_do10),
    .DO11(_24_bit_instruction_reg_2_do11), .DO12(_24_bit_instruction_reg_2_do12),
    .DO13(_24_bit_instruction_reg_2_do13), .DO14(_24_bit_instruction_reg_2_do14),
    .DO15(_24_bit_instruction_reg_2_do15), .DO16(_24_bit_instruction_reg_2_do16),
    .DO17(_24_bit_instruction_reg_2_do17), .DO18(_24_bit_instruction_reg_2_do18),
    .DO19(_24_bit_instruction_reg_2_do19), .DO20(_24_bit_instruction_reg_2_do20),
    .DO21(_24_bit_instruction_reg_2_do21), .DO22(_24_bit_instruction_reg_2_do22),
    .DO23(_24_bit_instruction_reg_2_do23));
  _24_BIT_INSTRUCTION_REG _24_bit_instruction_reg_3 (
    .DIN0(I0), .DIN1(I1), .DIN2(I2), .DIN3(I3), .DIN4(I4), .DIN5(I5), .DIN6(I6), .DIN7(I7), .DIN8(I8),
    .DIN9(I9), .DIN10(I10), .DIN11(I11), .DIN12(I12), .DIN13(I13), .DIN14(I14), .DIN15(I15), .DIN16(I16),
    .DIN17(I17), .DIN18(I18), .DIN19(I19), .DIN20(I20), .DIN21(I21), .DIN22(I22), .DIN23(I23), .CLK(CLK),
    .RST(RST), .EN(_2x4_dec_mem_1_o2), .DO0(_24_bit_instruction_reg_3_do0),
    .DO1(_24_bit_instruction_reg_3_do1), .DO2(_24_bit_instruction_reg_3_do2),
    .DO3(_24_bit_instruction_reg_3_do3), .DO4(_24_bit_instruction_reg_3_do4),
    .DO5(_24_bit_instruction_reg_3_do5), .DO6(_24_bit_instruction_reg_3_do6),
    .DO7(_24_bit_instruction_reg_3_do7), .DO8(_24_bit_instruction_reg_3_do8),
    .DO9(_24_bit_instruction_reg_3_do9), .DO10(_24_bit_instruction_reg_3_do10),
    .DO11(_24_bit_instruction_reg_3_do11), .DO12(_24_bit_instruction_reg_3_do12),
    .DO13(_24_bit_instruction_reg_3_do13), .DO14(_24_bit_instruction_reg_3_do14),
    .DO15(_24_bit_instruction_reg_3_do15), .DO16(_24_bit_instruction_reg_3_do16),
    .DO17(_24_bit_instruction_reg_3_do17), .DO18(_24_bit_instruction_reg_3_do18),
    .DO19(_24_bit_instruction_reg_3_do19), .DO20(_24_bit_instruction_reg_3_do20),
    .DO21(_24_bit_instruction_reg_3_do21), .DO22(_24_bit_instruction_reg_3_do22),
    .DO23(_24_bit_instruction_reg_3_do23));
  _24_BIT_INSTRUCTION_REG _24_bit_instruction_reg_4 (
    .DIN0(I0), .DIN1(I1), .DIN2(I2), .DIN3(I3), .DIN4(I4), .DIN5(I5), .DIN6(I6), .DIN7(I7), .DIN8(I8),
    .DIN9(I9), .DIN10(I10), .DIN11(I11), .DIN12(I12), .DIN13(I13), .DIN14(I14), .DIN15(I15), .DIN16(I16),
    .DIN17(I17), .DIN18(I18), .DIN19(I19), .DIN20(I20), .DIN21(I21), .DIN22(I22), .DIN23(I23), .CLK(CLK),
    .RST(RST), .EN(_2x4_dec_mem_1_o3), .DO0(_24_bit_instruction_reg_4_do0),
    .DO1(_24_bit_instruction_reg_4_do1), .DO2(_24_bit_instruction_reg_4_do2),
    .DO3(_24_bit_instruction_reg_4_do3), .DO4(_24_bit_instruction_reg_4_do4),
    .DO5(_24_bit_instruction_reg_4_do5), .DO6(_24_bit_instruction_reg_4_do6),
    .DO7(_24_bit_instruction_reg_4_do7), .DO8(_24_bit_instruction_reg_4_do8),
    .DO9(_24_bit_instruction_reg_4_do9), .DO10(_24_bit_instruction_reg_4_do10),
    .DO11(_24_bit_instruction_reg_4_do11), .DO12(_24_bit_instruction_reg_4_do12),
    .DO13(_24_bit_instruction_reg_4_do13), .DO14(_24_bit_instruction_reg_4_do14),
    .DO15(_24_bit_instruction_reg_4_do15), .DO16(_24_bit_instruction_reg_4_do16),
    .DO17(_24_bit_instruction_reg_4_do17), .DO18(_24_bit_instruction_reg_4_do18),
    .DO19(_24_bit_instruction_reg_4_do19), .DO20(_24_bit_instruction_reg_4_do20),
    .DO21(_24_bit_instruction_reg_4_do21), .DO22(_24_bit_instruction_reg_4_do22),
    .DO23(_24_bit_instruction_reg_4_do23));
  _2X1_MUX_24_BIT_V1 _2x1_mux_24_bit_v1_1 (
    .IN0_0(_24_bit_instruction_reg_1_do0), .IN0_1(_24_bit_instruction_reg_1_do1),
    .IN0_2(_24_bit_instruction_reg_1_do2), .IN0_3(_24_bit_instruction_reg_1_do3),
    .IN0_4(_24_bit_instruction_reg_1_do4), .IN0_5(_24_bit_instruction_reg_1_do5),
    .IN0_6(_24_bit_instruction_reg_1_do6), .IN0_7(_24_bit_instruction_reg_1_do7),
    .IN0_8(_24_bit_instruction_reg_1_do8), .IN0_9(_24_bit_instruction_reg_1_do9),
    .IN0_10(_24_bit_instruction_reg_1_do10), .IN0_11(_24_bit_instruction_reg_1_do11),
    .IN0_12(_24_bit_instruction_reg_1_do12), .IN0_13(_24_bit_instruction_reg_1_do13),
    .IN0_14(_24_bit_instruction_reg_1_do14), .IN0_15(_24_bit_instruction_reg_1_do15),
    .IN0_16(_24_bit_instruction_reg_1_do16), .IN0_17(_24_bit_instruction_reg_1_do17),
    .IN0_18(_24_bit_instruction_reg_1_do18), .IN0_19(_24_bit_instruction_reg_1_do19),
    .IN0_20(_24_bit_instruction_reg_1_do20), .IN0_21(_24_bit_instruction_reg_1_do21),
    .IN0_22(_24_bit_instruction_reg_1_do22), .IN0_23(_24_bit_instruction_reg_1_do23),
    .IN1_0(_24_bit_instruction_reg_2_do0), .IN1_1(_24_bit_instruction_reg_2_do1),
    .IN1_2(_24_bit_instruction_reg_2_do2), .IN1_3(_24_bit_instruction_reg_2_do3),
    .IN1_4(_24_bit_instruction_reg_2_do4), .IN1_5(_24_bit_instruction_reg_2_do5),
    .IN1_6(_24_bit_instruction_reg_2_do6), .IN1_7(_24_bit_instruction_reg_2_do7),
    .IN1_8(_24_bit_instruction_reg_2_do8), .IN1_9(_24_bit_instruction_reg_2_do9),
    .IN1_10(_24_bit_instruction_reg_2_do10), .IN1_11(_24_bit_instruction_reg_2_do11),
    .IN1_12(_24_bit_instruction_reg_2_do12), .IN1_13(_24_bit_instruction_reg_2_do13),
    .IN1_14(_24_bit_instruction_reg_2_do14), .IN1_15(_24_bit_instruction_reg_2_do15),
    .IN1_16(_24_bit_instruction_reg_2_do16), .IN1_17(_24_bit_instruction_reg_2_do17),
    .IN1_18(_24_bit_instruction_reg_2_do18), .IN1_19(_24_bit_instruction_reg_2_do19),
    .IN1_20(_24_bit_instruction_reg_2_do20), .IN1_21(_24_bit_instruction_reg_2_do21),
    .IN1_22(_24_bit_instruction_reg_2_do22), .IN1_23(_24_bit_instruction_reg_2_do23), .S0(AR0), .EN(1'b1),
    .O0(_2x1_mux_24_bit_v1_1_o0), .O1(_2x1_mux_24_bit_v1_1_o1), .O2(_2x1_mux_24_bit_v1_1_o2),
    .O3(_2x1_mux_24_bit_v1_1_o3), .O4(_2x1_mux_24_bit_v1_1_o4), .O5(_2x1_mux_24_bit_v1_1_o5),
    .O6(_2x1_mux_24_bit_v1_1_o6), .O7(_2x1_mux_24_bit_v1_1_o7), .O8(_2x1_mux_24_bit_v1_1_o8),
    .O9(_2x1_mux_24_bit_v1_1_o9), .O10(_2x1_mux_24_bit_v1_1_o10), .O11(_2x1_mux_24_bit_v1_1_o11),
    .O12(_2x1_mux_24_bit_v1_1_o12), .O13(_2x1_mux_24_bit_v1_1_o13), .O14(_2x1_mux_24_bit_v1_1_o14),
    .O15(_2x1_mux_24_bit_v1_1_o15), .O16(_2x1_mux_24_bit_v1_1_o16), .O17(_2x1_mux_24_bit_v1_1_o17),
    .O18(_2x1_mux_24_bit_v1_1_o18), .O19(_2x1_mux_24_bit_v1_1_o19), .O20(_2x1_mux_24_bit_v1_1_o20),
    .O21(_2x1_mux_24_bit_v1_1_o21), .O22(_2x1_mux_24_bit_v1_1_o22), .O23(_2x1_mux_24_bit_v1_1_o23));
  _2X1_MUX_24_BIT_V1 _2x1_mux_24_bit_v1_2 (
    .IN0_0(_24_bit_instruction_reg_3_do0), .IN0_1(_24_bit_instruction_reg_3_do1),
    .IN0_2(_24_bit_instruction_reg_3_do2), .IN0_3(_24_bit_instruction_reg_3_do3),
    .IN0_4(_24_bit_instruction_reg_3_do4), .IN0_5(_24_bit_instruction_reg_3_do5),
    .IN0_6(_24_bit_instruction_reg_3_do6), .IN0_7(_24_bit_instruction_reg_3_do7),
    .IN0_8(_24_bit_instruction_reg_3_do8), .IN0_9(_24_bit_instruction_reg_3_do9),
    .IN0_10(_24_bit_instruction_reg_3_do10), .IN0_11(_24_bit_instruction_reg_3_do11),
    .IN0_12(_24_bit_instruction_reg_3_do12), .IN0_13(_24_bit_instruction_reg_3_do13),
    .IN0_14(_24_bit_instruction_reg_3_do14), .IN0_15(_24_bit_instruction_reg_3_do15),
    .IN0_16(_24_bit_instruction_reg_3_do16), .IN0_17(_24_bit_instruction_reg_3_do17),
    .IN0_18(_24_bit_instruction_reg_3_do18), .IN0_19(_24_bit_instruction_reg_3_do19),
    .IN0_20(_24_bit_instruction_reg_3_do20), .IN0_21(_24_bit_instruction_reg_3_do21),
    .IN0_22(_24_bit_instruction_reg_3_do22), .IN0_23(_24_bit_instruction_reg_3_do23),
    .IN1_0(_24_bit_instruction_reg_4_do0), .IN1_1(_24_bit_instruction_reg_4_do1),
    .IN1_2(_24_bit_instruction_reg_4_do2), .IN1_3(_24_bit_instruction_reg_4_do3),
    .IN1_4(_24_bit_instruction_reg_4_do4), .IN1_5(_24_bit_instruction_reg_4_do5),
    .IN1_6(_24_bit_instruction_reg_4_do6), .IN1_7(_24_bit_instruction_reg_4_do7),
    .IN1_8(_24_bit_instruction_reg_4_do8), .IN1_9(_24_bit_instruction_reg_4_do9),
    .IN1_10(_24_bit_instruction_reg_4_do10), .IN1_11(_24_bit_instruction_reg_4_do11),
    .IN1_12(_24_bit_instruction_reg_4_do12), .IN1_13(_24_bit_instruction_reg_4_do13),
    .IN1_14(_24_bit_instruction_reg_4_do14), .IN1_15(_24_bit_instruction_reg_4_do15),
    .IN1_16(_24_bit_instruction_reg_4_do16), .IN1_17(_24_bit_instruction_reg_4_do17),
    .IN1_18(_24_bit_instruction_reg_4_do18), .IN1_19(_24_bit_instruction_reg_4_do19),
    .IN1_20(_24_bit_instruction_reg_4_do20), .IN1_21(_24_bit_instruction_reg_4_do21),
    .IN1_22(_24_bit_instruction_reg_4_do22), .IN1_23(_24_bit_instruction_reg_4_do23), .S0(AR0), .EN(1'b1),
    .O0(_2x1_mux_24_bit_v1_2_o0), .O1(_2x1_mux_24_bit_v1_2_o1), .O2(_2x1_mux_24_bit_v1_2_o2),
    .O3(_2x1_mux_24_bit_v1_2_o3), .O4(_2x1_mux_24_bit_v1_2_o4), .O5(_2x1_mux_24_bit_v1_2_o5),
    .O6(_2x1_mux_24_bit_v1_2_o6), .O7(_2x1_mux_24_bit_v1_2_o7), .O8(_2x1_mux_24_bit_v1_2_o8),
    .O9(_2x1_mux_24_bit_v1_2_o9), .O10(_2x1_mux_24_bit_v1_2_o10), .O11(_2x1_mux_24_bit_v1_2_o11),
    .O12(_2x1_mux_24_bit_v1_2_o12), .O13(_2x1_mux_24_bit_v1_2_o13), .O14(_2x1_mux_24_bit_v1_2_o14),
    .O15(_2x1_mux_24_bit_v1_2_o15), .O16(_2x1_mux_24_bit_v1_2_o16), .O17(_2x1_mux_24_bit_v1_2_o17),
    .O18(_2x1_mux_24_bit_v1_2_o18), .O19(_2x1_mux_24_bit_v1_2_o19), .O20(_2x1_mux_24_bit_v1_2_o20),
    .O21(_2x1_mux_24_bit_v1_2_o21), .O22(_2x1_mux_24_bit_v1_2_o22), .O23(_2x1_mux_24_bit_v1_2_o23));
  _2X1_MUX_24_BIT_V1 _2x1_mux_24_bit_v1_3 (
    .IN0_0(_2x1_mux_24_bit_v1_1_o0), .IN0_1(_2x1_mux_24_bit_v1_1_o1), .IN0_2(_2x1_mux_24_bit_v1_1_o2),
    .IN0_3(_2x1_mux_24_bit_v1_1_o3), .IN0_4(_2x1_mux_24_bit_v1_1_o4), .IN0_5(_2x1_mux_24_bit_v1_1_o5),
    .IN0_6(_2x1_mux_24_bit_v1_1_o6), .IN0_7(_2x1_mux_24_bit_v1_1_o7), .IN0_8(_2x1_mux_24_bit_v1_1_o8),
    .IN0_9(_2x1_mux_24_bit_v1_1_o9), .IN0_10(_2x1_mux_24_bit_v1_1_o10), .IN0_11(_2x1_mux_24_bit_v1_1_o11),
    .IN0_12(_2x1_mux_24_bit_v1_1_o12), .IN0_13(_2x1_mux_24_bit_v1_1_o13), .IN0_14(_2x1_mux_24_bit_v1_1_o14),
    .IN0_15(_2x1_mux_24_bit_v1_1_o15), .IN0_16(_2x1_mux_24_bit_v1_1_o16), .IN0_17(_2x1_mux_24_bit_v1_1_o17),
    .IN0_18(_2x1_mux_24_bit_v1_1_o18), .IN0_19(_2x1_mux_24_bit_v1_1_o19), .IN0_20(_2x1_mux_24_bit_v1_1_o20),
    .IN0_21(_2x1_mux_24_bit_v1_1_o21), .IN0_22(_2x1_mux_24_bit_v1_1_o22), .IN0_23(_2x1_mux_24_bit_v1_1_o23),
    .IN1_0(_2x1_mux_24_bit_v1_2_o0), .IN1_1(_2x1_mux_24_bit_v1_2_o1), .IN1_2(_2x1_mux_24_bit_v1_2_o2),
    .IN1_3(_2x1_mux_24_bit_v1_2_o3), .IN1_4(_2x1_mux_24_bit_v1_2_o4), .IN1_5(_2x1_mux_24_bit_v1_2_o5),
    .IN1_6(_2x1_mux_24_bit_v1_2_o6), .IN1_7(_2x1_mux_24_bit_v1_2_o7), .IN1_8(_2x1_mux_24_bit_v1_2_o8),
    .IN1_9(_2x1_mux_24_bit_v1_2_o9), .IN1_10(_2x1_mux_24_bit_v1_2_o10), .IN1_11(_2x1_mux_24_bit_v1_2_o11),
    .IN1_12(_2x1_mux_24_bit_v1_2_o12), .IN1_13(_2x1_mux_24_bit_v1_2_o13), .IN1_14(_2x1_mux_24_bit_v1_2_o14),
    .IN1_15(_2x1_mux_24_bit_v1_2_o15), .IN1_16(_2x1_mux_24_bit_v1_2_o16), .IN1_17(_2x1_mux_24_bit_v1_2_o17),
    .IN1_18(_2x1_mux_24_bit_v1_2_o18), .IN1_19(_2x1_mux_24_bit_v1_2_o19), .IN1_20(_2x1_mux_24_bit_v1_2_o20),
    .IN1_21(_2x1_mux_24_bit_v1_2_o21), .IN1_22(_2x1_mux_24_bit_v1_2_o22), .IN1_23(_2x1_mux_24_bit_v1_2_o23),
    .S0(AR1), .EN(1'b1), .O0(O0), .O1(O1), .O2(O2), .O3(O3), .O4(O4), .O5(O5), .O6(O6), .O7(O7), .O8(O8),
    .O9(O9), .O10(O10), .O11(O11), .O12(O12), .O13(O13), .O14(O14), .O15(O15), .O16(O16), .O17(O17),
    .O18(O18), .O19(O19), .O20(O20), .O21(O21), .O22(O22), .O23(O23));

  // Notes on the sheet:
  //   CLK: Hz: 200
endmodule
