// Digital circuit 24 BIT INSTRUCTION REG.dig as structural Verilog
module _24_BIT_INSTRUCTION_REG (
  input  RST,
  input  EN,
  input  DIN0,
  input  CLK,
  input  DIN1,
  input  DIN2,
  input  DIN3,
  input  DIN4,
  input  DIN5,
  input  DIN6,
  input  DIN7,
  input  DIN8,
  input  DIN9,
  input  DIN10,
  input  DIN11,
  input  DIN12,
  input  DIN13,
  input  DIN14,
  input  DIN15,
  input  DIN16,
  input  DIN17,
  input  DIN18,
  input  DIN19,
  input  DIN20,
  input  DIN21,
  input  DIN22,
  input  DIN23,
  output DO0,
  output DO1,
  output DO2,
  output DO3,
  output DO4,
  output DO5,
  output DO6,
  output DO7,
  output DO8,
  output DO9,
  output DO10,
  output DO11,
  output DO12,
  output DO13,
  output DO14,
  output DO15,
  output DO16,
  output DO17,
  output DO18,
  output DO19,
  output DO20,
  output DO21,
  output DO22,
  output DO23
);

  // _1_BIT_REG_V1 B0: pin names not known; wires that end beside it: CLK, RST, EN, DIN0, DO0
  // _1_BIT_REG_V1 B1: pin names not known; wires that end beside it: CLK, RST, EN, DIN3, DO3
  // _1_BIT_REG_V1 B2: pin names not known; wires that end beside it: CLK, RST, EN, DIN6, DO6
  // _1_BIT_REG_V1 B3: pin names not known; wires that end beside it: CLK, RST, EN, DIN9, DO9
  // _1_BIT_REG_V1 B4: pin names not known; wires that end beside it: CLK, RST, EN, DIN12, DO12
  // _1_BIT_REG_V1 B5: pin names not known; wires that end beside it: CLK, RST, EN, DIN15, DO15
  // _1_BIT_REG_V1 B6: pin names not known; wires that end beside it: CLK, RST, EN, DIN18, DO18
  // _1_BIT_REG_V1 B7: pin names not known; wires that end beside it: CLK, RST, EN, DIN21, DO21
  // _1_BIT_REG_V1 B8: pin names not known; wires that end beside it: CLK, RST, EN, DIN1, DO1
  // _1_BIT_REG_V1 B9: pin names not known; wires that end beside it: CLK, RST, EN, DIN4, DO4
  // _1_BIT_REG_V1 B10: pin names not known; wires that end beside it: CLK, RST, EN, DIN7, DO7
  // _1_BIT_REG_V1 B11: pin names not known; wires that end beside it: CLK, RST, EN, DIN10, DO10
  // _1_BIT_REG_V1 B12: pin names not known; wires that end beside it: CLK, RST, EN, DIN13, DO13
  // _1_BIT_REG_V1 B13: pin names not known; wires that end beside it: CLK, RST, EN, DIN16, DO16
  // _1_BIT_REG_V1 B14: pin names not known; wires that end beside it: CLK, RST, EN, DIN19, DO19
  // _1_BIT_REG_V1 B15: pin names not known; wires that end beside it: CLK, RST, EN, DIN22, DO22
  // _1_BIT_REG_V1 B16: pin names not known; wires that end beside it: CLK, RST, EN, DIN2, DO2
  // _1_BIT_REG_V1 B17: pin names not known; wires that end beside it: CLK, RST, EN, DIN5, DO5
  // _1_BIT_REG_V1 B18: pin names not known; wires that end beside it: CLK, RST, EN, DIN8, DO8
  // _1_BIT_REG_V1 B19: pin names not known; wires that end beside it: CLK, RST, EN, DIN11, DO11
  // _1_BIT_REG_V1 B20: pin names not known; wires that end beside it: CLK, RST, EN, DIN14, DO14
  // _1_BIT_REG_V1 B21: pin names not known; wires that end beside it: CLK, RST, EN, DIN17, DO17
  // _1_BIT_REG_V1 B22: pin names not known; wires that end beside it: CLK, RST, EN, DIN20, DO20
  // _1_BIT_REG_V1 B23: pin names not known; wires that end beside it: CLK, RST, EN, DIN23, DO23

  // Notes on the sheet:
  //   CLK: Hz: 10
endmodule
