// Digital circuit 2x4 DEC MEM.dig as structural Verilog
module _2x4_DEC_MEM (
  input  I0,
  input  EN,
  input  I1,
  output O0,
  output O1,
  output O2,
  output O3
);

  wire _1x2_dec_mem_1_p3, _1x2_dec_mem_1_p4;

  // _1x2_DEC_MEM _1x2_dec_mem_1: pin names not known; wires that end beside it: EN, I1, _1x2_dec_mem_1_p3, _1x2_dec_mem_1_p4
  // _1x2_DEC_MEM _1x2_dec_mem_2: pin names not known; wires that end beside it: _1x2_dec_mem_1_p3, I0, O0, O1
  // _1x2_DEC_MEM _1x2_dec_mem_3: pin names not known; wires that end beside it: _1x2_dec_mem_1_p4, I0, O2, O3
endmodule
