// Digital circuit 2X1 MUX 24 BIT V1.dig as structural Verilog
module _2X1_MUX_24_BIT_V1 (
  input  IN0_0,
  input  IN0_1,
  input  IN0_2,
  input  IN0_3,
  input  IN0_4,
  input  IN0_5,
  input  IN0_6,
  input  IN0_7,
  input  IN0_8,
  input  IN0_9,
  input  IN0_10,
  input  IN0_11,
  input  IN0_12,
  input  IN0_13,
  input  IN0_14,
  input  IN0_15,
  input  IN1_0,
  input  IN1_1,
  input  IN1_2,
  input  IN1_3,
  input  IN1_4,
  input  IN1_5,
  input  IN1_6,
  input  IN1_7,
  input  IN1_8,
  input  IN1_9,
  input  IN1_10,
  input  IN1_11,
  input  IN1_12,
  input  IN1_13,
  input  IN1_14,
  input  IN1_15,
  input  S0,
  input  EN,
  input  IN1_16,
  input  IN1_17,
  input  IN1_18,
  input  IN1_19,
  input  IN1_20,
  input  IN1_21,
  input  IN1_22,
  input  IN1_23,
  input  IN0_16,
  input  IN0_17,
  input  IN0_18,
  input  IN0_19,
  input  IN0_20,
  input  IN0_21,
  input  IN0_22,
  input  IN0_23,
  output O0,
  output O1,
  output O2,
  output O3,
  output O4,
  output O5,
  output O6,
  output O7,
  output O8,
  output O9,
  output O10,
  output O11,
  output O12,
  output O13,
  output O14,
  output O15,
  output O16,
  output O17,
  output O18,
  output O19,
  output O20,
  output O21,
  output O22,
  output O23
);

  wire and_1_out, and_2_out, and_3_out, and_4_out, and_5_out, and_6_out, and_7_out, and_8_out, and_9_out,
       and_10_out, and_11_out, and_12_out, and_13_out, and_14_out, and_15_out, and_16_out, and_17_out,
       and_18_out, and_19_out, and_20_out, and_21_out, and_22_out, and_23_out, and_24_out, and_25_out,
       and_26_out, and_27_out, and_28_out, and_29_out, and_30_out, and_31_out, and_32_out, and_33_out,
       and_34_out, and_35_out, and_36_out, and_37_out, and_38_out, and_39_out, and_40_out, and_41_out,
       and_42_out, and_43_out, and_44_out, and_45_out, and_46_out, and_47_out, and_48_out, not_1_out,
       not_2_out, not_3_out, not_4_out, not_5_out, not_6_out, not_7_out, not_8_out, not_9_out, not_10_out,
       not_11_out, not_12_out, not_13_out, not_14_out, not_15_out, not_16_out, not_17_out, not_18_out,
       not_19_out, not_20_out, not_21_out, not_22_out, not_23_out, not_24_out, or_1_out, or_2_out, or_3_out,
       or_4_out, or_5_out, or_6_out, or_7_out, or_8_out, or_9_out, or_10_out, or_11_out, or_12_out,
       or_13_out, or_14_out, or_15_out, or_16_out, or_17_out, or_18_out, or_19_out, or_20_out, or_21_out,
       or_22_out, or_23_out, or_24_out;

  not not_1 (not_1_out, S0);
  not not_2 (not_2_out, S0);
  not not_3 (not_3_out, S0);
  not not_4 (not_4_out, S0);
  not not_5 (not_5_out, S0);
  not not_6 (not_6_out, S0);
  not not_7 (not_7_out, S0);
  not not_8 (not_8_out, S0);
  not not_9 (not_9_out, S0);
  not not_10 (not_10_out, S0);
  not not_11 (not_11_out, S0);
  not not_12 (not_12_out, S0);
  not not_13 (not_13_out, S0);
  not not_14 (not_14_out, S0);
  not not_15 (not_15_out, S0);
  not not_16 (not_16_out, S0);
  not not_17 (not_17_out, S0);
  not not_18 (not_18_out, S0);
  not not_19 (not_19_out, S0);
  not not_20 (not_20_out, S0);
  not not_21 (not_21_out, S0);
  not not_22 (not_22_out, S0);
  not not_23 (not_23_out, S0);
  not not_24 (not_24_out, S0);
  and and_1 (and_1_out, IN0_0, not_1_out);
  and and_2 (and_2_out, IN0_1, not_2_out);
  and and_3 (and_3_out, IN0_2, not_3_out);
  and and_4 (and_4_out, IN0_3, not_4_out);
  and and_5 (and_5_out, IN0_4, not_5_out);
  and and_6 (and_6_out, IN0_5, not_6_out);
  and and_7 (and_7_out, IN0_6, not_7_out);
  and and_8 (and_8_out, IN0_7, not_8_out);
  and and_9 (and_9_out, IN0_8, not_9_out);
  and and_10 (and_10_out, IN0_9, not_10_out);
  and and_11 (and_11_out, IN0_10, not_11_out);
  and and_12 (and_12_out, IN0_11, not_12_out);
  and and_13 (and_13_out, IN0_12, not_13_out);
  and and_14 (and_14_out, IN0_13, not_14_out);
  and and_15 (and_15_out, IN0_14, not_15_out);
  and and_16 (and_16_out, IN0_15, not_16_out);
  and and_17 (and_17_out, IN0_16, not_17_out);
  and and_18 (and_18_out, IN0_17, not_18_out);
  and and_19 (and_19_out, IN0_18, not_19_out);
  and and_20 (and_20_out, IN0_19, not_20_out);
  and and_21 (and_21_out, IN0_20, not_21_out);
  and and_22 (and_22_out, IN0_21, not_22_out);
  and and_23 (and_23_out, IN0_22, not_23_out);
  and and_24 (and_24_out, IN0_23, not_24_out);
  and and_25 (and_25_out, IN1_0, S0);
  and and_26 (and_26_out, IN1_1, S0);
  and and_27 (and_27_out, IN1_2, S0);
  and and_28 (and_28_out, IN1_3, S0);
  and and_29 (and_29_out, IN1_4, S0);
  and and_30 (and_30_out, IN1_5, S0);
  and and_31 (and_31_out, IN1_6, S0);
  and and_32 (and_32_out, IN1_7, S0);
  and and_33 (and_33_out, IN1_8, S0);
  and and_34 (and_34_out, IN1_9, S0);
  and and_35 (and_35_out, IN1_10, S0);
  and and_36 (and_36_out, IN1_11, S0);
  and and_37 (and_37_out, IN1_12, S0);
  and and_38 (and_38_out, IN1_13, S0);
  and and_39 (and_39_out, IN1_14, S0);
  and and_40 (and_40_out, IN1_15, S0);
  and and_41 (and_41_out, IN1_16, S0);
  and and_42 (and_42_out, IN1_17, S0);
  and and_43 (and_43_out, IN1_18, S0);
  and and_44 (and_44_out, IN1_19, S0);
  and and_45 (and_45_out, IN1_20, S0);
  and and_46 (and_46_out, IN1_21, S0);
  and and_47 (and_47_out, IN1_22, S0);
  and and_48 (and_48_out, IN1_23, S0);
  or or_1 (or_1_out, and_1_out, and_25_out);
  or or_2 (or_2_out, and_2_out, and_26_out);
  or or_3 (or_3_out, and_3_out, and_27_out);
  or or_4 (or_4_out, and_4_out, and_28_out);
  or or_5 (or_5_out, and_5_out, and_29_out);
  or or_6 (or_6_out, and_6_out, and_30_out);
  or or_7 (or_7_out, and_7_out, and_31_out);
  or or_8 (or_8_out, and_8_out, and_32_out);
  or or_9 (or_9_out, and_9_out, and_33_out);
  or or_10 (or_10_out, and_10_out, and_34_out);
  or or_11 (or_11_out, and_11_out, and_35_out);
  or or_12 (or_12_out, and_12_out, and_36_out);
  or or_13 (or_13_out, and_13_out, and_37_out);
  or or_14 (or_14_out, and_14_out, and_38_out);
  or or_15 (or_15_out, and_15_out, and_39_out);
  or or_16 (or_16_out, and_16_out, and_40_out);
  or or_17 (or_17_out, and_17_out, and_41_out);
  or or_18 (or_18_out, and_18_out, and_42_out);
  or or_19 (or_19_out, and_19_out, and_43_out);
  or or_20 (or_20_out, and_20_out, and_44_out);
  or or_21 (or_21_out, and_21_out, and_45_out);
  or or_22 (or_22_out, and_22_out, and_46_out);
  or or_23 (or_23_out, and_23_out, and_47_out);
  or or_24 (or_24_out, and_24_out, and_48_out);
  and and_49 (O0, or_1_out, EN);
  and and_50 (O1, or_2_out, EN);
  and and_51 (O2, or_3_out, EN);
  and and_52 (O3, or_4_out, EN);
  and and_53 (O4, or_5_out, EN);
  and and_54 (O5, or_6_out, EN);
  and and_55 (O6, or_7_out, EN);
  and and_56 (O7, or_8_out, EN);
  and and_57 (O8, or_9_out, EN);
  and and_58 (O9, or_10_out, EN);
  and and_59 (O10, or_11_out, EN);
  and and_60 (O11, or_12_out, EN);
  and and_61 (O12, or_13_out, EN);
  and and_62 (O13, or_14_out, EN);
  and and_63 (O14, or_15_out, EN);
  and and_64 (O15, or_16_out, EN);
  and and_65 (O16, or_17_out, EN);
  and and_66 (O17, or_18_out, EN);
  and and_67 (O18, or_19_out, EN);
  and and_68 (O19, or_20_out, EN);
  and and_69 (O20, or_21_out, EN);
  and and_70 (O21, or_22_out, EN);
  and and_71 (O22, or_23_out, EN);
  and and_72 (O23, or_24_out, EN);
endmodule
