// Digital circuit 1 BIT REG V1.1.dig as structural Verilog
module _1_BIT_REG_V1_1 (
  input  CLK,
  input  RST,
  input  EN,
  input  DIN,
  output DOUT
);

  wire and_1_out, and_2_out, and_3_out, not_1_out, not_2_out, or_1_out;

  not not_1 (not_1_out, RST);
  and and_1 (and_1_out, DIN, EN);
  and and_2 (and_2_out, not_2_out, DOUT);
  not not_2 (not_2_out, EN);
  and and_3 (and_3_out, or_1_out, not_1_out);
  or or_1 (or_1_out, and_1_out, and_2_out);
  D_FF d_ff_1 (.D(and_3_out), .C(CLK), .Q(DOUT));  // open: nQ

  // Notes on the sheet:
  //   CLK: Hz: 10
endmodule
